// Logisim project Atividade2.circ as structural Verilog
module DivisorDeFrenquencia (
  input  J,
  output out_2,
  output out_3,
  output out_4,
  output out_5
);

  wire CLEAR_out, CLK_out, ff_jk_me_pc_t_1_qq, ff_jk_me_pc_t_2_qq, ff_jk_me_pc_t_3_qq, ff_jk_me_pc_t_4_qq,
       not_1_out, not_2_out, not_3_out, not_4_out, not_5_out, not_6_out, not_7_out, not_8_out, not_9_out,
       not_10_out, not_11_out, not_12_out, not_13_out, not_14_out, not_15_out, not_16_out, not_17_out,
       not_18_out, not_19_out, not_20_out, PRESET_out;
  wire [6:0] decodificador_hex_1_out_2;

  not not_1 (not_1_out, J);
  not not_2 (not_2_out, J);
  _7_Segment_Display u_7_segment_display_1 (
    .f(not_1_out), .a(not_2_out), .b(1'b1), .e(not_3_out), .d(not_4_out), .c(1'b1));  // open: g, dp
  not not_3 (not_3_out, J);
  not not_4 (not_4_out, J);
  Button PRESET (.out(PRESET_out));
  Button CLEAR (.out(CLEAR_out));
  Clock CLK (.out(CLK_out));
  not not_5 (not_5_out, out_5);
  not not_6 (not_6_out, out_5);
  _7_Segment_Display u_7_segment_display_2 (
    .f(not_5_out), .a(not_6_out), .b(1'b1), .e(not_7_out), .d(not_8_out), .c(1'b1));  // open: g, dp
  not not_7 (not_7_out, out_5);
  not not_8 (not_8_out, out_5);
  not not_9 (not_9_out, out_4);
  not not_10 (not_10_out, out_4);
  not not_11 (not_11_out, out_3);
  _7_Segment_Display u_7_segment_display_3 (
    .f(not_9_out), .a(not_10_out), .b(1'b1), .e(not_12_out), .d(not_13_out), .c(1'b1));  // open: g, dp
  _7_Segment_Display u_7_segment_display_4 (
    .f(not_11_out), .a(not_16_out), .b(1'b1), .e(not_14_out), .d(not_15_out), .c(1'b1));  // open: g, dp
  not not_12 (not_12_out, out_4);
  not not_13 (not_13_out, out_4);
  not not_14 (not_14_out, out_3);
  not not_15 (not_15_out, out_3);
  not not_16 (not_16_out, out_3);
  not not_17 (not_17_out, out_2);
  not not_18 (not_18_out, out_2);
  _7_Segment_Display u_7_segment_display_5 (
    .f(not_17_out), .a(not_18_out), .b(1'b1), .e(not_19_out), .d(not_20_out), .c(1'b1));  // open: g, dp
  not not_19 (not_19_out, out_2);
  not not_20 (not_20_out, out_2);
  FF_JK_ME_PC_T ff_jk_me_pc_t_1 (
    .PRESET(PRESET_out), .J(J), .CLK(CLK_out), .CLEAR(CLEAR_out), .Q(out_2), .Qq(ff_jk_me_pc_t_1_qq));
  // NoConnect on ff_jk_me_pc_t_1_qq
  decodificador_hex decodificador_hex_1 (.in_1({out_5, out_4, out_3, out_2}), .out_2(decodificador_hex_1_out_2));
  _7_Segment_Display u_7_segment_display_6 (
    .g(decodificador_hex_1_out_2[6]), .f(decodificador_hex_1_out_2[5]), .a(decodificador_hex_1_out_2[0]),
    .b(decodificador_hex_1_out_2[1]), .e(decodificador_hex_1_out_2[4]), .d(decodificador_hex_1_out_2[3]),
    .c(decodificador_hex_1_out_2[2]));  // open: dp
  FF_JK_ME_PC_T ff_jk_me_pc_t_2 (
    .PRESET(PRESET_out), .J(J), .CLK(out_2), .CLEAR(CLEAR_out), .Q(out_3), .Qq(ff_jk_me_pc_t_2_qq));
  // NoConnect on ff_jk_me_pc_t_2_qq
  FF_JK_ME_PC_T ff_jk_me_pc_t_3 (
    .PRESET(PRESET_out), .J(J), .CLK(out_3), .CLEAR(CLEAR_out), .Q(out_4), .Qq(ff_jk_me_pc_t_3_qq));
  // NoConnect on ff_jk_me_pc_t_3_qq
  FF_JK_ME_PC_T ff_jk_me_pc_t_4 (
    .PRESET(PRESET_out), .J(J), .CLK(out_4), .CLEAR(CLEAR_out), .Q(out_5), .Qq(ff_jk_me_pc_t_4_qq));
  // NoConnect on ff_jk_me_pc_t_4_qq

  // Other names for the same wires on the sheet: B = J; S[3:0] = {out_5, out_4, out_3, out_2}

  // Notes on the sheet:
  //   ENTRADA
  //   Divisor de Frequência
  //   SAIDA PARALELA
  //   SAÍDA
endmodule

module RegistradorDeDeslocamento (
  input  [3:0] E_PARALELA,
  input  E_SERIAL,
  output S_SERIAL,
  output out_4,
  output out_5,
  output out_6,
  output out_7,
  output [3:0] S_PARALELA
);

  wire CLEAR_out, CLK_out, delay_1_clear, delay_1_preset, delay_2_clear, delay_2_preset, delay_3_clear,
       delay_3_preset, delay_4_clear, delay_4_preset, ENABLE_out, ff_jk_me_pc_d_1_qq, ff_jk_me_pc_d_2_qq,
       ff_jk_me_pc_d_3_qq, ff_jk_me_pc_d_4_qq, not_1_out, not_2_out, not_3_out, not_4_out, not_5_out,
       not_6_out, not_7_out, not_8_out, not_9_out, not_10_out, not_11_out, not_12_out, not_13_out,
       not_14_out, not_15_out, not_16_out, not_17_out, not_18_out, not_19_out, not_20_out, not_21_out,
       not_22_out, not_23_out, not_24_out, not_25_out, not_26_out, not_27_out, not_28_out, not_29_out,
       not_30_out, not_31_out, not_32_out, not_33_out, not_34_out, not_35_out, not_36_out, not_37_out,
       not_38_out, not_39_out, not_40_out, or_1_out, or_2_out, or_3_out, or_4_out;
  wire [6:0] decodificador_hex_1_out_2, decodificador_hex_2_out_2;

  not not_1 (not_1_out, E_PARALELA[3]);
  not not_2 (not_2_out, E_PARALELA[2]);
  not not_3 (not_3_out, E_PARALELA[2]);
  not not_4 (not_4_out, E_PARALELA[3]);
  _7_Segment_Display u_7_segment_display_1 (
    .f(not_2_out), .a(not_3_out), .b(1'b1), .e(not_5_out), .d(not_6_out), .c(1'b1));  // open: g, dp
  _7_Segment_Display u_7_segment_display_2 (
    .f(not_4_out), .a(not_1_out), .b(1'b1), .e(not_7_out), .d(not_8_out), .c(1'b1));  // open: g, dp
  not not_5 (not_5_out, E_PARALELA[2]);
  not not_6 (not_6_out, E_PARALELA[2]);
  not not_7 (not_7_out, E_PARALELA[3]);
  not not_8 (not_8_out, E_PARALELA[3]);
  Button ENABLE (.out(ENABLE_out));
  Button CLEAR (.out(CLEAR_out));
  Clock CLK (.out(CLK_out));
  not not_9 (not_9_out, E_PARALELA[1]);
  not not_10 (not_10_out, E_PARALELA[1]);
  _7_Segment_Display u_7_segment_display_3 (
    .f(not_9_out), .a(not_10_out), .b(1'b1), .e(not_11_out), .d(not_12_out), .c(1'b1));  // open: g, dp
  _7_Segment_Display u_7_segment_display_4 (
    .f(not_14_out), .a(not_15_out), .b(1'b1), .e(not_13_out), .d(not_16_out), .c(1'b1));  // open: g, dp
  not not_11 (not_11_out, E_PARALELA[1]);
  not not_12 (not_12_out, E_PARALELA[1]);
  not not_13 (not_13_out, E_PARALELA[0]);
  not not_14 (not_14_out, E_PARALELA[0]);
  not not_15 (not_15_out, E_PARALELA[0]);
  not not_16 (not_16_out, E_PARALELA[0]);
  Delay delay_1 (.VALOR_PRESETADO(E_PARALELA[3]), .ENABLE(ENABLE_out), .PRESET(delay_1_preset), .CLEAR(delay_1_clear));
  or or_1 (or_1_out, delay_1_clear, CLEAR_out);
  not not_17 (not_17_out, E_SERIAL);
  not not_18 (not_18_out, E_SERIAL);
  _7_Segment_Display u_7_segment_display_5 (
    .f(not_17_out), .a(not_18_out), .b(1'b1), .e(not_19_out), .d(not_20_out), .c(1'b1));  // open: g, dp
  not not_19 (not_19_out, E_SERIAL);
  not not_20 (not_20_out, E_SERIAL);
  decodificador_hex decodificador_hex_1 (.in_1(E_PARALELA), .out_2(decodificador_hex_1_out_2));
  _7_Segment_Display u_7_segment_display_6 (
    .g(decodificador_hex_1_out_2[6]), .f(decodificador_hex_1_out_2[5]), .a(decodificador_hex_1_out_2[0]),
    .b(decodificador_hex_1_out_2[1]), .e(decodificador_hex_1_out_2[4]), .d(decodificador_hex_1_out_2[3]),
    .c(decodificador_hex_1_out_2[2]));  // open: dp
  FF_JK_ME_PC_D ff_jk_me_pc_d_1 (
    .PRESET(delay_1_preset), .J(E_SERIAL), .CLK(CLK_out), .CLEAR(or_1_out), .Q(out_4), .Qq(ff_jk_me_pc_d_1_qq));
  // NoConnect on ff_jk_me_pc_d_1_qq
  or or_2 (or_2_out, delay_2_clear, CLEAR_out);
  Delay delay_2 (.VALOR_PRESETADO(E_PARALELA[2]), .ENABLE(ENABLE_out), .PRESET(delay_2_preset), .CLEAR(delay_2_clear));
  not not_21 (not_21_out, out_4);
  not not_22 (not_22_out, out_4);
  not not_23 (not_23_out, out_5);
  _7_Segment_Display u_7_segment_display_7 (
    .f(not_21_out), .a(not_22_out), .b(1'b1), .e(not_24_out), .d(not_25_out), .c(1'b1));  // open: g, dp
  _7_Segment_Display u_7_segment_display_8 (
    .f(not_23_out), .a(not_28_out), .b(1'b1), .e(not_26_out), .d(not_27_out), .c(1'b1));  // open: g, dp
  not not_24 (not_24_out, out_4);
  not not_25 (not_25_out, out_4);
  not not_26 (not_26_out, out_5);
  not not_27 (not_27_out, out_5);
  FF_JK_ME_PC_D ff_jk_me_pc_d_2 (
    .PRESET(delay_2_preset), .J(out_4), .CLK(CLK_out), .CLEAR(or_2_out), .Q(out_5), .Qq(ff_jk_me_pc_d_2_qq));
  // NoConnect on ff_jk_me_pc_d_2_qq
  not not_28 (not_28_out, out_5);
  not not_29 (not_29_out, out_6);
  not not_30 (not_30_out, out_6);
  _7_Segment_Display u_7_segment_display_9 (
    .f(not_29_out), .a(not_30_out), .b(1'b1), .e(not_31_out), .d(not_32_out), .c(1'b1));  // open: g, dp
  not not_31 (not_31_out, out_6);
  not not_32 (not_32_out, out_6);
  Delay delay_3 (.VALOR_PRESETADO(E_PARALELA[1]), .ENABLE(ENABLE_out), .PRESET(delay_3_preset), .CLEAR(delay_3_clear));
  or or_3 (or_3_out, delay_3_clear, CLEAR_out);
  not not_33 (not_33_out, out_7);
  not not_34 (not_34_out, out_7);
  _7_Segment_Display u_7_segment_display_10 (
    .f(not_33_out), .a(not_34_out), .b(1'b1), .e(not_35_out), .d(not_36_out), .c(1'b1));  // open: g, dp
  not not_35 (not_35_out, out_7);
  not not_36 (not_36_out, out_7);
  not not_37 (not_37_out, out_7);
  not not_38 (not_38_out, out_7);
  _7_Segment_Display u_7_segment_display_11 (
    .f(not_38_out), .a(not_37_out), .b(1'b1), .e(not_39_out), .d(not_40_out), .c(1'b1));  // open: g, dp
  not not_39 (not_39_out, out_7);
  not not_40 (not_40_out, out_7);
  FF_JK_ME_PC_D ff_jk_me_pc_d_3 (
    .PRESET(delay_3_preset), .J(out_5), .CLK(CLK_out), .CLEAR(or_3_out), .Q(out_6), .Qq(ff_jk_me_pc_d_3_qq));
  // NoConnect on ff_jk_me_pc_d_3_qq
  decodificador_hex decodificador_hex_2 (.in_1({out_4, out_5, out_6, out_7}), .out_2(decodificador_hex_2_out_2));
  or or_4 (or_4_out, delay_4_clear, CLEAR_out);
  _7_Segment_Display u_7_segment_display_12 (
    .g(decodificador_hex_2_out_2[6]), .f(decodificador_hex_2_out_2[5]), .a(decodificador_hex_2_out_2[0]),
    .b(decodificador_hex_2_out_2[1]), .e(decodificador_hex_2_out_2[4]), .d(decodificador_hex_2_out_2[3]),
    .c(decodificador_hex_2_out_2[2]));  // open: dp
  Delay delay_4 (.VALOR_PRESETADO(E_PARALELA[0]), .ENABLE(ENABLE_out), .PRESET(delay_4_preset), .CLEAR(delay_4_clear));
  FF_JK_ME_PC_D ff_jk_me_pc_d_4 (
    .PRESET(delay_4_preset), .J(out_6), .CLK(CLK_out), .CLEAR(or_4_out), .Q(out_7), .Qq(ff_jk_me_pc_d_4_qq));
  // NoConnect on ff_jk_me_pc_d_4_qq

  assign S_PARALELA = {out_4, out_5, out_6, out_7};
  assign S_SERIAL = out_7;

  // Other names for the same wires on the sheet: A[3:0] = E_PARALELA; B = E_SERIAL; C = out_7;
  //   S[3:0] = {out_4, out_5, out_6, out_7}

  // Notes on the sheet:
  //   Registrador de Deslocamento
  //   ENTRADA PARALELA
  //   ENTRADA SERIAL
  //   ENTRADA
  //   SAIDA PARALELA
  //   SAIDA SERIAL
  //   SAÍDA
endmodule

module RegistradorDeDeslocamentoUniversal (
  input  [1:0] SEL,
  input  [3:0] E_PARALELA,
  input  E_SERIAL_DIR,
  input  E_SERIAL_ESQ,
  output S_SERIAL,
  output [3:0] S_PARALELA
);

  wire CLEAR_out, CLK_out, ff_jk_me_pc_d_1_qq, ff_jk_me_pc_d_2_qq, ff_jk_me_pc_d_3_qq, ff_jk_me_pc_d_4_qq,
       mux_1_s, mux_2_s, mux_3_s, mux_4_s, not_1_out, not_2_out, not_3_out, not_4_out, not_5_out, not_6_out,
       not_7_out, not_8_out, not_9_out, not_10_out, not_11_out, not_12_out, not_13_out, not_14_out,
       not_15_out, not_16_out, not_17_out, not_18_out, not_19_out, not_20_out, not_21_out, not_22_out,
       not_23_out, not_24_out, not_25_out, not_26_out, not_27_out, not_28_out, not_29_out, not_30_out,
       not_31_out, not_32_out, not_33_out, not_34_out, not_35_out, not_36_out, not_37_out, not_38_out,
       not_39_out, not_40_out, not_41_out, not_42_out, not_43_out, not_44_out, not_45_out, not_46_out,
       not_47_out, not_48_out, not_49_out, not_50_out, not_51_out, not_52_out, PRESET_out;
  wire [6:0] decodificador_hex_1_out_2, decodificador_hex_2_out_2;

  Button PRESET (.out(PRESET_out));
  Button CLEAR (.out(CLEAR_out));
  Clock CLK (.out(CLK_out));
  not not_1 (not_1_out, SEL[1]);
  not not_2 (not_2_out, SEL[1]);
  _7_Segment_Display u_7_segment_display_1 (
    .f(not_1_out), .a(not_2_out), .b(1'b1), .e(not_3_out), .d(not_4_out), .c(1'b1));  // open: g, dp
  not not_3 (not_3_out, SEL[1]);
  not not_4 (not_4_out, SEL[1]);
  not not_5 (not_5_out, SEL[0]);
  not not_6 (not_6_out, SEL[0]);
  _7_Segment_Display u_7_segment_display_2 (
    .f(not_5_out), .a(not_6_out), .b(1'b1), .e(not_7_out), .d(not_8_out), .c(1'b1));  // open: g, dp
  not not_7 (not_7_out, SEL[0]);
  not not_8 (not_8_out, SEL[0]);
  not not_9 (not_9_out, E_PARALELA[3]);
  _7_Segment_Display u_7_segment_display_3 (
    .f(not_9_out), .a(not_12_out), .b(1'b1), .e(not_10_out), .d(not_11_out), .c(1'b1));  // open: g, dp
  not not_10 (not_10_out, E_PARALELA[3]);
  not not_11 (not_11_out, E_PARALELA[3]);
  MUX mux_1 (
    .I0(S_PARALELA[3]), .I1(S_PARALELA[2]), .I2(E_SERIAL_ESQ), .I3(E_PARALELA[3]), .A(SEL[0]), .B(SEL[1]),
    .S(mux_1_s));
  not not_12 (not_12_out, E_PARALELA[3]);
  not not_13 (not_13_out, E_PARALELA[2]);
  not not_14 (not_14_out, E_PARALELA[2]);
  _7_Segment_Display u_7_segment_display_4 (
    .f(not_13_out), .a(not_14_out), .b(1'b1), .e(not_15_out), .d(not_16_out), .c(1'b1));  // open: g, dp
  not not_15 (not_15_out, E_PARALELA[2]);
  not not_16 (not_16_out, E_PARALELA[2]);
  not not_17 (not_17_out, E_PARALELA[1]);
  not not_18 (not_18_out, E_PARALELA[1]);
  not not_19 (not_19_out, E_PARALELA[0]);
  not not_20 (not_20_out, E_PARALELA[0]);
  _7_Segment_Display u_7_segment_display_5 (
    .f(not_17_out), .a(not_18_out), .b(1'b1), .e(not_21_out), .d(not_22_out), .c(1'b1));  // open: g, dp
  _7_Segment_Display u_7_segment_display_6 (
    .f(not_19_out), .a(not_20_out), .b(1'b1), .e(not_23_out), .d(not_24_out), .c(1'b1));  // open: g, dp
  not not_21 (not_21_out, E_PARALELA[1]);
  not not_22 (not_22_out, E_PARALELA[1]);
  not not_23 (not_23_out, E_PARALELA[0]);
  not not_24 (not_24_out, E_PARALELA[0]);
  decodificador_hex decodificador_hex_1 (.in_1(E_PARALELA), .out_2(decodificador_hex_1_out_2));
  FF_JK_ME_PC_D ff_jk_me_pc_d_1 (
    .PRESET(PRESET_out), .J(mux_1_s), .CLK(CLK_out), .CLEAR(CLEAR_out), .Q(S_PARALELA[3]),
    .Qq(ff_jk_me_pc_d_1_qq));
  // NoConnect on ff_jk_me_pc_d_1_qq
  _7_Segment_Display u_7_segment_display_7 (
    .g(decodificador_hex_1_out_2[6]), .f(decodificador_hex_1_out_2[5]), .a(decodificador_hex_1_out_2[0]),
    .b(decodificador_hex_1_out_2[1]), .e(decodificador_hex_1_out_2[4]), .d(decodificador_hex_1_out_2[3]),
    .c(decodificador_hex_1_out_2[2]));  // open: dp
  MUX mux_2 (
    .I0(S_PARALELA[2]), .I1(S_PARALELA[1]), .I2(S_PARALELA[3]), .I3(E_PARALELA[2]), .A(SEL[0]), .B(SEL[1]),
    .S(mux_2_s));
  not not_25 (not_25_out, E_SERIAL_ESQ);
  not not_26 (not_26_out, E_SERIAL_ESQ);
  _7_Segment_Display u_7_segment_display_8 (
    .f(not_25_out), .a(not_26_out), .b(1'b1), .e(not_27_out), .d(not_28_out), .c(1'b1));  // open: g, dp
  not not_27 (not_27_out, E_SERIAL_ESQ);
  not not_28 (not_28_out, E_SERIAL_ESQ);
  FF_JK_ME_PC_D ff_jk_me_pc_d_2 (
    .PRESET(PRESET_out), .J(mux_2_s), .CLK(CLK_out), .CLEAR(CLEAR_out), .Q(S_PARALELA[2]),
    .Qq(ff_jk_me_pc_d_2_qq));
  // NoConnect on ff_jk_me_pc_d_2_qq
  not not_29 (not_29_out, S_PARALELA[3]);
  not not_30 (not_30_out, S_PARALELA[3]);
  _7_Segment_Display u_7_segment_display_9 (
    .f(not_29_out), .a(not_30_out), .b(1'b1), .e(not_31_out), .d(not_32_out), .c(1'b1));  // open: g, dp
  not not_31 (not_31_out, S_PARALELA[3]);
  not not_32 (not_32_out, S_PARALELA[3]);
  MUX mux_3 (
    .I0(S_PARALELA[1]), .I1(S_PARALELA[0]), .I2(S_PARALELA[2]), .I3(E_PARALELA[1]), .A(SEL[0]), .B(SEL[1]),
    .S(mux_3_s));
  not not_33 (not_33_out, S_PARALELA[2]);
  not not_34 (not_34_out, S_PARALELA[2]);
  not not_35 (not_35_out, S_PARALELA[1]);
  _7_Segment_Display u_7_segment_display_10 (
    .f(not_33_out), .a(not_34_out), .b(1'b1), .e(not_36_out), .d(not_37_out), .c(1'b1));  // open: g, dp
  _7_Segment_Display u_7_segment_display_11 (
    .f(not_35_out), .a(not_40_out), .b(1'b1), .e(not_38_out), .d(not_39_out), .c(1'b1));  // open: g, dp
  not not_36 (not_36_out, S_PARALELA[2]);
  not not_37 (not_37_out, S_PARALELA[2]);
  not not_38 (not_38_out, S_PARALELA[1]);
  not not_39 (not_39_out, S_PARALELA[1]);
  not not_40 (not_40_out, S_PARALELA[1]);
  not not_41 (not_41_out, S_PARALELA[0]);
  not not_42 (not_42_out, S_PARALELA[0]);
  _7_Segment_Display u_7_segment_display_12 (
    .f(not_41_out), .a(not_42_out), .b(1'b1), .e(not_43_out), .d(not_44_out), .c(1'b1));  // open: g, dp
  not not_43 (not_43_out, S_PARALELA[0]);
  not not_44 (not_44_out, S_PARALELA[0]);
  not not_45 (not_45_out, E_SERIAL_DIR);
  _7_Segment_Display u_7_segment_display_13 (
    .f(not_45_out), .a(not_48_out), .b(1'b1), .e(not_46_out), .d(not_47_out), .c(1'b1));  // open: g, dp
  not not_46 (not_46_out, E_SERIAL_DIR);
  not not_47 (not_47_out, E_SERIAL_DIR);
  FF_JK_ME_PC_D ff_jk_me_pc_d_3 (
    .PRESET(PRESET_out), .J(mux_3_s), .CLK(CLK_out), .CLEAR(CLEAR_out), .Q(S_PARALELA[1]),
    .Qq(ff_jk_me_pc_d_3_qq));
  // NoConnect on ff_jk_me_pc_d_3_qq
  not not_48 (not_48_out, E_SERIAL_DIR);
  MUX mux_4 (
    .I0(S_PARALELA[0]), .I1(E_SERIAL_DIR), .I2(S_PARALELA[1]), .I3(E_PARALELA[0]), .A(SEL[0]), .B(SEL[1]),
    .S(mux_4_s));
  _7_Segment_Display u_7_segment_display_14 (
    .f(not_50_out), .a(not_51_out), .b(1'b1), .e(not_49_out), .d(not_52_out), .c(1'b1));  // open: g, dp
  not not_49 (not_49_out, S_PARALELA[0]);
  not not_50 (not_50_out, S_PARALELA[0]);
  not not_51 (not_51_out, S_PARALELA[0]);
  not not_52 (not_52_out, S_PARALELA[0]);
  decodificador_hex decodificador_hex_2 (.in_1(S_PARALELA), .out_2(decodificador_hex_2_out_2));
  FF_JK_ME_PC_D ff_jk_me_pc_d_4 (
    .PRESET(PRESET_out), .J(mux_4_s), .CLK(CLK_out), .CLEAR(CLEAR_out), .Q(S_PARALELA[0]),
    .Qq(ff_jk_me_pc_d_4_qq));
  // NoConnect on ff_jk_me_pc_d_4_qq
  _7_Segment_Display u_7_segment_display_15 (
    .g(decodificador_hex_2_out_2[6]), .f(decodificador_hex_2_out_2[5]), .a(decodificador_hex_2_out_2[0]),
    .b(decodificador_hex_2_out_2[1]), .e(decodificador_hex_2_out_2[4]), .d(decodificador_hex_2_out_2[3]),
    .c(decodificador_hex_2_out_2[2]));  // open: dp

  assign S_SERIAL = S_PARALELA[0];

  // Other names for the same wires on the sheet: A[1:0] = SEL; B[3:0] = E_PARALELA; C = E_SERIAL_ESQ;
  //   D[3:0] = S_PARALELA; F = S_PARALELA[0]; E = E_SERIAL_DIR

  // Notes on the sheet:
  //   00 - MANTER
  //   01 - SHIFT A ESQ
  //   10 - SHIFT A DIR
  //   11 - CARGA PARALELA
  //   Registrador de Deslocamento Universal
  //   SELETOR
  //   ENTRADA PARALELA
  //   ENTRADA
  //   ENTRADA SERIAL ESQ
  //   ------->
  //   SAIDA PARALELA
  //   <-------
  //   ENTRADA SERIAL DIR
  //   SAIDA SERIAL
  //   ENTRADA
endmodule

module FF_RS (
  input  set,
  input  clock,
  input  reset,
  output Q,
  output Ql
);

  wire nand_1_out, nand_2_out;

  nand nand_1 (nand_1_out, set, clock);
  nand nand_2 (nand_2_out, clock, reset);
  nand nand_3 (Q, nand_1_out, Ql);
  nand nand_4 (Ql, Q, nand_2_out);

  // Notes on the sheet:
  //   Flip-Flop Reset Set c/ Clock
endmodule

module FF_JK (
  input  J,
  input  clock,
  input  K,
  output Q,
  output Ql
);

  wire nand_1_out, nand_2_out;

  nand nand_1 (nand_1_out, J, clock, Ql);
  nand nand_2 (nand_2_out, Q, clock, K);
  nand nand_3 (Q, nand_1_out, Ql);
  nand nand_4 (Ql, Q, nand_2_out);

  // Notes on the sheet:
  //   Flip-Flop JK
endmodule

module FF_JK_PC (
  input  preset,
  input  J,
  input  clock,
  input  K,
  input  clear,
  output Q,
  output Ql
);

  wire nand_1_out, nand_2_out, not_1_out, not_2_out;

  not not_1 (not_1_out, preset);
  nand nand_1 (nand_1_out, J, clock, Ql);
  nand nand_2 (nand_2_out, Q, clock, K);
  not not_2 (not_2_out, clear);
  nand nand_3 (Q, not_1_out, nand_1_out, Ql);
  nand nand_4 (Ql, Q, nand_2_out, not_2_out);

  // Notes on the sheet:
  //   Flip-Flop JK com Entrada Preset e Clear
endmodule

module FF_JK_ME_PC (
  input  PRESET,
  input  J,
  input  CLK,
  input  K,
  input  CLEAR,
  output Q,
  output Qq
);

  wire nand_1_out, nand_2_out, nand_3_out, nand_4_out, nand_5_out, nand_6_out, not_1_out, not_2_out,
       not_3_out;

  nand nand_1 (nand_1_out, J, CLK, Qq);
  nand nand_2 (nand_2_out, Q, CLK, K);
  not not_1 (not_1_out, PRESET);
  not not_2 (not_2_out, CLEAR);
  nand nand_3 (nand_3_out, not_1_out, nand_1_out, nand_4_out);
  nand nand_4 (nand_4_out, nand_3_out, nand_2_out, not_2_out);
  not not_3 (not_3_out, CLK);
  nand nand_5 (nand_5_out, nand_3_out, not_3_out);
  nand nand_6 (nand_6_out, not_3_out, nand_4_out);
  nand nand_7 (Q, not_1_out, nand_5_out, Qq);
  nand nand_8 (Qq, Q, nand_6_out, not_2_out);

  // Notes on the sheet:
  //   Flip-Flop JK Mestre-Escravo com Entrada Preset e Clear
endmodule

module FF_JK_ME_PC_D (
  input  PRESET,
  input  J,
  input  CLK,
  input  CLEAR,
  output Q,
  output Qq
);

  wire nand_1_out, nand_2_out, nand_3_out, nand_4_out, nand_5_out, nand_6_out, not_1_out, not_2_out,
       not_3_out, not_4_out;

  not not_1 (not_1_out, J);
  nand nand_1 (nand_1_out, J, CLK, Qq);
  nand nand_2 (nand_2_out, Q, CLK, not_1_out);
  not not_2 (not_2_out, PRESET);
  not not_3 (not_3_out, CLEAR);
  nand nand_3 (nand_3_out, not_2_out, nand_1_out, nand_4_out);
  nand nand_4 (nand_4_out, nand_3_out, nand_2_out, not_3_out);
  not not_4 (not_4_out, CLK);
  nand nand_5 (nand_5_out, nand_3_out, not_4_out);
  nand nand_6 (nand_6_out, not_4_out, nand_4_out);
  nand nand_7 (Q, not_2_out, nand_5_out, Qq);
  nand nand_8 (Qq, Q, nand_6_out, not_3_out);

  // Notes on the sheet:
  //   Flip-Flop JK Mestre-Escravo com Entrada Preset e Clear D
endmodule

module FF_JK_ME_PC_T (
  input  PRESET,
  input  J,
  input  CLK,
  input  CLEAR,
  output Q,
  output Qq
);

  wire nand_1_out, nand_2_out, nand_3_out, nand_4_out, nand_5_out, nand_6_out, not_1_out, not_2_out,
       not_3_out;

  nand nand_1 (nand_1_out, J, CLK, Qq);
  nand nand_2 (nand_2_out, Q, CLK, J);
  not not_1 (not_1_out, PRESET);
  not not_2 (not_2_out, CLEAR);
  nand nand_3 (nand_3_out, not_1_out, nand_1_out, nand_4_out);
  nand nand_4 (nand_4_out, nand_3_out, nand_2_out, not_2_out);
  not not_3 (not_3_out, CLK);
  nand nand_5 (nand_5_out, nand_3_out, not_3_out);
  nand nand_6 (nand_6_out, not_3_out, nand_4_out);
  nand nand_7 (Q, not_1_out, nand_5_out, Qq);
  nand nand_8 (Qq, Q, nand_6_out, not_2_out);

  // Notes on the sheet:
  //   Flip-Flop JK Mestre-Escravo com Entrada Preset e Clear T
endmodule

module decodificador_hex (
  input  [3:0] in_1,
  output [6:0] out_2
);

  wire and_1_out, and_2_out, and_3_out, and_4_out, and_5_out, and_6_out, and_7_out, and_8_out, and_9_out,
       and_10_out, and_11_out, and_12_out, and_13_out, and_14_out, and_15_out, and_16_out, and_17_out,
       and_18_out, and_19_out, and_20_out, and_21_out, and_22_out, and_23_out, and_24_out, and_25_out,
       and_26_out, and_27_out, and_28_out, and_29_out, and_30_out, and_31_out, and_32_out, and_33_out,
       and_34_out, and_35_out, not_1_out, not_2_out, not_3_out, not_4_out;

  not not_1 (not_1_out, in_1[3]);
  not not_2 (not_2_out, in_1[2]);
  not not_3 (not_3_out, in_1[1]);
  not not_4 (not_4_out, in_1[0]);
  and and_1 (and_1_out, not_2_out, not_4_out);
  and and_2 (and_2_out, not_1_out, in_1[1]);
  and and_3 (and_3_out, not_1_out, in_1[2], in_1[0]);
  and and_4 (and_4_out, in_1[3], not_2_out, not_3_out);
  and and_5 (and_5_out, in_1[3], not_4_out);
  and and_6 (and_6_out, in_1[2], in_1[1]);
  and and_7 (and_7_out, not_1_out, not_3_out, not_4_out);
  and and_8 (and_8_out, not_1_out, in_1[1], in_1[0]);
  and and_9 (and_9_out, not_2_out, not_4_out);
  and and_10 (and_10_out, in_1[3], not_3_out, in_1[0]);
  and and_11 (and_11_out, not_1_out, not_2_out);
  and and_12 (and_12_out, not_1_out, in_1[2]);
  and and_13 (and_13_out, in_1[3], not_2_out);
  and and_14 (and_14_out, not_3_out, in_1[0]);
  and and_15 (and_15_out, not_2_out, not_3_out);
  and and_16 (and_16_out, not_2_out, in_1[0]);
  and and_17 (and_17_out, in_1[2], not_3_out, in_1[0]);
  and and_18 (and_18_out, not_1_out, not_2_out, not_4_out);
  and and_19 (and_19_out, not_2_out, in_1[1], in_1[0]);
  and and_20 (and_20_out, in_1[3], not_3_out);
  and and_21 (and_21_out, in_1[2], in_1[1], not_4_out);
  and and_22 (and_22_out, not_2_out, not_4_out);
  and and_23 (and_23_out, in_1[1], not_4_out);
  and and_24 (and_24_out, in_1[3], in_1[1]);
  and and_25 (and_25_out, in_1[3], in_1[2]);
  and and_26 (and_26_out, not_3_out, not_4_out);
  and and_27 (and_27_out, not_1_out, in_1[2], not_3_out);
  and and_28 (and_28_out, in_1[2], not_4_out);
  and and_29 (and_29_out, in_1[3], not_2_out);
  and and_30 (and_30_out, in_1[3], in_1[1]);
  and and_31 (and_31_out, not_2_out, in_1[1]);
  and and_32 (and_32_out, in_1[3], not_2_out);
  and and_33 (and_33_out, not_1_out, in_1[2], not_3_out);
  and and_34 (and_34_out, in_1[1], not_4_out);
  and and_35 (and_35_out, in_1[3], in_1[0]);
  or or_1 (out_2[0], and_1_out, and_2_out, and_3_out, and_4_out, and_5_out, and_6_out);
  or or_2 (out_2[1], and_7_out, and_8_out, and_9_out, and_10_out, and_11_out);
  or or_3 (out_2[2], and_12_out, and_13_out, and_14_out, and_15_out, and_16_out);
  or or_4 (out_2[3], and_17_out, and_18_out, and_19_out, and_20_out, and_21_out);
  or or_5 (out_2[4], and_22_out, and_23_out, and_24_out, and_25_out);
  or or_6 (out_2[5], and_26_out, and_27_out, and_28_out, and_29_out, and_30_out);
  or or_7 (out_2[6], and_31_out, and_32_out, and_33_out, and_34_out, and_35_out);
endmodule

module Delay (
  input  VALOR_PRESETADO,
  input  ENABLE,
  output PRESET,
  output CLEAR
);

  wire not_1_out;

  not not_1 (not_1_out, VALOR_PRESETADO);
  and and_1 (PRESET, VALOR_PRESETADO, ENABLE);
  and and_2 (CLEAR, not_1_out, ENABLE);
endmodule

module MUX (
  input  A,
  input  B,
  input  I0,
  input  I1,
  input  I2,
  input  I3,
  output S
);

  wire and_1_out, and_2_out, and_3_out, and_4_out;

  and and_1 (and_1_out, ~B, I0, ~A);  // AND_Gate
  and and_2 (and_2_out, B, I1, ~A);  // AND_Gate
  and and_3 (and_3_out, ~B, I2, A);  // AND_Gate
  and and_4 (and_4_out, B, I3, A);
  or or_1 (S, and_1_out, and_2_out, and_3_out, and_4_out);
endmodule

module DivisorDeFrequencia_vhdl (
  input  J,
  output out_2,
  output out_3,
  output out_4,
  output out_5
);

  wire CLEAR_out, CLK_out, ff_jk_me_pc_t_vhdl_1_qn, ff_jk_me_pc_t_vhdl_2_qn, ff_jk_me_pc_t_vhdl_3_qn,
       ff_jk_me_pc_t_vhdl_4_qn, not_1_out, not_2_out, not_3_out, not_4_out, not_5_out, not_6_out, not_7_out,
       not_8_out, not_9_out, not_10_out, not_11_out, not_12_out, not_13_out, not_14_out, not_15_out,
       not_16_out, not_17_out, not_18_out, not_19_out, not_20_out, not_21_out, not_22_out, PRESET_out;
  wire [6:0] decodificador_hex_vhdl_1_saida;

  not not_1 (not_1_out, J);
  not not_2 (not_2_out, J);
  _7_Segment_Display u_7_segment_display_1 (
    .f(not_1_out), .a(not_2_out), .b(1'b1), .e(not_3_out), .d(not_4_out), .c(1'b1));  // open: g, dp
  not not_3 (not_3_out, J);
  not not_4 (not_4_out, J);
  not not_5 (not_5_out, PRESET_out);
  Button PRESET (.out(PRESET_out));
  not not_6 (not_6_out, CLEAR_out);
  Button CLEAR (.out(CLEAR_out));
  Clock CLK (.out(CLK_out));
  not not_7 (not_7_out, out_5);
  not not_8 (not_8_out, out_5);
  _7_Segment_Display u_7_segment_display_2 (
    .f(not_7_out), .a(not_8_out), .b(1'b1), .e(not_9_out), .d(not_10_out), .c(1'b1));  // open: g, dp
  not not_9 (not_9_out, out_5);
  not not_10 (not_10_out, out_5);
  not not_11 (not_11_out, out_4);
  not not_12 (not_12_out, out_4);
  _7_Segment_Display u_7_segment_display_3 (
    .f(not_11_out), .a(not_12_out), .b(1'b1), .e(not_13_out), .d(not_14_out), .c(1'b1));  // open: g, dp
  _7_Segment_Display u_7_segment_display_4 (
    .f(not_16_out), .a(not_17_out), .b(1'b1), .e(not_15_out), .d(not_20_out), .c(1'b1));  // open: g, dp
  not not_13 (not_13_out, out_4);
  not not_14 (not_14_out, out_4);
  not not_15 (not_15_out, out_3);
  not not_16 (not_16_out, out_3);
  not not_17 (not_17_out, out_3);
  not not_18 (not_18_out, out_2);
  not not_19 (not_19_out, out_2);
  _7_Segment_Display u_7_segment_display_5 (
    .f(not_18_out), .a(not_19_out), .b(1'b1), .e(not_21_out), .d(not_22_out), .c(1'b1));  // open: g, dp
  not not_20 (not_20_out, out_3);
  not not_21 (not_21_out, out_2);
  not not_22 (not_22_out, out_2);
  FF_JK_ME_PC_T_vhdl ff_jk_me_pc_t_vhdl_1 (
    .PRESET(not_5_out), .J(J), .CLK(CLK_out), .CLEAR(not_6_out), .Q(out_2), .QN(ff_jk_me_pc_t_vhdl_1_qn));
  // NoConnect on ff_jk_me_pc_t_vhdl_1_qn
  decodificador_hex_vhdl decodificador_hex_vhdl_1 (
    .entrada({out_5, out_4, out_3, out_2}), .saida(decodificador_hex_vhdl_1_saida));
  _7_Segment_Display u_7_segment_display_6 (
    .g(decodificador_hex_vhdl_1_saida[6]), .f(decodificador_hex_vhdl_1_saida[5]),
    .a(decodificador_hex_vhdl_1_saida[0]), .b(decodificador_hex_vhdl_1_saida[1]),
    .e(decodificador_hex_vhdl_1_saida[4]), .d(decodificador_hex_vhdl_1_saida[3]),
    .c(decodificador_hex_vhdl_1_saida[2]));  // open: dp
  FF_JK_ME_PC_T_vhdl ff_jk_me_pc_t_vhdl_2 (
    .PRESET(not_5_out), .J(J), .CLK(out_2), .CLEAR(not_6_out), .Q(out_3), .QN(ff_jk_me_pc_t_vhdl_2_qn));
  // NoConnect on ff_jk_me_pc_t_vhdl_2_qn
  FF_JK_ME_PC_T_vhdl ff_jk_me_pc_t_vhdl_3 (
    .PRESET(not_5_out), .J(J), .CLK(out_3), .CLEAR(not_6_out), .Q(out_4), .QN(ff_jk_me_pc_t_vhdl_3_qn));
  // NoConnect on ff_jk_me_pc_t_vhdl_3_qn
  FF_JK_ME_PC_T_vhdl ff_jk_me_pc_t_vhdl_4 (
    .PRESET(not_5_out), .J(J), .CLK(out_4), .CLEAR(not_6_out), .Q(out_5), .QN(ff_jk_me_pc_t_vhdl_4_qn));
  // NoConnect on ff_jk_me_pc_t_vhdl_4_qn

  // Other names for the same wires on the sheet: B = J; S[3:0] = {out_5, out_4, out_3, out_2}

  // Notes on the sheet:
  //   ENTRADA
  //   Divisor de Frequência VHDL
  //   SAIDA PARALELA
  //   SAÍDA
endmodule

module RegistradorDeDeslocamento_vhdl (
  input  [3:0] E_PARALELA,
  input  E_SERIAL,
  output S_SERIAL,
  output out_4,
  output out_5,
  output out_6,
  output out_7,
  output [3:0] S_PARALELA
);

  wire CLEAR_out, CLK_out, delay_vhdl_1_clear, delay_vhdl_1_preset, delay_vhdl_2_clear, delay_vhdl_2_preset,
       delay_vhdl_3_clear, delay_vhdl_3_preset, delay_vhdl_4_clear, delay_vhdl_4_preset, ENABLE_out,
       ff_jk_me_pc_d_vhdl_1_qn, ff_jk_me_pc_d_vhdl_2_qn, ff_jk_me_pc_d_vhdl_3_qn, ff_jk_me_pc_d_vhdl_4_qn,
       nor_1_out, nor_2_out, nor_3_out, nor_4_out, not_1_out, not_2_out, not_3_out, not_4_out, not_5_out,
       not_6_out, not_7_out, not_8_out, not_9_out, not_10_out, not_11_out, not_12_out, not_13_out,
       not_14_out, not_15_out, not_16_out, not_17_out, not_18_out, not_19_out, not_20_out, not_21_out,
       not_22_out, not_23_out, not_24_out, not_25_out, not_26_out, not_27_out, not_28_out, not_29_out,
       not_30_out, not_31_out, not_32_out, not_33_out, not_34_out, not_35_out, not_36_out, not_37_out,
       not_38_out, not_39_out, not_40_out, not_41_out, not_42_out, not_43_out, not_44_out;
  wire [6:0] decodificador_hex_vhdl_1_saida, decodificador_hex_vhdl_2_saida;

  not not_1 (not_1_out, E_PARALELA[3]);
  not not_2 (not_2_out, E_PARALELA[3]);
  not not_3 (not_3_out, E_PARALELA[2]);
  _7_Segment_Display u_7_segment_display_1 (
    .f(not_3_out), .a(not_8_out), .b(1'b1), .e(not_5_out), .d(not_6_out), .c(1'b1));  // open: g, dp
  _7_Segment_Display u_7_segment_display_2 (
    .f(not_1_out), .a(not_2_out), .b(1'b1), .e(not_7_out), .d(not_4_out), .c(1'b1));  // open: g, dp
  not not_4 (not_4_out, E_PARALELA[3]);
  not not_5 (not_5_out, E_PARALELA[2]);
  not not_6 (not_6_out, E_PARALELA[2]);
  not not_7 (not_7_out, E_PARALELA[3]);
  Button ENABLE (.out(ENABLE_out));
  Button CLEAR (.out(CLEAR_out));
  Clock CLK (.out(CLK_out));
  not not_8 (not_8_out, E_PARALELA[2]);
  not not_9 (not_9_out, E_PARALELA[1]);
  not not_10 (not_10_out, E_PARALELA[1]);
  _7_Segment_Display u_7_segment_display_3 (
    .f(not_9_out), .a(not_10_out), .b(1'b1), .e(not_11_out), .d(not_12_out), .c(1'b1));  // open: g, dp
  not not_11 (not_11_out, E_PARALELA[1]);
  not not_12 (not_12_out, E_PARALELA[1]);
  not not_13 (not_13_out, E_PARALELA[0]);
  not not_14 (not_14_out, E_PARALELA[0]);
  _7_Segment_Display u_7_segment_display_4 (
    .f(not_13_out), .a(not_14_out), .b(1'b1), .e(not_15_out), .d(not_16_out), .c(1'b1));  // open: g, dp
  not not_15 (not_15_out, E_PARALELA[0]);
  not not_16 (not_16_out, E_PARALELA[0]);
  not not_17 (not_17_out, delay_vhdl_1_preset);
  nor nor_1 (nor_1_out, delay_vhdl_1_clear, CLEAR_out);
  not not_18 (not_18_out, E_SERIAL);
  not not_19 (not_19_out, E_SERIAL);
  _7_Segment_Display u_7_segment_display_5 (
    .f(not_18_out), .a(not_19_out), .b(1'b1), .e(not_20_out), .d(not_21_out), .c(1'b1));  // open: g, dp
  not not_20 (not_20_out, E_SERIAL);
  not not_21 (not_21_out, E_SERIAL);
  Delay_vhdl delay_vhdl_1 (.A(E_PARALELA[3]), .B(ENABLE_out), .preset(delay_vhdl_1_preset), .clear(delay_vhdl_1_clear));
  decodificador_hex_vhdl decodificador_hex_vhdl_1 (.entrada(E_PARALELA), .saida(decodificador_hex_vhdl_1_saida));
  _7_Segment_Display u_7_segment_display_6 (
    .g(decodificador_hex_vhdl_1_saida[6]), .f(decodificador_hex_vhdl_1_saida[5]),
    .a(decodificador_hex_vhdl_1_saida[0]), .b(decodificador_hex_vhdl_1_saida[1]),
    .e(decodificador_hex_vhdl_1_saida[4]), .d(decodificador_hex_vhdl_1_saida[3]),
    .c(decodificador_hex_vhdl_1_saida[2]));  // open: dp
  FF_JK_ME_PC_D_vhdl ff_jk_me_pc_d_vhdl_1 (
    .PRESET(not_17_out), .J(E_SERIAL), .CLK(CLK_out), .CLEAR(nor_1_out), .Q(out_4),
    .QN(ff_jk_me_pc_d_vhdl_1_qn));
  // NoConnect on ff_jk_me_pc_d_vhdl_1_qn
  Delay_vhdl delay_vhdl_2 (.A(E_PARALELA[2]), .B(ENABLE_out), .preset(delay_vhdl_2_preset), .clear(delay_vhdl_2_clear));
  not not_22 (not_22_out, delay_vhdl_2_preset);
  nor nor_2 (nor_2_out, delay_vhdl_2_clear, CLEAR_out);
  not not_23 (not_23_out, out_4);
  not not_24 (not_24_out, out_4);
  _7_Segment_Display u_7_segment_display_7 (
    .f(not_23_out), .a(not_24_out), .b(1'b1), .e(not_25_out), .d(not_26_out), .c(1'b1));  // open: g, dp
  _7_Segment_Display u_7_segment_display_8 (
    .f(not_28_out), .a(not_29_out), .b(1'b1), .e(not_27_out), .d(not_32_out), .c(1'b1));  // open: g, dp
  not not_25 (not_25_out, out_4);
  not not_26 (not_26_out, out_4);
  not not_27 (not_27_out, out_5);
  FF_JK_ME_PC_D_vhdl ff_jk_me_pc_d_vhdl_2 (
    .PRESET(not_22_out), .J(out_4), .CLK(CLK_out), .CLEAR(nor_2_out), .Q(out_5), .QN(ff_jk_me_pc_d_vhdl_2_qn));
  // NoConnect on ff_jk_me_pc_d_vhdl_2_qn
  not not_28 (not_28_out, out_5);
  not not_29 (not_29_out, out_5);
  not not_30 (not_30_out, out_6);
  not not_31 (not_31_out, out_6);
  _7_Segment_Display u_7_segment_display_9 (
    .f(not_30_out), .a(not_31_out), .b(1'b1), .e(not_33_out), .d(not_34_out), .c(1'b1));  // open: g, dp
  not not_32 (not_32_out, out_5);
  not not_33 (not_33_out, out_6);
  not not_34 (not_34_out, out_6);
  not not_35 (not_35_out, delay_vhdl_3_preset);
  nor nor_3 (nor_3_out, delay_vhdl_3_clear, CLEAR_out);
  not not_36 (not_36_out, out_7);
  not not_37 (not_37_out, out_7);
  _7_Segment_Display u_7_segment_display_10 (
    .f(not_36_out), .a(not_37_out), .b(1'b1), .e(not_38_out), .d(not_39_out), .c(1'b1));  // open: g, dp
  not not_38 (not_38_out, out_7);
  not not_39 (not_39_out, out_7);
  Delay_vhdl delay_vhdl_3 (.A(E_PARALELA[1]), .B(ENABLE_out), .preset(delay_vhdl_3_preset), .clear(delay_vhdl_3_clear));
  not not_40 (not_40_out, out_7);
  not not_41 (not_41_out, out_7);
  _7_Segment_Display u_7_segment_display_11 (
    .f(not_40_out), .a(not_41_out), .b(1'b1), .e(not_43_out), .d(not_42_out), .c(1'b1));  // open: g, dp
  not not_42 (not_42_out, out_7);
  not not_43 (not_43_out, out_7);
  decodificador_hex_vhdl decodificador_hex_vhdl_2 (
    .entrada({out_4, out_5, out_6, out_7}), .saida(decodificador_hex_vhdl_2_saida));
  FF_JK_ME_PC_D_vhdl ff_jk_me_pc_d_vhdl_3 (
    .PRESET(not_35_out), .J(out_5), .CLK(CLK_out), .CLEAR(nor_3_out), .Q(out_6), .QN(ff_jk_me_pc_d_vhdl_3_qn));
  // NoConnect on ff_jk_me_pc_d_vhdl_3_qn
  Delay_vhdl delay_vhdl_4 (.A(E_PARALELA[0]), .B(ENABLE_out), .preset(delay_vhdl_4_preset), .clear(delay_vhdl_4_clear));
  not not_44 (not_44_out, delay_vhdl_4_preset);
  nor nor_4 (nor_4_out, delay_vhdl_4_clear, CLEAR_out);
  _7_Segment_Display u_7_segment_display_12 (
    .g(decodificador_hex_vhdl_2_saida[6]), .f(decodificador_hex_vhdl_2_saida[5]),
    .a(decodificador_hex_vhdl_2_saida[0]), .b(decodificador_hex_vhdl_2_saida[1]),
    .e(decodificador_hex_vhdl_2_saida[4]), .d(decodificador_hex_vhdl_2_saida[3]),
    .c(decodificador_hex_vhdl_2_saida[2]));  // open: dp
  FF_JK_ME_PC_D_vhdl ff_jk_me_pc_d_vhdl_4 (
    .PRESET(not_44_out), .J(out_6), .CLK(CLK_out), .CLEAR(nor_4_out), .Q(out_7), .QN(ff_jk_me_pc_d_vhdl_4_qn));
  // NoConnect on ff_jk_me_pc_d_vhdl_4_qn

  assign S_PARALELA = {out_4, out_5, out_6, out_7};
  assign S_SERIAL = out_7;

  // Other names for the same wires on the sheet: A[3:0] = E_PARALELA; B = E_SERIAL; C = out_7;
  //   S[3:0] = {out_4, out_5, out_6, out_7}

  // Notes on the sheet:
  //   Registrador de Deslocamento VHDL
  //   ENTRADA PARALELA
  //   ENTRADA SERIAL
  //   ENTRADA
  //   SAIDA PARALELA
  //   SAIDA SERIAL
  //   SAÍDA
endmodule

module RegistradorDeDeslocamentoUniversal_vhdl (
  input  [1:0] SEL,
  input  [3:0] E_PARALELA,
  input  E_SERIAL_DIR,
  input  E_SERIAL_ESQ,
  output S_SERIAL,
  output [3:0] S_PARALELA
);

  wire CLEAR_out, CLK_out, ff_jk_me_pc_d_vhdl_1_qn, ff_jk_me_pc_d_vhdl_2_qn, ff_jk_me_pc_d_vhdl_3_qn,
       ff_jk_me_pc_d_vhdl_4_qn, mux_vhdl_1_res, mux_vhdl_2_res, mux_vhdl_3_res, mux_vhdl_4_res, not_1_out,
       not_2_out, not_3_out, not_4_out, not_5_out, not_6_out, not_7_out, not_8_out, not_9_out, not_10_out,
       not_11_out, not_12_out, not_13_out, not_14_out, not_15_out, not_16_out, not_17_out, not_18_out,
       not_19_out, not_20_out, not_21_out, not_22_out, not_23_out, not_24_out, not_25_out, not_26_out,
       not_27_out, not_28_out, not_29_out, not_30_out, not_31_out, not_32_out, not_33_out, not_34_out,
       not_35_out, not_36_out, not_37_out, not_38_out, not_39_out, not_40_out, not_41_out, not_42_out,
       not_43_out, not_44_out, not_45_out, not_46_out, not_47_out, not_48_out, not_49_out, not_50_out,
       not_51_out, not_52_out, not_53_out, not_54_out, PRESET_out;
  wire [6:0] decodificador_hex_vhdl_1_saida, decodificador_hex_vhdl_2_saida;

  Button PRESET (.out(PRESET_out));
  Button CLEAR (.out(CLEAR_out));
  Clock CLK (.out(CLK_out));
  not not_1 (not_1_out, SEL[1]);
  _7_Segment_Display u_7_segment_display_1 (
    .f(not_1_out), .a(not_6_out), .b(1'b1), .e(not_2_out), .d(not_3_out), .c(1'b1));  // open: g, dp
  not not_2 (not_2_out, SEL[1]);
  not not_3 (not_3_out, SEL[1]);
  not not_4 (not_4_out, PRESET_out);
  not not_5 (not_5_out, CLEAR_out);
  not not_6 (not_6_out, SEL[1]);
  not not_7 (not_7_out, SEL[0]);
  not not_8 (not_8_out, SEL[0]);
  _7_Segment_Display u_7_segment_display_2 (
    .f(not_7_out), .a(not_8_out), .b(1'b1), .e(not_9_out), .d(not_10_out), .c(1'b1));  // open: g, dp
  not not_9 (not_9_out, SEL[0]);
  not not_10 (not_10_out, SEL[0]);
  _7_Segment_Display u_7_segment_display_3 (
    .f(not_12_out), .a(not_13_out), .b(1'b1), .e(not_11_out), .d(not_16_out), .c(1'b1));  // open: g, dp
  not not_11 (not_11_out, E_PARALELA[3]);
  MUX_vhdl mux_vhdl_1 (
    .sel(SEL), .A(S_PARALELA[3]), .B(S_PARALELA[2]), .C(E_SERIAL_ESQ), .D(E_PARALELA[3]), .RES(mux_vhdl_1_res));
  not not_12 (not_12_out, E_PARALELA[3]);
  not not_13 (not_13_out, E_PARALELA[3]);
  not not_14 (not_14_out, E_PARALELA[2]);
  not not_15 (not_15_out, E_PARALELA[2]);
  _7_Segment_Display u_7_segment_display_4 (
    .f(not_14_out), .a(not_15_out), .b(1'b1), .e(not_17_out), .d(not_18_out), .c(1'b1));  // open: g, dp
  not not_16 (not_16_out, E_PARALELA[3]);
  not not_17 (not_17_out, E_PARALELA[2]);
  not not_18 (not_18_out, E_PARALELA[2]);
  not not_19 (not_19_out, E_PARALELA[1]);
  not not_20 (not_20_out, E_PARALELA[1]);
  not not_21 (not_21_out, E_PARALELA[0]);
  _7_Segment_Display u_7_segment_display_5 (
    .f(not_19_out), .a(not_20_out), .b(1'b1), .e(not_22_out), .d(not_23_out), .c(1'b1));  // open: g, dp
  _7_Segment_Display u_7_segment_display_6 (
    .f(not_21_out), .a(not_26_out), .b(1'b1), .e(not_24_out), .d(not_25_out), .c(1'b1));  // open: g, dp
  not not_22 (not_22_out, E_PARALELA[1]);
  not not_23 (not_23_out, E_PARALELA[1]);
  not not_24 (not_24_out, E_PARALELA[0]);
  not not_25 (not_25_out, E_PARALELA[0]);
  decodificador_hex_vhdl decodificador_hex_vhdl_1 (.entrada(E_PARALELA), .saida(decodificador_hex_vhdl_1_saida));
  not not_26 (not_26_out, E_PARALELA[0]);
  FF_JK_ME_PC_D_vhdl ff_jk_me_pc_d_vhdl_1 (
    .PRESET(not_4_out), .J(mux_vhdl_1_res), .CLK(CLK_out), .CLEAR(not_5_out), .Q(S_PARALELA[3]),
    .QN(ff_jk_me_pc_d_vhdl_1_qn));
  // NoConnect on ff_jk_me_pc_d_vhdl_1_qn
  MUX_vhdl mux_vhdl_2 (
    .sel(SEL), .A(S_PARALELA[2]), .B(S_PARALELA[1]), .C(S_PARALELA[3]), .D(E_PARALELA[2]),
    .RES(mux_vhdl_2_res));
  _7_Segment_Display u_7_segment_display_7 (
    .g(decodificador_hex_vhdl_1_saida[6]), .f(decodificador_hex_vhdl_1_saida[5]),
    .a(decodificador_hex_vhdl_1_saida[0]), .b(decodificador_hex_vhdl_1_saida[1]),
    .e(decodificador_hex_vhdl_1_saida[4]), .d(decodificador_hex_vhdl_1_saida[3]),
    .c(decodificador_hex_vhdl_1_saida[2]));  // open: dp
  not not_27 (not_27_out, E_SERIAL_ESQ);
  not not_28 (not_28_out, E_SERIAL_ESQ);
  _7_Segment_Display u_7_segment_display_8 (
    .f(not_27_out), .a(not_28_out), .b(1'b1), .e(not_29_out), .d(not_30_out), .c(1'b1));  // open: g, dp
  not not_29 (not_29_out, E_SERIAL_ESQ);
  not not_30 (not_30_out, E_SERIAL_ESQ);
  FF_JK_ME_PC_D_vhdl ff_jk_me_pc_d_vhdl_2 (
    .PRESET(not_4_out), .J(mux_vhdl_2_res), .CLK(CLK_out), .CLEAR(not_5_out), .Q(S_PARALELA[2]),
    .QN(ff_jk_me_pc_d_vhdl_2_qn));
  // NoConnect on ff_jk_me_pc_d_vhdl_2_qn
  not not_31 (not_31_out, S_PARALELA[3]);
  not not_32 (not_32_out, S_PARALELA[3]);
  _7_Segment_Display u_7_segment_display_9 (
    .f(not_31_out), .a(not_32_out), .b(1'b1), .e(not_33_out), .d(not_34_out), .c(1'b1));  // open: g, dp
  not not_33 (not_33_out, S_PARALELA[3]);
  not not_34 (not_34_out, S_PARALELA[3]);
  MUX_vhdl mux_vhdl_3 (
    .sel(SEL), .A(S_PARALELA[1]), .B(S_PARALELA[0]), .C(S_PARALELA[2]), .D(E_PARALELA[1]),
    .RES(mux_vhdl_3_res));
  not not_35 (not_35_out, S_PARALELA[2]);
  not not_36 (not_36_out, S_PARALELA[2]);
  _7_Segment_Display u_7_segment_display_10 (
    .f(not_35_out), .a(not_36_out), .b(1'b1), .e(not_37_out), .d(not_38_out), .c(1'b1));  // open: g, dp
  _7_Segment_Display u_7_segment_display_11 (
    .f(not_40_out), .a(not_41_out), .b(1'b1), .e(not_39_out), .d(not_44_out), .c(1'b1));  // open: g, dp
  not not_37 (not_37_out, S_PARALELA[2]);
  not not_38 (not_38_out, S_PARALELA[2]);
  not not_39 (not_39_out, S_PARALELA[1]);
  not not_40 (not_40_out, S_PARALELA[1]);
  not not_41 (not_41_out, S_PARALELA[1]);
  not not_42 (not_42_out, S_PARALELA[0]);
  not not_43 (not_43_out, S_PARALELA[0]);
  _7_Segment_Display u_7_segment_display_12 (
    .f(not_42_out), .a(not_43_out), .b(1'b1), .e(not_45_out), .d(not_46_out), .c(1'b1));  // open: g, dp
  not not_44 (not_44_out, S_PARALELA[1]);
  not not_45 (not_45_out, S_PARALELA[0]);
  not not_46 (not_46_out, S_PARALELA[0]);
  _7_Segment_Display u_7_segment_display_13 (
    .f(not_48_out), .a(not_49_out), .b(1'b1), .e(not_47_out), .d(not_50_out), .c(1'b1));  // open: g, dp
  not not_47 (not_47_out, E_SERIAL_DIR);
  FF_JK_ME_PC_D_vhdl ff_jk_me_pc_d_vhdl_3 (
    .PRESET(not_4_out), .J(mux_vhdl_3_res), .CLK(CLK_out), .CLEAR(not_5_out), .Q(S_PARALELA[1]),
    .QN(ff_jk_me_pc_d_vhdl_3_qn));
  // NoConnect on ff_jk_me_pc_d_vhdl_3_qn
  not not_48 (not_48_out, E_SERIAL_DIR);
  not not_49 (not_49_out, E_SERIAL_DIR);
  not not_50 (not_50_out, E_SERIAL_DIR);
  MUX_vhdl mux_vhdl_4 (
    .sel(SEL), .A(S_PARALELA[0]), .B(E_SERIAL_DIR), .C(S_PARALELA[1]), .D(E_PARALELA[0]), .RES(mux_vhdl_4_res));
  not not_51 (not_51_out, S_PARALELA[0]);
  not not_52 (not_52_out, S_PARALELA[0]);
  _7_Segment_Display u_7_segment_display_14 (
    .f(not_51_out), .a(not_52_out), .b(1'b1), .e(not_53_out), .d(not_54_out), .c(1'b1));  // open: g, dp
  not not_53 (not_53_out, S_PARALELA[0]);
  not not_54 (not_54_out, S_PARALELA[0]);
  decodificador_hex_vhdl decodificador_hex_vhdl_2 (.entrada(S_PARALELA), .saida(decodificador_hex_vhdl_2_saida));
  FF_JK_ME_PC_D_vhdl ff_jk_me_pc_d_vhdl_4 (
    .PRESET(not_4_out), .J(mux_vhdl_4_res), .CLK(CLK_out), .CLEAR(not_5_out), .Q(S_PARALELA[0]),
    .QN(ff_jk_me_pc_d_vhdl_4_qn));
  // NoConnect on ff_jk_me_pc_d_vhdl_4_qn
  _7_Segment_Display u_7_segment_display_15 (
    .g(decodificador_hex_vhdl_2_saida[6]), .f(decodificador_hex_vhdl_2_saida[5]),
    .a(decodificador_hex_vhdl_2_saida[0]), .b(decodificador_hex_vhdl_2_saida[1]),
    .e(decodificador_hex_vhdl_2_saida[4]), .d(decodificador_hex_vhdl_2_saida[3]),
    .c(decodificador_hex_vhdl_2_saida[2]));  // open: dp

  assign S_SERIAL = S_PARALELA[0];

  // Other names for the same wires on the sheet: A[1:0] = SEL; B[3:0] = E_PARALELA; C = E_SERIAL_ESQ;
  //   D[3:0] = S_PARALELA; F = S_PARALELA[0]; E = E_SERIAL_DIR

  // Notes on the sheet:
  //   00 - MANTER
  //   01 - SHIFT A ESQ
  //   10 - SHIFT A DIR
  //   11 - CARGA PARALELA
  //   Registrador de Deslocamento Universal VHDL
  //   SELETOR
  //   ENTRADA PARALELA
  //   ENTRADA
  //   ENTRADA SERIAL ESQ
  //   ------->
  //   SAIDA PARALELA
  //   <-------
  //   ENTRADA SERIAL DIR
  //   SAIDA SERIAL
  //   ENTRADA
endmodule

// VHDL entity FF_RS_vhdl, as the project stores it:
library IEEE;
use IEEE.STD_LOGIC_1164.ALL;

entity FF_RS_vhdl is
    Port ( set   : in  STD_LOGIC;  
           clk   : in  STD_LOGIC;  
           reset : in  STD_LOGIC; 
           Q     : out STD_LOGIC; 
           Ql    : out STD_LOGIC); 
end FF_RS_vhdl;

architecture Behavioral of FF_RS_vhdl is
    signal Q_int : STD_LOGIC := '0';
begin
    process (clk, reset, set)
    begin
        if reset = '1' then
            Q_int <= '0';
        elsif set = '1' then
            Q_int <= '1';
        elsif falling_edge(clk) then
            Q_int <= Q_int;
        end if;
    end process;
    
    Q <= Q_int;
    
    Ql <= not Q_int;

end Behavioral;

// VHDL entity FF_JK_vhdl, as the project stores it:
library IEEE;
use IEEE.STD_LOGIC_1164.ALL;

entity FF_JK_vhdl is
    Port ( J     : in  STD_LOGIC;   
           clk   : in  STD_LOGIC;   
           K     : in  STD_LOGIC;   
           Q     : out STD_LOGIC;   
           Ql    : out STD_LOGIC);  
end FF_JK_vhdl;

architecture Behavioral of FF_JK_vhdl is
    signal Q_int : STD_LOGIC := '0';  
begin
    process (clk)
    begin
        if falling_edge(clk) then
            case (STD_LOGIC_VECTOR'(J & K)) is  
                when "00" =>  
                    Q_int <= Q_int;
                when "01" =>  
                    Q_int <= '0';
                when "10" =>  
                    Q_int <= '1';
                when "11" =>  
                    Q_int <= not Q_int;
                when others =>  
                    Q_int <= Q_int;
            end case;
        end if;
    end process;
    
    Q <= Q_int;
    Ql <= not Q_int;

end Behavioral;

// VHDL entity FF_JK_PC_vhdl, as the project stores it:
library IEEE;
use IEEE.STD_LOGIC_1164.ALL;

entity FF_JK_PC_vhdl is
    Port ( preset : in  STD_LOGIC;   
           J      : in  STD_LOGIC;   
           clk    : in  STD_LOGIC;   
           K      : in  STD_LOGIC;   
           Q      : out STD_LOGIC;   
           Ql     : out STD_LOGIC;   
           clear  : in  STD_LOGIC);  
end FF_JK_PC_vhdl;

architecture Behavioral of FF_JK_PC_vhdl is
    signal Q_int : STD_LOGIC := '0';  
begin
    process (clk, preset, clear)
    begin
        if clear = '1' then
            Q_int <= '0';  
        elsif preset = '1' then
            Q_int <= '1';  
        elsif rising_edge(clk) then
            case (std_logic_vector'(J & K)) is  
                when "00" =>  
                    Q_int <= Q_int;  
                when "01" =>  
                    Q_int <= '0';  
                when "10" =>  
                    Q_int <= '1';  
                when "11" =>  
                    Q_int <= not Q_int;  
                when others =>  
                    Q_int <= Q_int;  
            end case;
        end if;
    end process;
    
    Q <= Q_int;
    Ql <= not Q_int;

end Behavioral;

// VHDL entity FF_JK_ME_PC_vhdl, as the project stores it:
library IEEE;
use IEEE.STD_LOGIC_1164.ALL;

entity FF_JK_ME_PC_vhdl is
    Port ( preset : in  STD_LOGIC;   
           J      : in  STD_LOGIC;   
           clk    : in  STD_LOGIC;   
           K      : in  STD_LOGIC;   
           Q      : out STD_LOGIC;   
           Ql     : out STD_LOGIC;   
           clear  : in  STD_LOGIC);  
end FF_JK_ME_PC_vhdl;

architecture Behavioral of FF_JK_ME_PC_vhdl is
    signal Q_int_master  : STD_LOGIC := '0';  
    signal Q_int_slave   : STD_LOGIC := '0';  
begin  

    process (preset, clear, clk)
    begin
        if clear = '1' then
            Q_int_master <= '0';  
        elsif preset = '1' then
            Q_int_master <= '1';    
        elsif rising_edge(clk) then
            case (std_logic_vector'(J & K)) is
                when "00" =>  
                    Q_int_master <= Q_int_master;  
                when "01" =>  
                    Q_int_master <= '0';  
                when "10" =>  
                    Q_int_master <= '1';  
                when "11" =>  
                    Q_int_master <= not Q_int_master;  
                when others =>  
                    Q_int_master <= Q_int_master;  
            end case;
        end if;
    end process;

    Q_int_slave <= Q_int_master;
    Q <= Q_int_slave;  
    Ql <= not Q_int_slave;  

end Behavioral;

// VHDL entity FF_JK_ME_PC_D_vhdl, as the project stores it:
library IEEE;
use IEEE.STD_LOGIC_1164.ALL;

entity FF_JK_ME_PC_D_vhdl is
    Port (
	   PRESET : in STD_LOGIC;
        J      : in STD_LOGIC;
        CLK    : in STD_LOGIC;
        CLEAR  : in STD_LOGIC;
        Q      : out STD_LOGIC;
        QN     : out STD_LOGIC
    );
end FF_JK_ME_PC_D_vhdl;

architecture Behavioral of FF_JK_ME_PC_D_vhdl is
    signal master_q : STD_LOGIC := '0'; 
    signal slave_q : STD_LOGIC := '0';
begin

    process(CLK, PRESET, CLEAR)
    begin
        if (CLEAR = '0') then
            master_q <= '0';
        elsif (PRESET = '0') then
            master_q <= '1';
        elsif rising_edge(CLK) then
            if (J = '0') then
                master_q <= '0'; 
            elsif (J = '1') then
                master_q <= '1'; 
            end if;
        end if;
    end process;

 
    process(CLK, PRESET, CLEAR)
    begin
        if (CLEAR = '0') then
            slave_q <= '0';
        elsif (PRESET = '0') then
            slave_q <= '1';
        elsif falling_edge(CLK) then
            slave_q <= master_q; 
        end if;
    end process;


    Q  <= slave_q;
    QN <= NOT slave_q;


end Behavioral;

// VHDL entity FF_JK_ME_PC_T_vhdl, as the project stores it:
library IEEE;
use IEEE.STD_LOGIC_1164.ALL;

entity FF_JK_ME_PC_T_vhdl is
    Port (
	   PRESET : in STD_LOGIC;
        J      : in STD_LOGIC;
        CLK    : in STD_LOGIC;
        CLEAR  : in STD_LOGIC;
        Q      : out STD_LOGIC;
        QN     : out STD_LOGIC
    );
end FF_JK_ME_PC_T_vhdl;

architecture Behavioral of FF_JK_ME_PC_T_vhdl is
    signal master_q : STD_LOGIC := '0'; 
    signal slave_q : STD_LOGIC := '0';
begin

    process(CLK, PRESET, CLEAR)
    begin
        if (CLEAR = '0') then
            master_q <= '0';
        elsif (PRESET = '0') then
            master_q <= '1';
        elsif rising_edge(CLK) then
            if (J = '0') then
                master_q <= master_q; 
            elsif (J = '1') then
                master_q <= NOT master_q; 
            end if;
        end if;
    end process;

 
    process(CLK, PRESET, CLEAR)
    begin
        if (CLEAR = '0') then
            slave_q <= '0';
        elsif (PRESET = '0') then
            slave_q <= '1';
        elsif falling_edge(CLK) then
            slave_q <= master_q; 
        end if;
    end process;


    Q  <= slave_q;
    QN <= NOT slave_q;


end Behavioral;

// VHDL entity decodificador_hex_vhdl, as the project stores it:
library IEEE;
use IEEE.STD_LOGIC_1164.ALL;

entity decodificador_hex_vhdl is
    Port (
        entrada : in STD_LOGIC_VECTOR(3 downto 0);
        saida   : out STD_LOGIC_VECTOR(6 downto 0)
    );
end decodificador_hex_vhdl;

architecture Behavioral of decodificador_hex_vhdl is
begin
    process(entrada)
    begin
        case entrada is
            when "0000" => saida <= "0111111";
            when "0001" => saida <= "0000110";
            when "0010" => saida <= "1011011";
            when "0011" => saida <= "1001111";
            when "0100" => saida <= "1100110";
            when "0101" => saida <= "1101101";
            when "0110" => saida <= "1111101";
            when "0111" => saida <= "0000111";
            when "1000" => saida <= "1111111";
            when "1001" => saida <= "1101111";
            when "1010" => saida <= "1110111";
            when "1011" => saida <= "1111100";
            when "1100" => saida <= "0111001";
            when "1101" => saida <= "1011110";
            when "1110" => saida <= "1111001";
            when "1111" => saida <= "1110001";
            when others => saida <= "0000000";
        end case;
    end process;
end Behavioral;

// VHDL entity Delay_vhdl, as the project stores it:
library IEEE;
use IEEE.STD_LOGIC_1164.ALL;

entity Delay_vhdl is
    Port ( A       : in  STD_LOGIC;   
           B       : in  STD_LOGIC;   
           preset  : out STD_LOGIC;   
           clear   : out STD_LOGIC    
           );
end Delay_vhdl;

architecture Behavioral of Delay_vhdl is
begin
    process(A, B)
    begin
        if (A = '0' and B = '0') then
            preset <= '0';
            clear  <= '0';
        elsif (A = '0' and B = '1') then
            preset <= '0';
            clear  <= '1';
        elsif (A = '1' and B = '0') then
            preset <= '0';
            clear  <= '0';
        elsif (A = '1' and B = '1') then
            preset <= '1';
            clear  <= '0';
        end if;
    end process;
end Behavioral;

// VHDL entity MUX_vhdl, as the project stores it:
LIBRARY ieee;
USE ieee.std_logic_1164.all;

ENTITY MUX_vhdl IS
  PORT (
    sel      : IN  std_logic_vector(1 downto 0);
    A        : IN  std_logic;
    B        : IN  std_logic;
    C        : IN  std_logic;
    D        : IN  std_logic;
    RES      : OUT std_logic
    );
END MUX_vhdl;

ARCHITECTURE TypeArchitecture OF MUX_vhdl IS

BEGIN
    process (sel,A,B,C,D)
    BEGIN
        IF SEL = "00" THEN
            RES <= A;
        ELSIF SEL = "01" THEN
            RES <= B;
        ELSIF SEL = "10" THEN
            RES <= C;
        ELSIF SEL = "11" THEN
            RES <= D;
        END IF;
    END PROCESS;

END TypeArchitecture;
