// Logisim project FlipFlops.circ as structural Verilog
module FF_JK_ME_PC (
  input  J,
  input  K,
  output Q,
  output Qq
);

  wire clock_1_out, CLR_out, nand_1_out, nand_2_out, nand_3_out, nand_4_out, nand_5_out, nand_6_out,
       not_1_out, not_2_out, not_3_out, PR_out;

  Clock clock_1 (.out(clock_1_out));
  nand nand_1 (nand_1_out, J, clock_1_out, Qq);
  nand nand_2 (nand_2_out, Q, clock_1_out, K);
  Button PR (.out(PR_out));
  not not_1 (not_1_out, PR_out);
  not not_2 (not_2_out, CLR_out);
  Button CLR (.out(CLR_out));
  nand nand_3 (nand_3_out, not_1_out, nand_1_out, nand_4_out);
  nand nand_4 (nand_4_out, nand_3_out, nand_2_out, not_2_out);
  not not_3 (not_3_out, clock_1_out);
  nand nand_5 (nand_5_out, nand_3_out, not_3_out);
  nand nand_6 (nand_6_out, not_3_out, nand_4_out);
  nand nand_7 (Q, not_1_out, nand_5_out, Qq);
  nand nand_8 (Qq, Q, nand_6_out, not_2_out);

  // Notes on the sheet:
  //   Flip-Flop JK Mestre-Escravo com Entrada Preset e Clear
endmodule

module FF_JK_ME_PC_T (
  input  J,
  output Q,
  output Qq
);

  wire clock_1_out, CLR_out, nand_1_out, nand_2_out, nand_3_out, nand_4_out, nand_5_out, nand_6_out,
       not_1_out, not_2_out, not_3_out, PR_out;

  Clock clock_1 (.out(clock_1_out));
  nand nand_1 (nand_1_out, J, clock_1_out, Qq);
  nand nand_2 (nand_2_out, Q, clock_1_out, J);
  Button PR (.out(PR_out));
  not not_1 (not_1_out, PR_out);
  not not_2 (not_2_out, CLR_out);
  Button CLR (.out(CLR_out));
  nand nand_3 (nand_3_out, not_1_out, nand_1_out, nand_4_out);
  nand nand_4 (nand_4_out, nand_3_out, nand_2_out, not_2_out);
  not not_3 (not_3_out, clock_1_out);
  nand nand_5 (nand_5_out, nand_3_out, not_3_out);
  nand nand_6 (nand_6_out, not_3_out, nand_4_out);
  nand nand_7 (Q, not_1_out, nand_5_out, Qq);
  nand nand_8 (Qq, Q, nand_6_out, not_2_out);

  // Notes on the sheet:
  //   Flip-Flop JK Mestre-Escravo com Entrada Preset e Clear T
endmodule

module FF_JK_ME_PC_D (
  input  J,
  output Q,
  output Qq
);

  wire clock_1_out, CLR_out, nand_1_out, nand_2_out, nand_3_out, nand_4_out, nand_5_out, nand_6_out,
       not_1_out, not_2_out, not_3_out, not_4_out, PR_out;

  Clock clock_1 (.out(clock_1_out));
  not not_1 (not_1_out, J);
  nand nand_1 (nand_1_out, J, clock_1_out, Qq);
  nand nand_2 (nand_2_out, Q, clock_1_out, not_1_out);
  Button PR (.out(PR_out));
  not not_2 (not_2_out, PR_out);
  not not_3 (not_3_out, CLR_out);
  Button CLR (.out(CLR_out));
  nand nand_3 (nand_3_out, not_2_out, nand_1_out, nand_4_out);
  nand nand_4 (nand_4_out, nand_3_out, nand_2_out, not_3_out);
  not not_4 (not_4_out, clock_1_out);
  nand nand_5 (nand_5_out, nand_3_out, not_4_out);
  nand nand_6 (nand_6_out, not_4_out, nand_4_out);
  nand nand_7 (Q, not_2_out, nand_5_out, Qq);
  nand nand_8 (Qq, Q, nand_6_out, not_3_out);

  // Notes on the sheet:
  //   Flip-Flop JK Mestre-Escravo com Entrada Preset e Clear T
endmodule
