// Logisim project antonioInacioNeto20242.circ as structural Verilog
module main (
);

  andNAND andnand_1 ();  // open: A, B, S
  notNAND notnand_1 ();  // open: A, S
  HalfSubtractor halfsubtractor_1 ();  // open: A, B, S, Cout
  xorNAND xornand_1 ();  // open: A, B, S
  orNAND ornand_1 ();  // open: A, B, S
  FullSubtractor fullsubtractor_1 ();  // open: A, B, Cin, S, Cout
  HalfAdder halfadder_1 ();  // open: A, B, S, Cout
  TwoComplementSubtractor4BITSVHDL twocomplementsubtractor4bitsvhdl_1 ();  // open: A, B, S, OVERF
  HalfSubtractorNAND halfsubtractornand_1 ();  // open: A, B, S, Cout
  HalfAdderNAND halfaddernand_1 ();  // open: A, B, S, Cout
  FullAdder fulladder_1 ();  // open: A, B, Cin, S, Cout
  FullSubtractorNAND fullsubtractornand_1 ();  // open: A, B, Cin, S, Cout
  FullAdderNAND fulladdernand_1 ();  // open: A, B, Cin, S, Cout
  HalfAdderSubtractor halfaddersubtractor_1 ();  // open: M, A, B, Cin, S, Cout
  HalfAdderSubtractorNAND halfaddersubtractornand_1 ();  // open: M, A, B, Cin, S, Cout
  AdderSubtractor4BITSVHDL addersubtractor4bitsvhdl_1 ();  // open: M, A, B, S, OVERF
  AdderSubtractor4BITS addersubtractor4bits_1 ();  // open: A3, A2, A1, A0, B3, B2, B1, B0, M, OVERF, S3, S2, S1, S0
  AdderSubtractor4BITSNAND addersubtractor4bitsnand_1 ();  // open: A3, A2, A1, A0, B3, B2, B1, B0, M, OVERF, S3, S2, S1, S0
  Adder4BITSVHDL adder4bitsvhdl_1 ();  // open: A, B, S, OVERF
  Subtractor4BITS subtractor4bits_1 ();  // open: A3, A2, A1, A0, B3, B2, B1, B0, OVERF, S3, S2, S1, S0
  Subtractor4BITSNAND subtractor4bitsnand_1 ();  // open: A3, A2, A1, A0, B3, B2, B1, B0, OVERF, S3, S2, S1, S0
  Subtractor4BITSVHDL subtractor4bitsvhdl_1 ();  // open: A, B, S, OVERF
  Adder4BITS adder4bits_1 ();  // open: A3, A2, A1, A0, B3, B2, B1, B0, OVERF, S3, S2, S1, S0
  Adder4BITSNAND adder4bitsnand_1 ();  // open: A3, A2, A1, A0, B3, B2, B1, B0, OVERF, S3, S2, S1, S0
  HalfAdderSubtractorVHDL halfaddersubtractorvhdl_1 ();  // open: A, B, Cin, M, S, Cout
  TwoComplementSubtractor4BITS twocomplementsubtractor4bits_1 ();  // open: A3, A2, A1, A0, B3, B2, B1, B0, OVERF, S3, S2, S1, S0
  TwoComplementSubtractor4BITSNAND twocomplementsubtractor4bitsnand_1 ();  // open: A3, A2, A1, A0, B3, B2, B1, B0, OVERF, S3, S2, S1, S0
  FullAdderVHDL fulladdervhdl_1 ();  // open: A, B, Cin, S, Cout
  FullSubtractorVHDL fullsubtractorvhdl_1 ();  // open: A, B, Cin, S, Cout
  HalfAdderVHDL halfaddervhdl_1 ();  // open: A, B, S, Cout
  HalfSubtractorVHDL halfsubtractorvhdl_1 ();  // open: A, B, S, Cout
endmodule

module TwoComplementSubtractor4BITS (
  input  A3,
  input  A2,
  input  A1,
  input  A0,
  input  B3,
  input  B2,
  input  B1,
  input  B0,
  output OVERF,
  output S3,
  output S2,
  output S1,
  output S0
);

  wire fulladder_2_cout, fulladder_3_cout, fulladder_4_cout, not_1_out, not_2_out, not_3_out, not_4_out;

  FullAdder fulladder_1 (.A(A3), .B(not_1_out), .Cin(fulladder_2_cout), .S(S3), .Cout(OVERF));
  FullAdder fulladder_2 (.A(A2), .B(not_2_out), .Cin(fulladder_3_cout), .S(S2), .Cout(fulladder_2_cout));
  not not_1 (not_1_out, B3);
  not not_2 (not_2_out, B2);
  not not_3 (not_3_out, B1);
  FullAdder fulladder_3 (.A(A1), .B(not_3_out), .Cin(fulladder_4_cout), .S(S1), .Cout(fulladder_3_cout));
  not not_4 (not_4_out, B0);
  FullAdder fulladder_4 (.A(A0), .B(not_4_out), .Cin(1'b1), .S(S0), .Cout(fulladder_4_cout));
endmodule

module Adder4BITS (
  input  A3,
  input  A2,
  input  A1,
  input  A0,
  input  B3,
  input  B2,
  input  B1,
  input  B0,
  output OVERF,
  output S3,
  output S2,
  output S1,
  output S0
);

  wire fulladder_2_cout, fulladder_3_cout, fulladder_4_cout;

  FullAdder fulladder_1 (.A(A3), .B(B3), .Cin(fulladder_2_cout), .S(S3), .Cout(OVERF));
  FullAdder fulladder_2 (.A(A2), .B(B2), .Cin(fulladder_3_cout), .S(S2), .Cout(fulladder_2_cout));
  FullAdder fulladder_3 (.A(A1), .B(B1), .Cin(fulladder_4_cout), .S(S1), .Cout(fulladder_3_cout));
  FullAdder fulladder_4 (.A(A0), .B(B0), .Cin(1'b0), .S(S0), .Cout(fulladder_4_cout));
endmodule

module Subtractor4BITS (
  input  A3,
  input  A2,
  input  A1,
  input  A0,
  input  B3,
  input  B2,
  input  B1,
  input  B0,
  output OVERF,
  output S3,
  output S2,
  output S1,
  output S0
);

  wire fullsubtractor_2_cout, fullsubtractor_3_cout, fullsubtractor_4_cout;

  FullSubtractor fullsubtractor_1 (.A(A3), .B(B3), .Cin(fullsubtractor_2_cout), .S(S3), .Cout(OVERF));
  FullSubtractor fullsubtractor_2 (.A(A2), .B(B2), .Cin(fullsubtractor_3_cout), .S(S2), .Cout(fullsubtractor_2_cout));
  FullSubtractor fullsubtractor_3 (.A(A1), .B(B1), .Cin(fullsubtractor_4_cout), .S(S1), .Cout(fullsubtractor_3_cout));
  FullSubtractor fullsubtractor_4 (.A(A0), .B(B0), .Cin(1'b0), .S(S0), .Cout(fullsubtractor_4_cout));
endmodule

module AdderSubtractor4BITS (
  input  A3,
  input  A2,
  input  A1,
  input  A0,
  input  B3,
  input  B2,
  input  B1,
  input  B0,
  input  M,
  output OVERF,
  output S3,
  output S2,
  output S1,
  output S0
);

  wire halfaddersubtractor_2_cout, halfaddersubtractor_3_cout, halfaddersubtractor_4_cout;

  HalfAdderSubtractor halfaddersubtractor_1 (
    .M(M), .A(A3), .B(B3), .Cin(halfaddersubtractor_2_cout), .S(S3), .Cout(OVERF));
  HalfAdderSubtractor halfaddersubtractor_2 (
    .M(M), .A(A2), .B(B2), .Cin(halfaddersubtractor_3_cout), .S(S2), .Cout(halfaddersubtractor_2_cout));
  HalfAdderSubtractor halfaddersubtractor_3 (
    .M(M), .A(A1), .B(B1), .Cin(halfaddersubtractor_4_cout), .S(S1), .Cout(halfaddersubtractor_3_cout));
  HalfAdderSubtractor halfaddersubtractor_4 (
    .M(M), .A(A0), .B(B0), .Cin(1'b0), .S(S0), .Cout(halfaddersubtractor_4_cout));
endmodule

module HalfAdderSubtractor (
  input  M,
  input  A,
  input  B,
  input  Cin,
  output S,
  output Cout
);

  wire and_1_out, and_2_out, and_3_out, xor_1_out, xor_2_out;

  xor xor_1 (xor_1_out, M, A);
  xor xor_2 (xor_2_out, A, B);
  and and_1 (and_1_out, xor_1_out, B);
  and and_2 (and_2_out, xor_1_out, Cin);
  and and_3 (and_3_out, B, Cin);
  xor xor_3 (S, xor_2_out, Cin);
  or or_1 (Cout, and_1_out, and_2_out, and_3_out);

  // Notes on the sheet:
  //   S = (A ⊕ B) ⊕ (Cin)
  //   Cout = ((M ⊕ A) . B) + ((M ⊕ A) . Cin) + (B . Cin)
endmodule

module FullAdder (
  input  A,
  input  B,
  input  Cin,
  output S,
  output Cout
);

  wire and_1_out, and_2_out, and_3_out, xor_1_out;

  xor xor_1 (xor_1_out, A, B);
  and and_1 (and_1_out, A, B);
  and and_2 (and_2_out, A, Cin);
  and and_3 (and_3_out, B, Cin);
  xor xor_2 (S, xor_1_out, Cin);
  or or_1 (Cout, and_1_out, and_2_out, and_3_out);

  // Notes on the sheet:
  //   S = (A ⊕ B) ⊕ Cin
  //   Cout = (A . B) + (A . Cin) + (B . Cin)
endmodule

module FullSubtractor (
  input  A,
  input  B,
  input  Cin,
  output S,
  output Cout
);

  wire and_1_out, and_2_out, and_3_out, not_1_out, xor_1_out;

  not not_1 (not_1_out, A);
  xor xor_1 (xor_1_out, A, B);
  and and_1 (and_1_out, not_1_out, B);
  and and_2 (and_2_out, not_1_out, Cin);
  and and_3 (and_3_out, B, Cin);
  xor xor_2 (S, xor_1_out, Cin);
  or or_1 (Cout, and_1_out, and_2_out, and_3_out);

  // Notes on the sheet:
  //   S = (A ⊕ B) ⊕ Cin
  //   Cout = (A' . B) + (A' . Cin) + (B . Cin)
endmodule

module HalfAdder (
  input  A,
  input  B,
  output S,
  output Cout
);

  xor xor_1 (S, A, B);
  and and_1 (Cout, A, B);

  // Notes on the sheet:
  //   S = A ⊕ B
  //   Cout = (A . B)
endmodule

module HalfSubtractor (
  input  A,
  input  B,
  output S,
  output Cout
);

  wire not_1_out;

  not not_1 (not_1_out, A);
  xor xor_1 (S, A, B);
  and and_1 (Cout, not_1_out, B);

  // Notes on the sheet:
  //   S = (A ⊕ B)
  //   Cout = (A' . B)
endmodule

module TwoComplementSubtractor4BITSNAND (
  input  A3,
  input  A2,
  input  A1,
  input  A0,
  input  B3,
  input  B2,
  input  B1,
  input  B0,
  output OVERF,
  output S3,
  output S2,
  output S1,
  output S0
);

  wire fulladdernand_2_cout, fulladdernand_3_cout, fulladdernand_4_cout, not_1_out, not_2_out, not_3_out,
       not_4_out;

  FullAdderNAND fulladdernand_1 (.A(A3), .B(not_1_out), .Cin(fulladdernand_2_cout), .S(S3), .Cout(OVERF));
  FullAdderNAND fulladdernand_2 (
    .A(A2), .B(not_2_out), .Cin(fulladdernand_3_cout), .S(S2), .Cout(fulladdernand_2_cout));
  not not_1 (not_1_out, B3);
  not not_2 (not_2_out, B2);
  not not_3 (not_3_out, B1);
  FullAdderNAND fulladdernand_3 (
    .A(A1), .B(not_3_out), .Cin(fulladdernand_4_cout), .S(S1), .Cout(fulladdernand_3_cout));
  not not_4 (not_4_out, B0);
  FullAdderNAND fulladdernand_4 (.A(A0), .B(not_4_out), .Cin(1'b1), .S(S0), .Cout(fulladdernand_4_cout));
endmodule

module Adder4BITSNAND (
  input  A3,
  input  A2,
  input  A1,
  input  A0,
  input  B3,
  input  B2,
  input  B1,
  input  B0,
  output OVERF,
  output S3,
  output S2,
  output S1,
  output S0
);

  wire fulladdernand_2_cout, fulladdernand_3_cout, fulladdernand_4_cout;

  FullAdderNAND fulladdernand_1 (.A(A3), .B(B3), .Cin(fulladdernand_2_cout), .S(S3), .Cout(OVERF));
  FullAdderNAND fulladdernand_2 (.A(A2), .B(B2), .Cin(fulladdernand_3_cout), .S(S2), .Cout(fulladdernand_2_cout));
  FullAdderNAND fulladdernand_3 (.A(A1), .B(B1), .Cin(fulladdernand_4_cout), .S(S1), .Cout(fulladdernand_3_cout));
  FullAdderNAND fulladdernand_4 (.A(A0), .B(B0), .Cin(1'b0), .S(S0), .Cout(fulladdernand_4_cout));
endmodule

module Subtractor4BITSNAND (
  input  A3,
  input  A2,
  input  A1,
  input  A0,
  input  B3,
  input  B2,
  input  B1,
  input  B0,
  output OVERF,
  output S3,
  output S2,
  output S1,
  output S0
);

  wire fullsubtractornand_2_cout, fullsubtractornand_3_cout, fullsubtractornand_4_cout;

  FullSubtractorNAND fullsubtractornand_1 (.A(A3), .B(B3), .Cin(fullsubtractornand_2_cout), .S(S3), .Cout(OVERF));
  FullSubtractorNAND fullsubtractornand_2 (
    .A(A2), .B(B2), .Cin(fullsubtractornand_3_cout), .S(S2), .Cout(fullsubtractornand_2_cout));
  FullSubtractorNAND fullsubtractornand_3 (
    .A(A1), .B(B1), .Cin(fullsubtractornand_4_cout), .S(S1), .Cout(fullsubtractornand_3_cout));
  FullSubtractorNAND fullsubtractornand_4 (.A(A0), .B(B0), .Cin(1'b0), .S(S0), .Cout(fullsubtractornand_4_cout));
endmodule

module AdderSubtractor4BITSNAND (
  input  A3,
  input  A2,
  input  A1,
  input  A0,
  input  B3,
  input  B2,
  input  B1,
  input  B0,
  input  M,
  output OVERF,
  output S3,
  output S2,
  output S1,
  output S0
);

  wire halfaddersubtractornand_2_cout, halfaddersubtractornand_3_cout, halfaddersubtractornand_4_cout;

  HalfAdderSubtractorNAND halfaddersubtractornand_1 (
    .M(M), .A(A3), .B(B3), .Cin(halfaddersubtractornand_2_cout), .S(S3), .Cout(OVERF));
  HalfAdderSubtractorNAND halfaddersubtractornand_2 (
    .M(M), .A(A2), .B(B2), .Cin(halfaddersubtractornand_3_cout), .S(S2), .Cout(halfaddersubtractornand_2_cout));
  HalfAdderSubtractorNAND halfaddersubtractornand_3 (
    .M(M), .A(A1), .B(B1), .Cin(halfaddersubtractornand_4_cout), .S(S1), .Cout(halfaddersubtractornand_3_cout));
  HalfAdderSubtractorNAND halfaddersubtractornand_4 (
    .M(M), .A(A0), .B(B0), .Cin(1'b0), .S(S0), .Cout(halfaddersubtractornand_4_cout));
endmodule

module HalfAdderSubtractorNAND (
  input  M,
  input  A,
  input  B,
  input  Cin,
  output S,
  output Cout
);

  wire andnand_1_s, andnand_2_s, andnand_3_s, ornand_1_s, xornand_1_s, xornand_2_s;

  xorNAND xornand_1 (.A(A), .B(M), .S(xornand_1_s));
  xorNAND xornand_2 (.A(A), .B(B), .S(xornand_2_s));
  andNAND andnand_1 (.A(xornand_1_s), .B(B), .S(andnand_1_s));
  andNAND andnand_2 (.A(xornand_1_s), .B(Cin), .S(andnand_2_s));
  andNAND andnand_3 (.A(B), .B(Cin), .S(andnand_3_s));
  xorNAND xornand_3 (.A(xornand_2_s), .B(Cin), .S(S));
  orNAND ornand_1 (.A(andnand_1_s), .B(andnand_2_s), .S(ornand_1_s));
  orNAND ornand_2 (.A(ornand_1_s), .B(andnand_3_s), .S(Cout));

  // Notes on the sheet:
  //   S = (A ⊕ B) ⊕ (Cin)
  //   Cout = ((M ⊕ A) . B) + ((M ⊕ A) . Cin) + (B . Cin)
endmodule

module FullAdderNAND (
  input  A,
  input  B,
  input  Cin,
  output S,
  output Cout
);

  wire andnand_1_s, andnand_2_s, andnand_3_s, ornand_1_s, xornand_1_s;

  xorNAND xornand_1 (.A(A), .B(B), .S(xornand_1_s));
  xorNAND xornand_2 (.A(xornand_1_s), .B(Cin), .S(S));
  andNAND andnand_1 (.A(A), .B(B), .S(andnand_1_s));
  andNAND andnand_2 (.A(A), .B(Cin), .S(andnand_2_s));
  andNAND andnand_3 (.A(B), .B(Cin), .S(andnand_3_s));
  orNAND ornand_1 (.A(andnand_1_s), .B(andnand_2_s), .S(ornand_1_s));
  orNAND ornand_2 (.A(ornand_1_s), .B(andnand_3_s), .S(Cout));

  // Notes on the sheet:
  //   S = (A ⊕ B) ⊕ Cin
  //   Cout = (A . B) + (A . Cin) + (B . Cin)
endmodule

module FullSubtractorNAND (
  input  A,
  input  B,
  input  Cin,
  output S,
  output Cout
);

  wire andnand_1_s, andnand_2_s, andnand_3_s, notnand_1_s, ornand_1_s, xornand_1_s;

  notNAND notnand_1 (.A(A), .S(notnand_1_s));
  xorNAND xornand_1 (.A(A), .B(B), .S(xornand_1_s));
  xorNAND xornand_2 (.A(xornand_1_s), .B(Cin), .S(S));
  andNAND andnand_1 (.A(notnand_1_s), .B(B), .S(andnand_1_s));
  andNAND andnand_2 (.A(notnand_1_s), .B(Cin), .S(andnand_2_s));
  andNAND andnand_3 (.A(B), .B(Cin), .S(andnand_3_s));
  orNAND ornand_1 (.A(andnand_1_s), .B(andnand_2_s), .S(ornand_1_s));
  orNAND ornand_2 (.A(ornand_1_s), .B(andnand_3_s), .S(Cout));

  // Notes on the sheet:
  //   S = (A ⊕ B) ⊕ Cin
  //   Cout = (A' . B) + (A' . Cin) + (B . Cin)
endmodule

module HalfAdderNAND (
  input  A,
  input  B,
  output S,
  output Cout
);

  xorNAND xornand_1 (.A(A), .B(B), .S(S));
  andNAND andnand_1 (.A(A), .B(B), .S(Cout));

  // Notes on the sheet:
  //   S = A ⊕ B
  //   Cout = (A . B)
endmodule

module HalfSubtractorNAND (
  input  A,
  input  B,
  output S,
  output Cout
);

  wire notnand_1_s;

  xorNAND xornand_1 (.A(A), .B(B), .S(S));
  notNAND notnand_1 (.A(A), .S(notnand_1_s));
  andNAND andnand_1 (.A(notnand_1_s), .B(B), .S(Cout));

  // Notes on the sheet:
  //   S = (A ⊕ B)
  //   Cout = (A' . B)
endmodule

module xorNAND (
  input  A,
  input  B,
  output S
);

  wire andnand_1_s, andnand_2_s, notnand_1_s, notnand_2_s;

  notNAND notnand_1 (.A(A), .S(notnand_1_s));
  notNAND notnand_2 (.A(B), .S(notnand_2_s));
  andNAND andnand_1 (.A(notnand_1_s), .B(B), .S(andnand_1_s));
  andNAND andnand_2 (.A(A), .B(notnand_2_s), .S(andnand_2_s));
  orNAND ornand_1 (.A(andnand_1_s), .B(andnand_2_s), .S(S));
endmodule

module orNAND (
  input  A,
  input  B,
  output S
);

  wire notnand_1_s, notnand_2_s;

  notNAND notnand_1 (.A(A), .S(notnand_1_s));
  notNAND notnand_2 (.A(B), .S(notnand_2_s));
  nand nand_1 (S, notnand_1_s, notnand_2_s);
endmodule

module andNAND (
  input  A,
  input  B,
  output S
);

  wire nand_1_out;

  nand nand_1 (nand_1_out, A, B);
  notNAND notnand_1 (.A(nand_1_out), .S(S));
endmodule

module notNAND (
  input  A,
  output S
);

  nand nand_1 (S, A, A);
endmodule

// VHDL entity HalfSubtractorVHDL, as the project stores it:
LIBRARY ieee;
USE ieee.std_logic_1164.all;

ENTITY HalfSubtractorVHDL IS
  PORT (
    A      : IN  std_logic;
    B      : IN  std_logic;
    S      : OUT std_logic;
    Cout   : OUT std_logic
  );
END HalfSubtractorVHDL;

ARCHITECTURE TypeArchitecture OF HalfSubtractorVHDL IS
BEGIN
  S <= A XOR B;
  Cout <= NOT A AND B;
END TypeArchitecture;

// VHDL entity HalfAdderVHDL, as the project stores it:
LIBRARY ieee;
USE ieee.std_logic_1164.all;

ENTITY HalfAdderVHDL IS
  PORT (
    A      : IN  std_logic;
    B      : IN  std_logic;
    S      : OUT std_logic;
    Cout   : OUT std_logic
  );
END HalfAdderVHDL;

ARCHITECTURE TypeArchitecture OF HalfAdderVHDL IS
BEGIN
  S <= A XOR B;
  Cout <= A AND B;
END TypeArchitecture;

// VHDL entity FullSubtractorVHDL, as the project stores it:
LIBRARY ieee;
USE ieee.std_logic_1164.all;

ENTITY FullSubtractorVHDL IS
  PORT (
    A      : IN  std_logic;
    B      : IN  std_logic;
    Cin    : IN  std_logic;
    S      : OUT std_logic;
    Cout   : OUT std_logic
  );
END FullSubtractorVHDL;

ARCHITECTURE TypeArchitecture OF FullSubtractorVHDL IS
BEGIN
  S <= (A XOR B) XOR Cin;
  Cout <= (NOT A AND B) or (NOT A AND Cin) or (B AND Cin);
END TypeArchitecture;

// VHDL entity FullAdderVHDL, as the project stores it:
LIBRARY ieee;
USE ieee.std_logic_1164.all;

ENTITY FullAdderVHDL IS
  PORT (
    A      : IN  std_logic;
    B      : IN  std_logic;
    Cin    : IN  std_logic;
    S      : OUT std_logic;
    Cout   : OUT std_logic
  );
END FullAdderVHDL;

ARCHITECTURE TypeArchitecture OF FullAdderVHDL IS
BEGIN
  S <= (A XOR B) XOR Cin;
  Cout <= (A AND B) or (A AND Cin) or (B AND Cin);
END TypeArchitecture;

// VHDL entity HalfAdderSubtractorVHDL, as the project stores it:
LIBRARY ieee;
USE ieee.std_logic_1164.all;

ENTITY HalfAdderSubtractorVHDL IS
  PORT (
    A      : IN  std_logic;
    B      : IN  std_logic;
    Cin    : IN  std_logic;
    M      : IN  std_logic;
    S      : OUT std_logic;
    Cout   : OUT std_logic
  );
END HalfAdderSubtractorVHDL;

ARCHITECTURE TypeArchitecture OF HalfAdderSubtractorVHDL IS
BEGIN
  S <= (A XOR B) XOR Cin;
  Cout <= ((M XOR A) AND B) OR ((M XOR A) AND Cin) OR (B AND Cin);
END TypeArchitecture;

// VHDL entity Subtractor4BITSVHDL, as the project stores it:
LIBRARY ieee;
USE ieee.std_logic_1164.all;

ENTITY Subtractor4BITSVHDL IS
  PORT (
    A     : IN  std_logic_vector(3 downto 0); 
    B     : IN  std_logic_vector(3 downto 0); 
    S     : OUT std_logic_vector(3 downto 0); 
    OVERF : OUT std_logic                     
  );
END Subtractor4BITSVHDL;

ARCHITECTURE TypeArchitecture OF Subtractor4BITSVHDL IS
  SIGNAL CARRY : std_logic_vector(3 downto 0);
BEGIN
  CARRY(0) <= '0';

  S(0) <= A(0) XOR B(0) XOR CARRY(0);
  CARRY(1) <= (NOT A(0) AND B(0)) OR (NOT A(0) AND CARRY(0)) OR (B(0) AND CARRY(0));

  S(1) <= A(1) XOR B(1) XOR CARRY(1);
  CARRY(2) <= (NOT A(1) AND B(1)) OR (NOT A(1) AND CARRY(1)) OR (B(1) AND CARRY(1));

  S(2) <= A(2) XOR B(2) XOR CARRY(2);
  CARRY(3) <= (NOT A(2) AND B(2)) OR (NOT A(2) AND CARRY(2)) OR (B(0) AND CARRY(2));

  S(3) <= A(3) XOR B(3) XOR CARRY(3);
  OVERF <= (NOT A(3) AND B(3)) OR (NOT A(3) AND CARRY(3)) OR (B(3) AND CARRY(3));
  
END TypeArchitecture;

// VHDL entity Adder4BITSVHDL, as the project stores it:
LIBRARY ieee;
USE ieee.std_logic_1164.all;

ENTITY Adder4BITSVHDL IS
  PORT (
    A     : IN  std_logic_vector(3 downto 0); 
    B     : IN  std_logic_vector(3 downto 0); 
    S     : OUT std_logic_vector(3 downto 0); 
    OVERF : OUT std_logic                     
  );
END Adder4BITSVHDL;

ARCHITECTURE TypeArchitecture OF Adder4BITSVHDL IS
  SIGNAL CARRY : std_logic_vector(3 downto 0);
BEGIN
  CARRY(0) <= '0';

  S(0) <= A(0) XOR B(0) XOR CARRY(0);
  CARRY(1) <= (A(0) AND B(0)) OR (A(0) AND CARRY(0)) OR (B(0) AND CARRY(0));

  S(1) <= A(1) XOR B(1) XOR CARRY(1);
  CARRY(2) <= (A(1) AND B(1)) OR (A(1) AND CARRY(1)) OR (B(1) AND CARRY(1));

  S(2) <= A(2) XOR B(2) XOR CARRY(2);
  CARRY(3) <= (A(2) AND B(2)) OR (A(2) AND CARRY(2)) OR (B(0) AND CARRY(2));

  S(3) <= A(3) XOR B(3) XOR CARRY(3);
  OVERF <= (A(3) AND B(3)) OR (A(3) AND CARRY(3)) OR (B(3) AND CARRY(3));
  
END TypeArchitecture;

// VHDL entity AdderSubtractor4BITSVHDL, as the project stores it:
LIBRARY ieee;
USE ieee.std_logic_1164.all;

ENTITY AdderSubtractor4BITSVHDL IS
  PORT (
    M	: IN	 std_logic;
    A     : IN  std_logic_vector(3 downto 0); 
    B     : IN  std_logic_vector(3 downto 0); 
    S     : OUT std_logic_vector(3 downto 0); 
    OVERF : OUT std_logic                     
  );
END AdderSubtractor4BITSVHDL;

ARCHITECTURE TypeArchitecture OF AdderSubtractor4BITSVHDL IS
  SIGNAL CARRY : std_logic_vector(3 downto 0);
BEGIN
  CARRY(0) <= '0';

  S(0) <= A(0) XOR B(0) XOR CARRY(0);
  CARRY(1) <= ((M XOR A(0)) AND B(0)) OR ((M XOR A(0)) AND CARRY(0)) OR (B(0) AND CARRY(0));

  S(1) <= A(1) XOR B(1) XOR CARRY(1);
  CARRY(2) <= ((M XOR A(1)) AND B(1)) OR ((M XOR A(1)) AND CARRY(1)) OR (B(1) AND CARRY(1));

  S(2) <= A(2) XOR B(2) XOR CARRY(2);
  CARRY(3) <= ((M XOR A(2)) AND B(2)) OR ((M XOR A(2)) AND CARRY(2)) OR (B(0) AND CARRY(2));

  S(3) <= A(3) XOR B(3) XOR CARRY(3);
  OVERF <= ((M XOR A(3)) AND B(3)) OR ((M XOR A(3)) AND CARRY(3)) OR (B(3) AND CARRY(3));
  
END TypeArchitecture;

// VHDL entity TwoComplementSubtractor4BITSVHDL, as the project stores it:
LIBRARY ieee;
USE ieee.std_logic_1164.all;

ENTITY TwoComplementSubtractor4BITSVHDL IS
  PORT (
    A     : IN  std_logic_vector(3 downto 0); 
    B     : IN  std_logic_vector(3 downto 0); 
    S     : OUT std_logic_vector(3 downto 0); 
    OVERF : OUT std_logic                     
  );
END TwoComplementSubtractor4BITSVHDL;

ARCHITECTURE TypeArchitecture OF TwoComplementSubtractor4BITSVHDL IS
  SIGNAL CARRY : std_logic_vector(3 downto 0);
BEGIN
  CARRY(0) <= '1';
  
  S(0) <= A(0) XOR NOT B(0) XOR CARRY(0);
  CARRY(1) <= (A(0) AND NOT B(0)) OR (A(0) AND CARRY(0)) OR (NOT B(0) AND CARRY(0));

  S(1) <= A(1) XOR NOT B(1) XOR CARRY(1);
  CARRY(2) <= (A(1) AND NOT B(1)) OR (A(1) AND CARRY(1)) OR (NOT B(1) AND CARRY(1));

  S(2) <= A(2) XOR NOT B(2) XOR CARRY(2);
  CARRY(3) <= (A(2) AND NOT B(2)) OR (A(2) AND CARRY(2)) OR (NOT B(0) AND CARRY(2));

  S(3) <= A(3) XOR NOT B(3) XOR CARRY(3);
  OVERF <= (A(3) AND NOT B(3)) OR (A(3) AND CARRY(3)) OR (NOT B(3) AND CARRY(3));
  
END TypeArchitecture;
