// Logisim project atividade1.circ as structural Verilog
module Presentation (
  input  [3:0] A,
  input  [3:0] B,
  input  M,
  output [4:0] S
);

  wire [6:0] decodificador_hex_1_out_2, decodificador_hex_2_out_2, decodificador_hex_3_out_2;

  decodificador_hex decodificador_hex_1 (.in_1(A), .out_2(decodificador_hex_1_out_2));
  _7_Segment_Display u_7_segment_display_1 (
    .g(decodificador_hex_1_out_2[6]), .f(decodificador_hex_1_out_2[5]), .a(decodificador_hex_1_out_2[0]),
    .b(decodificador_hex_1_out_2[1]), .e(decodificador_hex_1_out_2[4]), .d(decodificador_hex_1_out_2[3]),
    .c(decodificador_hex_1_out_2[2]));  // open: dp
  decodificador_hex decodificador_hex_2 (.in_1(B), .out_2(decodificador_hex_2_out_2));
  Adder4bits adder4bits_1 ();  // open: A, B, S
  Subtractor4bits subtractor4bits_1 ();  // open: A, B, S
  TwoComplementSubtractor4bits twocomplementsubtractor4bits_1 ();  // open: A, B, S
  AdderSubtractor4bits addersubtractor4bits_1 ();  // open: A, B, M, S
  _7_Segment_Display u_7_segment_display_2 (
    .g(decodificador_hex_2_out_2[6]), .f(decodificador_hex_2_out_2[5]), .a(decodificador_hex_2_out_2[0]),
    .b(decodificador_hex_2_out_2[1]), .e(decodificador_hex_2_out_2[4]), .d(decodificador_hex_2_out_2[3]),
    .c(decodificador_hex_2_out_2[2]));  // open: dp
  decodificador_hex decodificador_hex_3 (.in_1(S[3:0]), .out_2(decodificador_hex_3_out_2));
  Adder4bits_vhdl adder4bits_vhdl_1 ();  // open: A, B, S
  Sutractor4bits_vhdl sutractor4bits_vhdl_1 ();  // open: A, B, S
  TwoComplementSubtractor_vhdl twocomplementsubtractor_vhdl_1 ();  // open: A, B, S
  AdderSubtractor4bits_vhdl addersubtractor4bits_vhdl_1 ();  // open: A, B, M, S
  _7_Segment_Display u_7_segment_display_3 (
    .g(decodificador_hex_3_out_2[6]), .f(decodificador_hex_3_out_2[5]), .a(decodificador_hex_3_out_2[0]),
    .b(decodificador_hex_3_out_2[1]), .e(decodificador_hex_3_out_2[4]), .d(decodificador_hex_3_out_2[3]),
    .c(decodificador_hex_3_out_2[2]));  // open: dp
endmodule

module main (
);

  TwoComplementSubtractor4bits twocomplementsubtractor4bits_1 ();  // open: A, B, S
  HalfSubtractor_vhdl halfsubtractor_vhdl_1 ();  // open: A, B, S, Cout
  TwoComplementSubtractor4bits_nand twocomplementsubtractor4bits_nand_1 ();  // open: A3, A2, A1, A0, B3, B2, B1, B0, OVERF, S3, S2, S1, S0
  Adder4bits adder4bits_1 ();  // open: A, B, S
  HalfAdder_vhdl halfadder_vhdl_1 ();  // open: A, B, S, Cout
  Adder4bits_nand adder4bits_nand_1 ();  // open: A3, A2, A1, A0, B3, B2, B1, B0, OVERF, S3, S2, S1, S0
  Subtractor4bits subtractor4bits_1 ();  // open: A, B, S
  FullSubtractor_vhdl fullsubtractor_vhdl_1 ();  // open: A, B, Cin, S, Cout
  Subtractor4bits_nand subtractor4bits_nand_1 ();  // open: A3, A2, A1, A0, B3, B2, B1, B0, OVERF, S3, S2, S1, S0
  AdderSubtractor4bits addersubtractor4bits_1 ();  // open: A, B, M, S
  FullAdder_vhdl fulladder_vhdl_1 ();  // open: A, B, Cin, S, Cout
  AdderSubtractor4bits_nand addersubtractor4bits_nand_1 ();  // open: A3, A2, A1, A0, B3, B2, B1, B0, M, OVERF, S3, S2, S1, S0
  FullAdder fulladder_1 ();  // open: A, B, Cin, S, Cout
  HalfAdderSubtractor halfaddersubtractor_1 ();  // open: M, A, B, Cin, S, Cout
  xor_nand xor_nand_1 ();  // open: A, B, S
  HalfAdderSubtractor_nand halfaddersubtractor_nand_1 ();  // open: M, A, B, Cin, S, Cout
  or_nand or_nand_1 ();  // open: A, B, S
  FullAdder_nand fulladder_nand_1 ();  // open: A, B, Cin, S, Cout
  and_nand and_nand_1 ();  // open: A, B, S
  FullSubtractor_nand fullsubtractor_nand_1 ();  // open: A, B, Cin, S, Cout
  HalfAdder_nand halfadder_nand_1 ();  // open: A, B, S, Cout
  not_nand not_nand_1 ();  // open: A, S
  HalfSubtractor_nand halfsubtractor_nand_1 ();  // open: A, B, S, Cout
  decodificador_hex decodificador_hex_1 ();  // open: in_1, out_2
  FullSubtractor fullsubtractor_1 ();  // open: A, B, Cin, S, Cout
  decodificador_decimal decodificador_decimal_1 ();  // open: in_1, out_2
  HalfAdder halfadder_1 ();  // open: A, B, S, Cout
  HalfSubtractor halfsubtractor_1 ();  // open: A, B, S, Cout
  HalfAdderSubtractor_vhdl halfaddersubtractor_vhdl_1 ();  // open: A, B, Cin, M, S, Cout
  Sutractor4bits_vhdl sutractor4bits_vhdl_1 ();  // open: A, B, S
  Adder4bits_vhdl adder4bits_vhdl_1 ();  // open: A, B, S
  AdderSubtractor4bits_vhdl addersubtractor4bits_vhdl_1 ();  // open: A, B, M, S
  TwoComplementSubtractor_vhdl twocomplementsubtractor_vhdl_1 ();  // open: A, B, S
endmodule

module TwoComplementSubtractor4bits (
  input  [3:0] A,
  input  [3:0] B,
  output [4:0] S
);

  wire fulladder_2_cout, fulladder_3_cout, fulladder_4_cout, not_1_out, not_2_out, not_3_out, not_4_out;

  FullAdder fulladder_1 (.A(A[3]), .B(not_1_out), .Cin(fulladder_2_cout), .S(S[3]), .Cout(S[4]));
  not not_1 (not_1_out, B[3]);
  FullAdder fulladder_2 (.A(A[2]), .B(not_3_out), .Cin(fulladder_3_cout), .S(S[2]), .Cout(fulladder_2_cout));
  not not_2 (not_2_out, B[1]);
  not not_3 (not_3_out, B[2]);
  FullAdder fulladder_3 (.A(A[1]), .B(not_2_out), .Cin(fulladder_4_cout), .S(S[1]), .Cout(fulladder_3_cout));
  not not_4 (not_4_out, B[0]);
  FullAdder fulladder_4 (.A(A[0]), .B(not_4_out), .Cin(1'b1), .S(S[0]), .Cout(fulladder_4_cout));
endmodule

module Adder4bits (
  input  [3:0] A,
  input  [3:0] B,
  output [4:0] S
);

  wire fulladder_2_cout, fulladder_3_cout, fulladder_4_cout;

  FullAdder fulladder_1 (.A(A[3]), .B(B[3]), .Cin(fulladder_2_cout), .S(S[3]), .Cout(S[4]));
  FullAdder fulladder_2 (.A(A[2]), .B(B[2]), .Cin(fulladder_3_cout), .S(S[2]), .Cout(fulladder_2_cout));
  FullAdder fulladder_3 (.A(A[1]), .B(B[1]), .Cin(fulladder_4_cout), .S(S[1]), .Cout(fulladder_3_cout));
  FullAdder fulladder_4 (.A(A[0]), .B(B[0]), .Cin(1'b0), .S(S[0]), .Cout(fulladder_4_cout));
endmodule

module Subtractor4bits (
  input  [3:0] A,
  input  [3:0] B,
  output [4:0] S
);

  wire fullsubtractor_2_cout, fullsubtractor_3_cout, fullsubtractor_4_cout;

  FullSubtractor fullsubtractor_1 (.A(A[3]), .B(B[3]), .Cin(fullsubtractor_2_cout), .S(S[3]), .Cout(S[4]));
  FullSubtractor fullsubtractor_2 (
    .A(A[2]), .B(B[2]), .Cin(fullsubtractor_3_cout), .S(S[2]), .Cout(fullsubtractor_2_cout));
  FullSubtractor fullsubtractor_3 (
    .A(A[1]), .B(B[1]), .Cin(fullsubtractor_4_cout), .S(S[1]), .Cout(fullsubtractor_3_cout));
  FullSubtractor fullsubtractor_4 (.A(A[0]), .B(B[0]), .Cin(1'b0), .S(S[0]), .Cout(fullsubtractor_4_cout));
endmodule

module AdderSubtractor4bits (
  input  [3:0] A,
  input  [3:0] B,
  input  M,
  output [4:0] S
);

  wire halfaddersubtractor_2_cout, halfaddersubtractor_3_cout, halfaddersubtractor_4_cout;

  HalfAdderSubtractor halfaddersubtractor_1 (
    .M(M), .A(A[3]), .B(B[3]), .Cin(halfaddersubtractor_2_cout), .S(S[3]), .Cout(S[4]));
  HalfAdderSubtractor halfaddersubtractor_2 (
    .M(M), .A(A[2]), .B(B[2]), .Cin(halfaddersubtractor_3_cout), .S(S[2]), .Cout(halfaddersubtractor_2_cout));
  HalfAdderSubtractor halfaddersubtractor_3 (
    .M(M), .A(A[1]), .B(B[1]), .Cin(halfaddersubtractor_4_cout), .S(S[1]), .Cout(halfaddersubtractor_3_cout));
  HalfAdderSubtractor halfaddersubtractor_4 (
    .M(M), .A(A[0]), .B(B[0]), .Cin(1'b0), .S(S[0]), .Cout(halfaddersubtractor_4_cout));
endmodule

module HalfAdderSubtractor (
  input  M,
  input  A,
  input  B,
  input  Cin,
  output S,
  output Cout
);

  wire and_1_out, and_2_out, and_3_out, xor_1_out, xor_2_out;

  xor xor_1 (xor_1_out, M, A);
  xor xor_2 (xor_2_out, A, B);
  and and_1 (and_1_out, xor_1_out, B);
  and and_2 (and_2_out, xor_1_out, Cin);
  and and_3 (and_3_out, B, Cin);
  xor xor_3 (S, xor_2_out, Cin);
  or or_1 (Cout, and_1_out, and_2_out, and_3_out);

  // Notes on the sheet:
  //   S = (A ⊕ B) ⊕ (Cin)
  //   Cout = ((M ⊕ A) . B) + ((M ⊕ A) . Cin) + (B . Cin)
endmodule

module FullAdder (
  input  A,
  input  B,
  input  Cin,
  output S,
  output Cout
);

  wire and_1_out, and_2_out, and_3_out, xor_1_out;

  xor xor_1 (xor_1_out, A, B);
  and and_1 (and_1_out, A, B);
  and and_2 (and_2_out, A, Cin);
  and and_3 (and_3_out, B, Cin);
  xor xor_2 (S, xor_1_out, Cin);
  or or_1 (Cout, and_1_out, and_2_out, and_3_out);

  // Notes on the sheet:
  //   S = (A ⊕ B) ⊕ Cin
  //   Cout = (A . B) + (A . Cin) + (B . Cin)
endmodule

module FullSubtractor (
  input  A,
  input  B,
  input  Cin,
  output S,
  output Cout
);

  wire and_1_out, and_2_out, and_3_out, not_1_out, xor_1_out;

  not not_1 (not_1_out, A);
  xor xor_1 (xor_1_out, A, B);
  and and_1 (and_1_out, not_1_out, B);
  and and_2 (and_2_out, not_1_out, Cin);
  and and_3 (and_3_out, B, Cin);
  xor xor_2 (S, xor_1_out, Cin);
  or or_1 (Cout, and_1_out, and_2_out, and_3_out);

  // Notes on the sheet:
  //   S = (A ⊕ B) ⊕ Cin
  //   Cout = (A' . B) + (A' . Cin) + (B . Cin)
endmodule

module HalfAdder (
  input  A,
  input  B,
  output S,
  output Cout
);

  xor xor_1 (S, A, B);
  and and_1 (Cout, A, B);

  // Notes on the sheet:
  //   S = A ⊕ B
  //   Cout = (A . B)
endmodule

module HalfSubtractor (
  input  A,
  input  B,
  output S,
  output Cout
);

  wire not_1_out;

  not not_1 (not_1_out, A);
  xor xor_1 (S, A, B);
  and and_1 (Cout, not_1_out, B);

  // Notes on the sheet:
  //   S = (A ⊕ B)
  //   Cout = (A' . B)
endmodule

module decodificador_decimal (
  input  [3:0] in_1,
  output [6:0] out_2
);

  wire and_1_out, and_2_out, and_3_out, and_4_out, and_5_out, and_6_out, and_7_out, and_8_out, and_9_out,
       and_10_out, and_11_out, and_12_out, and_13_out, and_14_out, and_15_out, and_16_out, and_17_out,
       and_18_out, and_19_out, and_20_out, and_21_out, and_22_out, and_23_out, and_24_out, and_25_out,
       and_26_out, not_1_out, not_2_out, not_3_out, not_4_out;

  not not_1 (not_1_out, in_1[3]);
  not not_2 (not_2_out, in_1[2]);
  not not_3 (not_3_out, in_1[1]);
  not not_4 (not_4_out, in_1[0]);
  and and_1 (and_1_out, not_1_out, in_1[1]);
  and and_2 (and_2_out, not_1_out, in_1[2], in_1[0]);
  and and_3 (and_3_out, in_1[3], not_2_out, not_3_out);
  and and_4 (and_4_out, not_1_out, not_2_out, not_4_out);
  and and_5 (and_5_out, not_1_out, not_2_out);
  and and_6 (and_6_out, not_1_out, not_3_out, not_4_out);
  and and_7 (and_7_out, not_1_out, in_1[1], in_1[0]);
  and and_8 (and_8_out, not_2_out, not_3_out);
  and and_9 (and_9_out, not_1_out, in_1[0]);
  and and_10 (and_10_out, not_1_out, in_1[2]);
  and and_11 (and_11_out, not_2_out, not_3_out);
  and and_12 (and_12_out, not_1_out, not_2_out, in_1[1]);
  and and_13 (and_13_out, not_1_out, in_1[2], not_3_out, in_1[0]);
  and and_14 (and_14_out, not_1_out, in_1[1], not_4_out);
  and and_15 (and_15_out, in_1[3], not_2_out, not_3_out);
  and and_16 (and_16_out, not_1_out, not_2_out, not_4_out);
  and and_17 (and_17_out, not_1_out, in_1[1], not_4_out);
  and and_18 (and_18_out, not_2_out, not_3_out, not_4_out);
  and and_19 (and_19_out, not_1_out, in_1[2], not_3_out);
  and and_20 (and_20_out, not_1_out, in_1[2], not_4_out);
  and and_21 (and_21_out, in_1[3], not_2_out, not_3_out);
  and and_22 (and_22_out, not_1_out, not_3_out, not_4_out);
  and and_23 (and_23_out, not_1_out, not_2_out, in_1[1]);
  and and_24 (and_24_out, not_1_out, in_1[2], not_3_out);
  and and_25 (and_25_out, in_1[3], not_2_out, not_3_out);
  and and_26 (and_26_out, not_1_out, in_1[1], not_4_out);
  or or_1 (out_2[0], and_1_out, and_2_out, and_3_out, and_4_out);
  or or_2 (out_2[1], and_5_out, and_6_out, and_7_out, and_8_out);
  or or_3 (out_2[2], and_9_out, and_10_out, and_11_out);
  or or_4 (out_2[3], and_12_out, and_13_out, and_14_out, and_15_out, and_16_out);
  or or_5 (out_2[4], and_17_out, and_18_out);
  or or_6 (out_2[5], and_19_out, and_20_out, and_21_out, and_22_out);
  or or_7 (out_2[6], and_23_out, and_24_out, and_25_out, and_26_out);
endmodule

module decodificador_hex (
  input  [3:0] in_1,
  output [6:0] out_2
);

  wire and_1_out, and_2_out, and_3_out, and_4_out, and_5_out, and_6_out, and_7_out, and_8_out, and_9_out,
       and_10_out, and_11_out, and_12_out, and_13_out, and_14_out, and_15_out, and_16_out, and_17_out,
       and_18_out, and_19_out, and_20_out, and_21_out, and_22_out, and_23_out, and_24_out, and_25_out,
       and_26_out, and_27_out, and_28_out, and_29_out, and_30_out, and_31_out, and_32_out, and_33_out,
       and_34_out, and_35_out, not_1_out, not_2_out, not_3_out, not_4_out;

  not not_1 (not_1_out, in_1[3]);
  not not_2 (not_2_out, in_1[2]);
  not not_3 (not_3_out, in_1[1]);
  not not_4 (not_4_out, in_1[0]);
  and and_1 (and_1_out, not_2_out, not_4_out);
  and and_2 (and_2_out, not_1_out, in_1[1]);
  and and_3 (and_3_out, not_1_out, in_1[2], in_1[0]);
  and and_4 (and_4_out, in_1[3], not_2_out, not_3_out);
  and and_5 (and_5_out, in_1[3], not_4_out);
  and and_6 (and_6_out, in_1[2], in_1[1]);
  and and_7 (and_7_out, not_1_out, not_3_out, not_4_out);
  and and_8 (and_8_out, not_1_out, in_1[1], in_1[0]);
  and and_9 (and_9_out, not_2_out, not_4_out);
  and and_10 (and_10_out, in_1[3], not_3_out, in_1[0]);
  and and_11 (and_11_out, not_1_out, not_2_out);
  and and_12 (and_12_out, not_1_out, in_1[2]);
  and and_13 (and_13_out, in_1[3], not_2_out);
  and and_14 (and_14_out, not_3_out, in_1[0]);
  and and_15 (and_15_out, not_2_out, not_3_out);
  and and_16 (and_16_out, not_2_out, in_1[0]);
  and and_17 (and_17_out, in_1[2], not_3_out, in_1[0]);
  and and_18 (and_18_out, not_1_out, not_2_out, not_4_out);
  and and_19 (and_19_out, not_2_out, in_1[1], in_1[0]);
  and and_20 (and_20_out, in_1[3], not_3_out);
  and and_21 (and_21_out, in_1[2], in_1[1], not_4_out);
  and and_22 (and_22_out, not_2_out, not_4_out);
  and and_23 (and_23_out, in_1[1], not_4_out);
  and and_24 (and_24_out, in_1[3], in_1[1]);
  and and_25 (and_25_out, in_1[3], in_1[2]);
  and and_26 (and_26_out, not_3_out, not_4_out);
  and and_27 (and_27_out, not_1_out, in_1[2], not_3_out);
  and and_28 (and_28_out, in_1[2], not_4_out);
  and and_29 (and_29_out, in_1[3], not_2_out);
  and and_30 (and_30_out, in_1[3], in_1[1]);
  and and_31 (and_31_out, not_2_out, in_1[1]);
  and and_32 (and_32_out, in_1[3], not_2_out);
  and and_33 (and_33_out, not_1_out, in_1[2], not_3_out);
  and and_34 (and_34_out, in_1[1], not_4_out);
  and and_35 (and_35_out, in_1[3], in_1[0]);
  or or_1 (out_2[0], and_1_out, and_2_out, and_3_out, and_4_out, and_5_out, and_6_out);
  or or_2 (out_2[1], and_7_out, and_8_out, and_9_out, and_10_out, and_11_out);
  or or_3 (out_2[2], and_12_out, and_13_out, and_14_out, and_15_out, and_16_out);
  or or_4 (out_2[3], and_17_out, and_18_out, and_19_out, and_20_out, and_21_out);
  or or_5 (out_2[4], and_22_out, and_23_out, and_24_out, and_25_out);
  or or_6 (out_2[5], and_26_out, and_27_out, and_28_out, and_29_out, and_30_out);
  or or_7 (out_2[6], and_31_out, and_32_out, and_33_out, and_34_out, and_35_out);
endmodule

module TwoComplementSubtractor4bits_nand (
  input  A3,
  input  A2,
  input  A1,
  input  A0,
  input  B3,
  input  B2,
  input  B1,
  input  B0,
  output OVERF,
  output S3,
  output S2,
  output S1,
  output S0
);

  wire fulladder_nand_2_cout, fulladder_nand_3_cout, fulladder_nand_4_cout, not_1_out, not_2_out, not_3_out,
       not_4_out;

  FullAdder_nand fulladder_nand_1 (.A(A3), .B(not_1_out), .Cin(fulladder_nand_2_cout), .S(S3), .Cout(OVERF));
  FullAdder_nand fulladder_nand_2 (
    .A(A2), .B(not_2_out), .Cin(fulladder_nand_3_cout), .S(S2), .Cout(fulladder_nand_2_cout));
  not not_1 (not_1_out, B3);
  not not_2 (not_2_out, B2);
  not not_3 (not_3_out, B1);
  FullAdder_nand fulladder_nand_3 (
    .A(A1), .B(not_3_out), .Cin(fulladder_nand_4_cout), .S(S1), .Cout(fulladder_nand_3_cout));
  not not_4 (not_4_out, B0);
  FullAdder_nand fulladder_nand_4 (.A(A0), .B(not_4_out), .Cin(1'b1), .S(S0), .Cout(fulladder_nand_4_cout));
endmodule

module Adder4bits_nand (
  input  A3,
  input  A2,
  input  A1,
  input  A0,
  input  B3,
  input  B2,
  input  B1,
  input  B0,
  output OVERF,
  output S3,
  output S2,
  output S1,
  output S0
);

  wire fulladder_nand_2_cout, fulladder_nand_3_cout, fulladder_nand_4_cout;

  FullAdder_nand fulladder_nand_1 (.A(A3), .B(B3), .Cin(fulladder_nand_2_cout), .S(S3), .Cout(OVERF));
  FullAdder_nand fulladder_nand_2 (.A(A2), .B(B2), .Cin(fulladder_nand_3_cout), .S(S2), .Cout(fulladder_nand_2_cout));
  FullAdder_nand fulladder_nand_3 (.A(A1), .B(B1), .Cin(fulladder_nand_4_cout), .S(S1), .Cout(fulladder_nand_3_cout));
  FullAdder_nand fulladder_nand_4 (.A(A0), .B(B0), .Cin(1'b0), .S(S0), .Cout(fulladder_nand_4_cout));
endmodule

module Subtractor4bits_nand (
  input  A3,
  input  A2,
  input  A1,
  input  A0,
  input  B3,
  input  B2,
  input  B1,
  input  B0,
  output OVERF,
  output S3,
  output S2,
  output S1,
  output S0
);

  wire fullsubtractor_nand_2_cout, fullsubtractor_nand_3_cout, fullsubtractor_nand_4_cout;

  FullSubtractor_nand fullsubtractor_nand_1 (.A(A3), .B(B3), .Cin(fullsubtractor_nand_2_cout), .S(S3), .Cout(OVERF));
  FullSubtractor_nand fullsubtractor_nand_2 (
    .A(A2), .B(B2), .Cin(fullsubtractor_nand_3_cout), .S(S2), .Cout(fullsubtractor_nand_2_cout));
  FullSubtractor_nand fullsubtractor_nand_3 (
    .A(A1), .B(B1), .Cin(fullsubtractor_nand_4_cout), .S(S1), .Cout(fullsubtractor_nand_3_cout));
  FullSubtractor_nand fullsubtractor_nand_4 (.A(A0), .B(B0), .Cin(1'b0), .S(S0), .Cout(fullsubtractor_nand_4_cout));
endmodule

module AdderSubtractor4bits_nand (
  input  A3,
  input  A2,
  input  A1,
  input  A0,
  input  B3,
  input  B2,
  input  B1,
  input  B0,
  input  M,
  output OVERF,
  output S3,
  output S2,
  output S1,
  output S0
);

  wire halfaddersubtractor_nand_2_cout, halfaddersubtractor_nand_3_cout, halfaddersubtractor_nand_4_cout;

  HalfAdderSubtractor_nand halfaddersubtractor_nand_1 (
    .M(M), .A(A3), .B(B3), .Cin(halfaddersubtractor_nand_2_cout), .S(S3), .Cout(OVERF));
  HalfAdderSubtractor_nand halfaddersubtractor_nand_2 (
    .M(M), .A(A2), .B(B2), .Cin(halfaddersubtractor_nand_3_cout), .S(S2),
    .Cout(halfaddersubtractor_nand_2_cout));
  HalfAdderSubtractor_nand halfaddersubtractor_nand_3 (
    .M(M), .A(A1), .B(B1), .Cin(halfaddersubtractor_nand_4_cout), .S(S1),
    .Cout(halfaddersubtractor_nand_3_cout));
  HalfAdderSubtractor_nand halfaddersubtractor_nand_4 (
    .M(M), .A(A0), .B(B0), .Cin(1'b0), .S(S0), .Cout(halfaddersubtractor_nand_4_cout));
endmodule

module HalfAdderSubtractor_nand (
  input  M,
  input  A,
  input  B,
  input  Cin,
  output S,
  output Cout
);

  wire and_nand_1_s, and_nand_2_s, and_nand_3_s, or_nand_1_s, xor_nand_1_s, xor_nand_2_s;

  xor_nand xor_nand_1 (.A(A), .B(M), .S(xor_nand_1_s));
  xor_nand xor_nand_2 (.A(A), .B(B), .S(xor_nand_2_s));
  and_nand and_nand_1 (.A(xor_nand_1_s), .B(B), .S(and_nand_1_s));
  and_nand and_nand_2 (.A(xor_nand_1_s), .B(Cin), .S(and_nand_2_s));
  and_nand and_nand_3 (.A(B), .B(Cin), .S(and_nand_3_s));
  xor_nand xor_nand_3 (.A(xor_nand_2_s), .B(Cin), .S(S));
  or_nand or_nand_1 (.A(and_nand_1_s), .B(and_nand_2_s), .S(or_nand_1_s));
  or_nand or_nand_2 (.A(or_nand_1_s), .B(and_nand_3_s), .S(Cout));

  // Notes on the sheet:
  //   S = (A ⊕ B) ⊕ (Cin)
  //   Cout = ((M ⊕ A) . B) + ((M ⊕ A) . Cin) + (B . Cin)
endmodule

module FullAdder_nand (
  input  A,
  input  B,
  input  Cin,
  output S,
  output Cout
);

  wire and_nand_1_s, and_nand_2_s, and_nand_3_s, or_nand_1_s, xor_nand_1_s;

  xor_nand xor_nand_1 (.A(A), .B(B), .S(xor_nand_1_s));
  xor_nand xor_nand_2 (.A(xor_nand_1_s), .B(Cin), .S(S));
  and_nand and_nand_1 (.A(A), .B(B), .S(and_nand_1_s));
  and_nand and_nand_2 (.A(A), .B(Cin), .S(and_nand_2_s));
  and_nand and_nand_3 (.A(B), .B(Cin), .S(and_nand_3_s));
  or_nand or_nand_1 (.A(and_nand_1_s), .B(and_nand_2_s), .S(or_nand_1_s));
  or_nand or_nand_2 (.A(or_nand_1_s), .B(and_nand_3_s), .S(Cout));

  // Notes on the sheet:
  //   S = (A ⊕ B) ⊕ Cin
  //   Cout = (A . B) + (A . Cin) + (B . Cin)
endmodule

module FullSubtractor_nand (
  input  A,
  input  B,
  input  Cin,
  output S,
  output Cout
);

  wire and_nand_1_s, and_nand_2_s, and_nand_3_s, not_nand_1_s, or_nand_1_s, xor_nand_1_s;

  not_nand not_nand_1 (.A(A), .S(not_nand_1_s));
  xor_nand xor_nand_1 (.A(A), .B(B), .S(xor_nand_1_s));
  xor_nand xor_nand_2 (.A(xor_nand_1_s), .B(Cin), .S(S));
  and_nand and_nand_1 (.A(not_nand_1_s), .B(B), .S(and_nand_1_s));
  and_nand and_nand_2 (.A(not_nand_1_s), .B(Cin), .S(and_nand_2_s));
  and_nand and_nand_3 (.A(B), .B(Cin), .S(and_nand_3_s));
  or_nand or_nand_1 (.A(and_nand_1_s), .B(and_nand_2_s), .S(or_nand_1_s));
  or_nand or_nand_2 (.A(or_nand_1_s), .B(and_nand_3_s), .S(Cout));

  // Notes on the sheet:
  //   S = (A ⊕ B) ⊕ Cin
  //   Cout = (A' . B) + (A' . Cin) + (B . Cin)
endmodule

module HalfAdder_nand (
  input  A,
  input  B,
  output S,
  output Cout
);

  xor_nand xor_nand_1 (.A(A), .B(B), .S(S));
  and_nand and_nand_1 (.A(A), .B(B), .S(Cout));

  // Notes on the sheet:
  //   S = A ⊕ B
  //   Cout = (A . B)
endmodule

module HalfSubtractor_nand (
  input  A,
  input  B,
  output S,
  output Cout
);

  wire not_nand_1_s;

  xor_nand xor_nand_1 (.A(A), .B(B), .S(S));
  not_nand not_nand_1 (.A(A), .S(not_nand_1_s));
  and_nand and_nand_1 (.A(not_nand_1_s), .B(B), .S(Cout));

  // Notes on the sheet:
  //   S = (A ⊕ B)
  //   Cout = (A' . B)
endmodule

module xor_nand (
  input  A,
  input  B,
  output S
);

  wire and_nand_1_s, and_nand_2_s, not_nand_1_s, not_nand_2_s;

  not_nand not_nand_1 (.A(A), .S(not_nand_1_s));
  not_nand not_nand_2 (.A(B), .S(not_nand_2_s));
  and_nand and_nand_1 (.A(not_nand_1_s), .B(B), .S(and_nand_1_s));
  and_nand and_nand_2 (.A(A), .B(not_nand_2_s), .S(and_nand_2_s));
  or_nand or_nand_1 (.A(and_nand_1_s), .B(and_nand_2_s), .S(S));
endmodule

module or_nand (
  input  A,
  input  B,
  output S
);

  wire not_nand_1_s, not_nand_2_s;

  not_nand not_nand_1 (.A(A), .S(not_nand_1_s));
  not_nand not_nand_2 (.A(B), .S(not_nand_2_s));
  nand nand_1 (S, not_nand_1_s, not_nand_2_s);
endmodule

module and_nand (
  input  A,
  input  B,
  output S
);

  wire nand_1_out;

  nand nand_1 (nand_1_out, A, B);
  not_nand not_nand_1 (.A(nand_1_out), .S(S));
endmodule

module not_nand (
  input  A,
  output S
);

  nand nand_1 (S, A, A);
endmodule

// VHDL entity HalfSubtractor_vhdl, as the project stores it:
LIBRARY ieee;
USE ieee.std_logic_1164.all;

ENTITY HalfSubtractor_vhdl IS
  PORT (
    A      : IN  std_logic;
    B      : IN  std_logic;
    S      : OUT std_logic;
    Cout   : OUT std_logic
  );
END HalfSubtractor_vhdl;

ARCHITECTURE TypeArchitecture OF HalfSubtractor_vhdl IS
BEGIN
  S <= A XOR B;
  Cout <= NOT A AND B;
END TypeArchitecture;

// VHDL entity HalfAdder_vhdl, as the project stores it:
LIBRARY ieee;
USE ieee.std_logic_1164.all;

ENTITY HalfAdder_vhdl IS
  PORT (
    A      : IN  std_logic;
    B      : IN  std_logic;
    S      : OUT std_logic;
    Cout   : OUT std_logic
  );
END HalfAdder_vhdl;

ARCHITECTURE TypeArchitecture OF HalfAdder_vhdl IS
BEGIN
  S <= A XOR B;
  Cout <= A AND B;
END TypeArchitecture;

// VHDL entity FullSubtractor_vhdl, as the project stores it:
LIBRARY ieee;
USE ieee.std_logic_1164.all;

ENTITY FullSubtractor_vhdl IS
  PORT (
    A      : IN  std_logic;
    B      : IN  std_logic;
    Cin    : IN  std_logic;
    S      : OUT std_logic;
    Cout   : OUT std_logic
  );
END FullSubtractor_vhdl;

ARCHITECTURE TypeArchitecture OF FullSubtractor_vhdl IS
BEGIN
  S <= (A XOR B) XOR Cin;
  Cout <= (NOT A AND B) or (NOT A AND Cin) or (B AND Cin);
END TypeArchitecture;

// VHDL entity FullAdder_vhdl, as the project stores it:
LIBRARY ieee;
USE ieee.std_logic_1164.all;

ENTITY FullAdder_vhdl IS
  PORT (
    A      : IN  std_logic;
    B      : IN  std_logic;
    Cin    : IN  std_logic;
    S      : OUT std_logic;
    Cout   : OUT std_logic
  );
END FullAdder_vhdl;

ARCHITECTURE TypeArchitecture OF FullAdder_vhdl IS
BEGIN
  S <= (A XOR B) XOR Cin;
  Cout <= (A AND B) or (A AND Cin) or (B AND Cin);
END TypeArchitecture;

// VHDL entity HalfAdderSubtractor_vhdl, as the project stores it:
LIBRARY ieee;
USE ieee.std_logic_1164.all;

ENTITY HalfAdderSubtractor_vhdl IS
  PORT (
    A      : IN  std_logic;
    B      : IN  std_logic;
    Cin    : IN  std_logic;
    M      : IN  std_logic;
    S      : OUT std_logic;
    Cout   : OUT std_logic
  );
END HalfAdderSubtractor_vhdl;

ARCHITECTURE TypeArchitecture OF HalfAdderSubtractor_vhdl IS
BEGIN
  S <= (A XOR B) XOR Cin;
  Cout <= ((M XOR A) AND B) OR ((M XOR A) AND Cin) OR (B AND Cin);
END TypeArchitecture;

// VHDL entity Sutractor4bits_vhdl, as the project stores it:
LIBRARY ieee;
USE ieee.std_logic_1164.all;

ENTITY Sutractor4bits_vhdl IS
  PORT (
    A     : IN  std_logic_vector(3 downto 0); 
    B     : IN  std_logic_vector(3 downto 0); 
    S     : OUT std_logic_vector(4 downto 0)                    
  );
END Sutractor4bits_vhdl;

ARCHITECTURE TypeArchitecture OF Sutractor4bits_vhdl IS
  SIGNAL CARRY : std_logic_vector(3 downto 0);
BEGIN
  CARRY(0) <= '0';

  S(0) <= A(0) XOR B(0) XOR CARRY(0);
  CARRY(1) <= (NOT A(0) AND B(0)) OR (NOT A(0) AND CARRY(0)) OR (B(0) AND CARRY(0));

  S(1) <= A(1) XOR B(1) XOR CARRY(1);
  CARRY(2) <= (NOT A(1) AND B(1)) OR (NOT A(1) AND CARRY(1)) OR (B(1) AND CARRY(1));

  S(2) <= A(2) XOR B(2) XOR CARRY(2);
  CARRY(3) <= (NOT A(2) AND B(2)) OR (NOT A(2) AND CARRY(2)) OR (B(0) AND CARRY(2));

  S(3) <= A(3) XOR B(3) XOR CARRY(3);
  S(4) <= (NOT A(3) AND B(3)) OR (NOT A(3) AND CARRY(3)) OR (B(3) AND CARRY(3));
  
END TypeArchitecture;

// VHDL entity Adder4bits_vhdl, as the project stores it:
LIBRARY ieee;
USE ieee.std_logic_1164.all;

ENTITY Adder4bits_vhdl IS
  PORT (
    A     : IN  std_logic_vector(3 downto 0); 
    B     : IN  std_logic_vector(3 downto 0); 
    S     : OUT std_logic_vector(4 downto 0)                  
  );
END Adder4bits_vhdl;

ARCHITECTURE TypeArchitecture OF Adder4bits_vhdl IS
  SIGNAL CARRY : std_logic_vector(3 downto 0);
BEGIN
  CARRY(0) <= '0';

  S(0) <= A(0) XOR B(0) XOR CARRY(0);
  CARRY(1) <= (A(0) AND B(0)) OR (A(0) AND CARRY(0)) OR (B(0) AND CARRY(0));

  S(1) <= A(1) XOR B(1) XOR CARRY(1);
  CARRY(2) <= (A(1) AND B(1)) OR (A(1) AND CARRY(1)) OR (B(1) AND CARRY(1));

  S(2) <= A(2) XOR B(2) XOR CARRY(2);
  CARRY(3) <= (A(2) AND B(2)) OR (A(2) AND CARRY(2)) OR (B(0) AND CARRY(2));

  S(3) <= A(3) XOR B(3) XOR CARRY(3);
  S(4) <= (A(3) AND B(3)) OR (A(3) AND CARRY(3)) OR (B(3) AND CARRY(3));
  
END TypeArchitecture;

// VHDL entity AdderSubtractor4bits_vhdl, as the project stores it:
LIBRARY ieee;
USE ieee.std_logic_1164.all;

ENTITY AdderSubtractor4bits_vhdl IS
  PORT (
    A     : IN  std_logic_vector(3 downto 0); 
    B     : IN  std_logic_vector(3 downto 0);
    M	: IN	 std_logic;
    S     : OUT std_logic_vector(4 downto 0)                 
  );
END AdderSubtractor4bits_vhdl;

ARCHITECTURE TypeArchitecture OF AdderSubtractor4bits_vhdl IS
  SIGNAL CARRY : std_logic_vector(3 downto 0);
BEGIN
  CARRY(0) <= '0';

  S(0) <= A(0) XOR B(0) XOR CARRY(0);
  CARRY(1) <= ((M XOR A(0)) AND B(0)) OR ((M XOR A(0)) AND CARRY(0)) OR (B(0) AND CARRY(0));

  S(1) <= A(1) XOR B(1) XOR CARRY(1);
  CARRY(2) <= ((M XOR A(1)) AND B(1)) OR ((M XOR A(1)) AND CARRY(1)) OR (B(1) AND CARRY(1));

  S(2) <= A(2) XOR B(2) XOR CARRY(2);
  CARRY(3) <= ((M XOR A(2)) AND B(2)) OR ((M XOR A(2)) AND CARRY(2)) OR (B(2) AND CARRY(2));

  S(3) <= A(3) XOR B(3) XOR CARRY(3);
  S(4) <= ((M XOR A(3)) AND B(3)) OR ((M XOR A(3)) AND CARRY(3)) OR (B(3) AND CARRY(3));
  
END TypeArchitecture;

// VHDL entity TwoComplementSubtractor_vhdl, as the project stores it:
LIBRARY ieee;
USE ieee.std_logic_1164.all;

ENTITY TwoComplementSubtractor_vhdl IS
  PORT (
    A     : IN  std_logic_vector(3 downto 0); 
    B     : IN  std_logic_vector(3 downto 0); 
    S     : OUT std_logic_vector(4 downto 0)
                   
  );
END TwoComplementSubtractor_vhdl;

ARCHITECTURE TypeArchitecture OF TwoComplementSubtractor_vhdl IS
  SIGNAL CARRY : std_logic_vector(3 downto 0);
BEGIN
  CARRY(0) <= '1';
  
  S(0) <= A(0) XOR NOT B(0) XOR CARRY(0);
  CARRY(1) <= (A(0) AND NOT B(0)) OR (A(0) AND CARRY(0)) OR (NOT B(0) AND CARRY(0));

  S(1) <= A(1) XOR NOT B(1) XOR CARRY(1);
  CARRY(2) <= (A(1) AND NOT B(1)) OR (A(1) AND CARRY(1)) OR (NOT B(1) AND CARRY(1));

  S(2) <= A(2) XOR NOT B(2) XOR CARRY(2);
  CARRY(3) <= (A(2) AND NOT B(2)) OR (A(2) AND CARRY(2)) OR (NOT B(2) AND CARRY(2));

  S(3) <= A(3) XOR NOT B(3) XOR CARRY(3);
  S(4) <= (A(3) AND NOT B(3)) OR (A(3) AND CARRY(3)) OR (NOT B(3) AND CARRY(3));
  
END TypeArchitecture;
