// Logisim project trabalhoFinal1.circ as structural Verilog
module main (
  input  [2:0] sel,
  input  [3:0] A,
  input  [3:0] B,
  output [4:0] S
);

  unidade_logica_aritmetica unidade_logica_aritmetica_1 (.sel(sel), .A(A), .B(B), .S(S));
endmodule

module unidade_logica_aritmetica (
  input  [2:0] sel,
  input  [3:0] A,
  input  [3:0] B,
  output [4:0] S
);

  wire not_1_out, not_2_out, not_3_out, not_4_out, not_5_out, not_6_out, not_7_out, not_8_out, not_9_out,
       not_10_out, not_11_out, not_12_out, not_13_out, not_14_out, not_15_out, not_16_out, not_17_out,
       not_18_out, not_19_out, not_20_out, not_21_out, not_22_out, not_23_out, not_24_out, not_25_out,
       not_26_out, not_27_out, not_28_out, not_29_out, not_30_out, not_31_out, not_32_out, not_33_out,
       not_34_out, not_35_out, not_36_out, not_37_out, not_38_out, not_39_out, not_40_out, not_41_out,
       not_42_out, not_43_out, not_44_out, not_45_out, not_46_out, not_47_out, not_48_out, not_49_out,
       not_50_out, not_51_out, not_52_out, not_53_out, not_54_out, not_55_out, not_56_out, not_57_out,
       not_58_out, not_59_out, not_60_out, not_61_out, not_62_out, not_63_out, not_64_out, not_65_out,
       not_66_out, not_67_out, not_68_out, s0, s1, s2, seletor_1_sig3, seletor_1_sig4, seletor_1_sig5,
       seletor_1_sig6, seletor_1_sig7;
  wire [3:0] and_1_out, and_2_out;
  wire [3:3] or_1_out;
  wire [4:0] adder_000_1_s, and_3_out, and_011_1_s, gerador_de_paridade_111_1_s, mascara_ligar_101_1_s,
       mascara_modificar_110_1_s, or_100_1_s, subtractor_001_1_s, twocomplementsub_010_1_s;
  wire [6:0] decodificador_hex_1_out_2, decodificador_hex_2_out_2, decodificador_hex_3_out_2;

  not not_1 (not_1_out, sel[2]);
  not not_2 (not_2_out, sel[2]);
  _7_Segment_Display u_7_segment_display_1 (
    .f(not_1_out), .a(not_2_out), .b(1'b1), .e(not_3_out), .d(not_4_out), .c(1'b1));  // open: g, dp
  not not_3 (not_3_out, sel[2]);
  not not_4 (not_4_out, sel[2]);
  not not_5 (not_5_out, sel[1]);
  not not_6 (not_6_out, sel[0]);
  not not_7 (not_7_out, sel[0]);
  not not_8 (not_8_out, sel[1]);
  _7_Segment_Display u_7_segment_display_2 (
    .f(not_6_out), .a(not_7_out), .b(1'b1), .e(not_9_out), .d(not_10_out), .c(1'b1));  // open: g, dp
  _7_Segment_Display u_7_segment_display_3 (
    .f(not_8_out), .a(not_5_out), .b(1'b1), .e(not_11_out), .d(not_12_out), .c(1'b1));  // open: g, dp
  not not_9 (not_9_out, sel[0]);
  not not_10 (not_10_out, sel[0]);
  not not_11 (not_11_out, sel[1]);
  not not_12 (not_12_out, sel[1]);
  not not_13 (not_13_out, A[3]);
  not not_14 (not_14_out, A[3]);
  _7_Segment_Display u_7_segment_display_4 (
    .f(not_13_out), .a(not_14_out), .b(1'b1), .e(not_15_out), .d(not_16_out), .c(1'b1));  // open: g, dp
  not not_15 (not_15_out, A[3]);
  not not_16 (not_16_out, A[3]);
  not not_17 (not_17_out, A[2]);
  not not_18 (not_18_out, A[2]);
  not not_19 (not_19_out, A[1]);
  _7_Segment_Display u_7_segment_display_5 (
    .f(not_17_out), .a(not_18_out), .b(1'b1), .e(not_20_out), .d(not_21_out), .c(1'b1));  // open: g, dp
  _7_Segment_Display u_7_segment_display_6 (
    .f(not_19_out), .a(not_24_out), .b(1'b1), .e(not_22_out), .d(not_23_out), .c(1'b1));  // open: g, dp
  not not_20 (not_20_out, A[2]);
  not not_21 (not_21_out, A[2]);
  not not_22 (not_22_out, A[1]);
  not not_23 (not_23_out, A[1]);
  seletor seletor_1 (
    .sel(sel), .sig0(s0), .sig1(s1), .sig2(s2), .sig3(seletor_1_sig3), .sig4(seletor_1_sig4),
    .sig5(seletor_1_sig5), .sig6(seletor_1_sig6), .sig7(seletor_1_sig7));
  not not_24 (not_24_out, A[1]);
  not not_25 (not_25_out, A[0]);
  not not_26 (not_26_out, A[0]);
  _7_Segment_Display u_7_segment_display_7 (
    .f(not_25_out), .a(not_26_out), .b(1'b1), .e(not_27_out), .d(not_28_out), .c(1'b1));  // open: g, dp
  not not_27 (not_27_out, A[0]);
  not not_28 (not_28_out, A[0]);
  not not_29 (not_29_out, B[3]);
  not not_30 (not_30_out, B[3]);
  _7_Segment_Display u_7_segment_display_8 (
    .f(not_29_out), .a(not_30_out), .b(1'b1), .e(not_31_out), .d(not_32_out), .c(1'b1));  // open: g, dp
  _7_Segment_Display u_7_segment_display_9 (
    .f(not_34_out), .a(not_35_out), .b(1'b1), .e(not_33_out), .d(not_38_out), .c(1'b1));  // open: g, dp
  not not_31 (not_31_out, B[3]);
  not not_32 (not_32_out, B[3]);
  not not_33 (not_33_out, B[2]);
  not not_34 (not_34_out, B[2]);
  not not_35 (not_35_out, B[2]);
  not not_36 (not_36_out, B[1]);
  not not_37 (not_37_out, B[1]);
  _7_Segment_Display u_7_segment_display_10 (
    .f(not_36_out), .a(not_37_out), .b(1'b1), .e(not_39_out), .d(not_40_out), .c(1'b1));  // open: g, dp
  not not_38 (not_38_out, B[2]);
  not not_39 (not_39_out, B[1]);
  not not_40 (not_40_out, B[1]);
  not not_41 (not_41_out, B[0]);
  not not_42 (not_42_out, B[0]);
  _7_Segment_Display u_7_segment_display_11 (
    .f(not_41_out), .a(not_42_out), .b(1'b1), .e(not_43_out), .d(not_44_out), .c(1'b1));  // open: g, dp
  not not_43 (not_43_out, B[0]);
  not not_44 (not_44_out, B[0]);
  not not_45 (not_45_out, S[4]);
  not not_46 (not_46_out, S[4]);
  not not_47 (not_47_out, S[3]);
  not not_48 (not_48_out, S[3]);
  _7_Segment_Display u_7_segment_display_12 (
    .f(not_45_out), .a(not_46_out), .b(1'b1), .e(not_49_out), .d(not_50_out), .c(1'b1));  // open: g, dp
  _7_Segment_Display u_7_segment_display_13 (
    .f(not_47_out), .a(not_48_out), .b(1'b1), .e(not_51_out), .d(not_52_out), .c(1'b1));  // open: g, dp
  not not_49 (not_49_out, S[4]);
  not not_50 (not_50_out, S[4]);
  not not_51 (not_51_out, S[3]);
  not not_52 (not_52_out, S[3]);
  adder_000 adder_000_1 (.sig(s0), .A(A), .B(B), .S(adder_000_1_s));
  subtractor_001 subtractor_001_1 (.sig(s1), .A(A), .B(B), .S(subtractor_001_1_s));
  twocomplementsub_010 twocomplementsub_010_1 (.sig(s2), .A(A), .B(B), .S(twocomplementsub_010_1_s));
  and_011 and_011_1 (.sig(seletor_1_sig3), .A(A), .B(B), .S(and_011_1_s));
  or_100 or_100_1 (.sig(seletor_1_sig4), .A(A), .B(B), .S(or_100_1_s));
  mascara_ligar_101 mascara_ligar_101_1 (.sig(seletor_1_sig5), .A(A), .B(B), .S(mascara_ligar_101_1_s));
  mascara_modificar_110 mascara_modificar_110_1 (.sig(seletor_1_sig6), .A(A), .B(B), .S(mascara_modificar_110_1_s));
  gerador_de_paridade_111 gerador_de_paridade_111_1 (
    .sig(seletor_1_sig7), .A(A), .B(B), .S(gerador_de_paridade_111_1_s));
  not not_53 (not_53_out, S[2]);
  not not_54 (not_54_out, S[2]);
  _7_Segment_Display u_7_segment_display_14 (
    .f(not_53_out), .a(not_54_out), .b(1'b1), .e(not_55_out), .d(not_56_out), .c(1'b1));  // open: g, dp
  _7_Segment_Display u_7_segment_display_15 (
    .f(not_58_out), .a(not_59_out), .b(1'b1), .e(not_57_out), .d(not_62_out), .c(1'b1));  // open: g, dp
  not not_55 (not_55_out, S[2]);
  not not_56 (not_56_out, S[2]);
  not not_57 (not_57_out, S[1]);
  or or_1 (or_1_out[3], s0, s1, s2);
  not not_58 (not_58_out, S[1]);
  not not_59 (not_59_out, S[1]);
  not not_60 (not_60_out, S[0]);
  not not_61 (not_61_out, S[0]);
  _7_Segment_Display u_7_segment_display_16 (
    .f(not_60_out), .a(not_61_out), .b(1'b1), .e(not_63_out), .d(not_64_out), .c(1'b1));  // open: g, dp
  not not_62 (not_62_out, S[1]);
  not not_63 (not_63_out, S[0]);
  not not_64 (not_64_out, S[0]);
  assign and_1_out = {4{or_1_out[3]}} & A;  // AND_Gate and_1, 4 bits wide
  decodificador_hex decodificador_hex_1 (.in_1(and_1_out), .out_2(decodificador_hex_1_out_2));
  _7_Segment_Display u_7_segment_display_17 (
    .g(decodificador_hex_1_out_2[6]), .f(decodificador_hex_1_out_2[5]), .a(decodificador_hex_1_out_2[0]),
    .b(decodificador_hex_1_out_2[1]), .e(decodificador_hex_1_out_2[4]), .d(decodificador_hex_1_out_2[3]),
    .c(decodificador_hex_1_out_2[2]));  // open: dp
  big_or big_or_1 (
    .S0(adder_000_1_s), .S1(subtractor_001_1_s), .S2(twocomplementsub_010_1_s), .S3(and_011_1_s),
    .S4(or_100_1_s), .S5(mascara_ligar_101_1_s), .S6(mascara_modificar_110_1_s),
    .S7(gerador_de_paridade_111_1_s), .S(S));
  assign and_2_out = {4{or_1_out[3]}} & B;  // AND_Gate and_2, 4 bits wide
  decodificador_hex decodificador_hex_2 (.in_1(and_2_out), .out_2(decodificador_hex_2_out_2));
  assign and_3_out = S & {5{or_1_out[3]}};  // AND_Gate and_3, 5 bits wide
  decodificador_hex decodificador_hex_3 (.in_1(and_3_out[3:0]), .out_2(decodificador_hex_3_out_2));
  _7_Segment_Display u_7_segment_display_18 (
    .g(decodificador_hex_2_out_2[6]), .f(decodificador_hex_2_out_2[5]), .a(decodificador_hex_2_out_2[0]),
    .b(decodificador_hex_2_out_2[1]), .e(decodificador_hex_2_out_2[4]), .d(decodificador_hex_2_out_2[3]),
    .c(decodificador_hex_2_out_2[2]));  // open: dp
  _7_Segment_Display u_7_segment_display_19 (
    .f(not_66_out), .a(not_67_out), .b(1'b1), .e(not_65_out), .d(not_68_out), .c(1'b1));  // open: g, dp
  not not_65 (not_65_out, and_3_out[4]);
  not not_66 (not_66_out, and_3_out[4]);
  not not_67 (not_67_out, and_3_out[4]);
  _7_Segment_Display u_7_segment_display_20 (
    .g(decodificador_hex_3_out_2[6]), .f(decodificador_hex_3_out_2[5]), .a(decodificador_hex_3_out_2[0]),
    .b(decodificador_hex_3_out_2[1]), .e(decodificador_hex_3_out_2[4]), .d(decodificador_hex_3_out_2[3]),
    .c(decodificador_hex_3_out_2[2]));  // open: dp
  not not_68 (not_68_out, and_3_out[4]);

  // Notes on the sheet:
  //   Seletor
  //   BINARIO
  //   Menu de Operações Lógicas
  //   Operações Lógicas
  //   HEXADECIMAL
endmodule

module seletor (
  input  [2:0] sel,
  output sig0,
  output sig1,
  output sig2,
  output sig3,
  output sig4,
  output sig5,
  output sig6,
  output sig7
);

  and and_1 (sig0, ~sel[2], ~sel[1], ~sel[0]);  // AND_Gate
  and and_2 (sig1, ~sel[2], ~sel[1], sel[0]);  // AND_Gate
  and and_3 (sig2, ~sel[2], sel[1], ~sel[0]);  // AND_Gate
  and and_4 (sig3, ~sel[2], sel[1], sel[0]);  // AND_Gate
  and and_5 (sig4, sel[2], ~sel[1], ~sel[0]);  // AND_Gate
  and and_6 (sig5, sel[2], ~sel[1], sel[0]);  // AND_Gate
  and and_7 (sig6, sel[2], sel[1], ~sel[0]);  // AND_Gate
  and and_8 (sig7, sel[2], sel[1], sel[0]);
endmodule

module adder_000 (
  input  sig,
  input  [3:0] A,
  input  [3:0] B,
  output [4:0] S
);

  wire A0_out, A1_out, A2_out, A3_out, B0_out, B1_out, B2_out, B3_out, full_adder_2_cout, full_adder_3_cout,
       full_adder_4_cout;

  and A3 (A3_out, A[3], sig);
  and A2 (A2_out, A[2], sig);
  full_adder full_adder_1 (.A(A3_out), .B(B3_out), .Cin(full_adder_2_cout), .S(S[3]), .Cout(S[4]));
  and A1 (A1_out, A[1], sig);
  and A0 (A0_out, A[0], sig);
  full_adder full_adder_2 (.A(A2_out), .B(B2_out), .Cin(full_adder_3_cout), .S(S[2]), .Cout(full_adder_2_cout));
  and B3 (B3_out, B[3], sig);
  and B2 (B2_out, B[2], sig);
  full_adder full_adder_3 (.A(A1_out), .B(B1_out), .Cin(full_adder_4_cout), .S(S[1]), .Cout(full_adder_3_cout));
  and B1 (B1_out, B[1], sig);
  and B0 (B0_out, B[0], sig);
  full_adder full_adder_4 (.A(A0_out), .B(B0_out), .Cin(1'b0), .S(S[0]), .Cout(full_adder_4_cout));
endmodule

module subtractor_001 (
  input  sig,
  input  [3:0] A,
  input  [3:0] B,
  output [4:0] S
);

  wire A0_out, A1_out, A2_out, A3_out, B0_out, B1_out, B2_out, B3_out, full_subtractor_2_cout,
       full_subtractor_3_cout, full_subtractor_4_cout;

  and A3 (A3_out, A[3], sig);
  and A2 (A2_out, A[2], sig);
  full_subtractor full_subtractor_1 (.A(A3_out), .B(B3_out), .Cin(full_subtractor_2_cout), .S(S[3]), .Cout(S[4]));
  and A1 (A1_out, A[1], sig);
  and A0 (A0_out, A[0], sig);
  full_subtractor full_subtractor_2 (
    .A(A2_out), .B(B2_out), .Cin(full_subtractor_3_cout), .S(S[2]), .Cout(full_subtractor_2_cout));
  and B3 (B3_out, B[3], sig);
  and B2 (B2_out, B[2], sig);
  full_subtractor full_subtractor_3 (
    .A(A1_out), .B(B1_out), .Cin(full_subtractor_4_cout), .S(S[1]), .Cout(full_subtractor_3_cout));
  and B1 (B1_out, B[1], sig);
  and B0 (B0_out, B[0], sig);
  full_subtractor full_subtractor_4 (.A(A0_out), .B(B0_out), .Cin(1'b0), .S(S[0]), .Cout(full_subtractor_4_cout));
endmodule

module twocomplementsub_010 (
  input  sig,
  input  [3:0] A,
  input  [3:0] B,
  output [4:0] S
);

  wire A0_out, A1_out, A2_out, A3_out, and_1_out, B0_out, B1_out, B2_out, B3_out, full_adder_1_cout,
       full_adder_2_cout, full_adder_3_cout, full_adder_4_cout, not_1_out, not_2_out, not_3_out, not_4_out;

  and A3 (A3_out, A[3], sig);
  and A2 (A2_out, A[2], sig);
  full_adder full_adder_1 (.A(A3_out), .B(B3_out), .Cin(full_adder_2_cout), .S(S[3]), .Cout(full_adder_1_cout));
  // NoConnect on full_adder_1_cout
  and A1 (A1_out, A[1], sig);
  and A0 (A0_out, A[0], sig);
  full_adder full_adder_2 (.A(A2_out), .B(B2_out), .Cin(full_adder_3_cout), .S(S[2]), .Cout(full_adder_2_cout));
  not not_1 (not_1_out, B[3]);
  not not_2 (not_2_out, B[2]);
  and B3 (B3_out, not_1_out, sig);
  and B2 (B2_out, not_2_out, sig);
  full_adder full_adder_3 (.A(A1_out), .B(B1_out), .Cin(full_adder_4_cout), .S(S[1]), .Cout(full_adder_3_cout));
  not not_3 (not_3_out, B[1]);
  not not_4 (not_4_out, B[0]);
  and B1 (B1_out, not_3_out, sig);
  and B0 (B0_out, not_4_out, sig);
  and and_1 (and_1_out, sig, 1'b1);
  full_adder full_adder_4 (.A(A0_out), .B(B0_out), .Cin(and_1_out), .S(S[0]), .Cout(full_adder_4_cout));

  assign S[4] = 1'b0;
endmodule

module and_011 (
  input  sig,
  input  [3:0] A,
  input  [3:0] B,
  output [4:0] S
);

  wire S0_out, S1_out, S2_out, S3_out;

  and S3 (S3_out, B[3], A[3]);
  and S2 (S2_out, B[2], A[2]);
  and and_1 (S[2], S2_out, sig);
  and and_2 (S[3], S3_out, sig);
  and S1 (S1_out, B[1], A[1]);
  and S0 (S0_out, A[0], B[0]);
  and and_3 (S[0], S0_out, sig);
  and and_4 (S[1], S1_out, sig);

  assign S[4] = 1'b0;
endmodule

module or_100 (
  input  sig,
  input  [3:0] A,
  input  [3:0] B,
  output [4:0] S
);

  wire S0_out, S1_out, S2_out, S3_out;

  or S3 (S3_out, B[3], A[3]);
  or S2 (S2_out, B[2], A[2]);
  and and_1 (S[2], S2_out, sig);
  and and_2 (S[3], S3_out, sig);
  or S1 (S1_out, B[1], A[1]);
  or S0 (S0_out, A[0], B[0]);
  and and_3 (S[0], S0_out, sig);
  and and_4 (S[1], S1_out, sig);

  assign S[4] = 1'b0;
endmodule

module mascara_ligar_101 (
  input  sig,
  input  [3:0] A,
  input  [3:0] B,
  output [4:0] S
);

  wire S0_out, S1_out, S2_out, S3_out;

  or S3 (S3_out, B[3], A[3]);
  or S2 (S2_out, B[2], A[2]);
  and and_1 (S[2], S2_out, sig);
  and and_2 (S[3], S3_out, sig);
  or S1 (S1_out, B[1], A[1]);
  or S0 (S0_out, A[0], B[0]);
  and and_3 (S[0], S0_out, sig);
  and and_4 (S[1], S1_out, sig);

  assign S[4] = 1'b0;
endmodule

module mascara_modificar_110 (
  input  sig,
  input  [3:0] A,
  input  [3:0] B,
  output [4:0] S
);

  wire xor_1_out, xor_2_out, xor_3_out, xor_4_out;

  xor xor_1 (xor_1_out, B[3], A[3]);
  xor xor_2 (xor_2_out, B[2], A[2]);
  and and_1 (S[2], xor_2_out, sig);
  and and_2 (S[3], xor_1_out, sig);
  xor xor_3 (xor_3_out, B[1], A[1]);
  xor xor_4 (xor_4_out, A[0], B[0]);
  and and_3 (S[0], xor_4_out, sig);
  and and_4 (S[1], xor_3_out, sig);

  assign S[4] = 1'b0;
endmodule

module gerador_de_paridade_111 (
  input  sig,
  input  [3:0] A,
  input  [3:0] B,
  output [4:0] S
);

  wire and_1_out, and_2_out, and_3_out, and_4_out, not_1_out, not_2_out, xor_1_out, xor_2_out;

  not not_1 (not_1_out, A[3]);
  and and_1 (and_1_out, not_1_out, sig);
  and and_2 (and_2_out, A[2], sig);
  xor xor_1 (xor_1_out, and_1_out, and_2_out);
  not not_2 (not_2_out, A[1]);
  and and_3 (and_3_out, not_2_out, sig);
  and and_4 (and_4_out, A[0], sig);
  xor xor_2 (xor_2_out, and_3_out, and_4_out);
  xor xor_3 (S[0], xor_1_out, xor_2_out);

  assign B[2:0] = {3{B[3]}};
  assign S[4:1] = 4'b0000;
  // also tied to GND on the sheet: B[3]
endmodule

module full_adder (
  input  A,
  input  B,
  input  Cin,
  output S,
  output Cout
);

  wire and_1_out, and_2_out, and_3_out, xor_1_out;

  xor xor_1 (xor_1_out, A, B);
  and and_1 (and_1_out, A, B);
  and and_2 (and_2_out, A, Cin);
  and and_3 (and_3_out, B, Cin);
  xor xor_2 (S, xor_1_out, Cin);
  or or_1 (Cout, and_1_out, and_2_out, and_3_out);

  // Notes on the sheet:
  //   S = (A ⊕ B) ⊕ Cin
  //   Cout = (A . B) + (A . Cin) + (B . Cin)
endmodule

module full_subtractor (
  input  A,
  input  B,
  input  Cin,
  output S,
  output Cout
);

  wire and_1_out, and_2_out, and_3_out, not_1_out, xor_1_out;

  not not_1 (not_1_out, A);
  xor xor_1 (xor_1_out, A, B);
  and and_1 (and_1_out, not_1_out, B);
  and and_2 (and_2_out, not_1_out, Cin);
  and and_3 (and_3_out, B, Cin);
  xor xor_2 (S, xor_1_out, Cin);
  or or_1 (Cout, and_1_out, and_2_out, and_3_out);

  // Notes on the sheet:
  //   S = (A ⊕ B) ⊕ Cin
  //   Cout = (A' . B) + (A' . Cin) + (B . Cin)
endmodule

module big_or (
  input  [4:0] S0,
  input  [4:0] S1,
  input  [4:0] S2,
  input  [4:0] S3,
  input  [4:0] S4,
  input  [4:0] S5,
  input  [4:0] S6,
  input  [4:0] S7,
  output [4:0] S
);

  wire [4:0] or_1_out, or_2_out, or_3_out, or_5_out, or_6_out, or_7_out;

  assign or_1_out = S0 | S1;  // OR_Gate or_1, 5 bits wide
  assign or_2_out = S2 | S3;  // OR_Gate or_2, 5 bits wide
  assign or_3_out = or_1_out | or_2_out;  // OR_Gate or_3, 5 bits wide
  assign S = or_3_out | or_6_out;  // OR_Gate or_4, 5 bits wide
  assign or_5_out = S4 | S5;  // OR_Gate or_5, 5 bits wide
  assign or_6_out = or_5_out | or_7_out;  // OR_Gate or_6, 5 bits wide
  assign or_7_out = S6 | S7;  // OR_Gate or_7, 5 bits wide
endmodule

module decodificador_dec (
  input  [3:0] in_1,
  output [6:0] out_2
);

  wire and_1_out, and_2_out, and_3_out, and_4_out, and_5_out, and_6_out, and_7_out, and_8_out, and_9_out,
       and_10_out, and_11_out, and_12_out, and_13_out, and_14_out, and_15_out, and_16_out, and_17_out,
       and_18_out, and_19_out, and_20_out, and_21_out, and_22_out, and_23_out, and_24_out, and_25_out,
       and_26_out, not_1_out, not_2_out, not_3_out, not_4_out;

  not not_1 (not_1_out, in_1[3]);
  not not_2 (not_2_out, in_1[2]);
  not not_3 (not_3_out, in_1[1]);
  not not_4 (not_4_out, in_1[0]);
  and and_1 (and_1_out, not_1_out, in_1[1]);
  and and_2 (and_2_out, not_1_out, in_1[2], in_1[0]);
  and and_3 (and_3_out, in_1[3], not_2_out, not_3_out);
  and and_4 (and_4_out, not_1_out, not_2_out, not_4_out);
  and and_5 (and_5_out, not_1_out, not_2_out);
  and and_6 (and_6_out, not_1_out, not_3_out, not_4_out);
  and and_7 (and_7_out, not_1_out, in_1[1], in_1[0]);
  and and_8 (and_8_out, not_2_out, not_3_out);
  and and_9 (and_9_out, not_1_out, in_1[0]);
  and and_10 (and_10_out, not_1_out, in_1[2]);
  and and_11 (and_11_out, not_2_out, not_3_out);
  and and_12 (and_12_out, not_1_out, not_2_out, in_1[1]);
  and and_13 (and_13_out, not_1_out, in_1[2], not_3_out, in_1[0]);
  and and_14 (and_14_out, not_1_out, in_1[1], not_4_out);
  and and_15 (and_15_out, in_1[3], not_2_out, not_3_out);
  and and_16 (and_16_out, not_1_out, not_2_out, not_4_out);
  and and_17 (and_17_out, not_1_out, in_1[1], not_4_out);
  and and_18 (and_18_out, not_2_out, not_3_out, not_4_out);
  and and_19 (and_19_out, not_1_out, in_1[2], not_3_out);
  and and_20 (and_20_out, not_1_out, in_1[2], not_4_out);
  and and_21 (and_21_out, in_1[3], not_2_out, not_3_out);
  and and_22 (and_22_out, not_1_out, not_3_out, not_4_out);
  and and_23 (and_23_out, not_1_out, not_2_out, in_1[1]);
  and and_24 (and_24_out, not_1_out, in_1[2], not_3_out);
  and and_25 (and_25_out, in_1[3], not_2_out, not_3_out);
  and and_26 (and_26_out, not_1_out, in_1[1], not_4_out);
  or or_1 (out_2[0], and_1_out, and_2_out, and_3_out, and_4_out);
  or or_2 (out_2[1], and_5_out, and_6_out, and_7_out, and_8_out);
  or or_3 (out_2[2], and_9_out, and_10_out, and_11_out);
  or or_4 (out_2[3], and_12_out, and_13_out, and_14_out, and_15_out, and_16_out);
  or or_5 (out_2[4], and_17_out, and_18_out);
  or or_6 (out_2[5], and_19_out, and_20_out, and_21_out, and_22_out);
  or or_7 (out_2[6], and_23_out, and_24_out, and_25_out, and_26_out);
endmodule

module decodificador_hex (
  input  [3:0] in_1,
  output [6:0] out_2
);

  wire and_1_out, and_2_out, and_3_out, and_4_out, and_5_out, and_6_out, and_7_out, and_8_out, and_9_out,
       and_10_out, and_11_out, and_12_out, and_13_out, and_14_out, and_15_out, and_16_out, and_17_out,
       and_18_out, and_19_out, and_20_out, and_21_out, and_22_out, and_23_out, and_24_out, and_25_out,
       and_26_out, and_27_out, and_28_out, and_29_out, and_30_out, and_31_out, and_32_out, and_33_out,
       and_34_out, and_35_out, not_1_out, not_2_out, not_3_out, not_4_out;

  not not_1 (not_1_out, in_1[3]);
  not not_2 (not_2_out, in_1[2]);
  not not_3 (not_3_out, in_1[1]);
  not not_4 (not_4_out, in_1[0]);
  and and_1 (and_1_out, not_2_out, not_4_out);
  and and_2 (and_2_out, not_1_out, in_1[1]);
  and and_3 (and_3_out, not_1_out, in_1[2], in_1[0]);
  and and_4 (and_4_out, in_1[3], not_2_out, not_3_out);
  and and_5 (and_5_out, in_1[3], not_4_out);
  and and_6 (and_6_out, in_1[2], in_1[1]);
  and and_7 (and_7_out, not_1_out, not_3_out, not_4_out);
  and and_8 (and_8_out, not_1_out, in_1[1], in_1[0]);
  and and_9 (and_9_out, not_2_out, not_4_out);
  and and_10 (and_10_out, in_1[3], not_3_out, in_1[0]);
  and and_11 (and_11_out, not_1_out, not_2_out);
  and and_12 (and_12_out, not_1_out, in_1[2]);
  and and_13 (and_13_out, in_1[3], not_2_out);
  and and_14 (and_14_out, not_3_out, in_1[0]);
  and and_15 (and_15_out, not_2_out, not_3_out);
  and and_16 (and_16_out, not_2_out, in_1[0]);
  and and_17 (and_17_out, in_1[2], not_3_out, in_1[0]);
  and and_18 (and_18_out, not_1_out, not_2_out, not_4_out);
  and and_19 (and_19_out, not_2_out, in_1[1], in_1[0]);
  and and_20 (and_20_out, in_1[3], not_3_out);
  and and_21 (and_21_out, in_1[2], in_1[1], not_4_out);
  and and_22 (and_22_out, not_2_out, not_4_out);
  and and_23 (and_23_out, in_1[1], not_4_out);
  and and_24 (and_24_out, in_1[3], in_1[1]);
  and and_25 (and_25_out, in_1[3], in_1[2]);
  and and_26 (and_26_out, not_3_out, not_4_out);
  and and_27 (and_27_out, not_1_out, in_1[2], not_3_out);
  and and_28 (and_28_out, in_1[2], not_4_out);
  and and_29 (and_29_out, in_1[3], not_2_out);
  and and_30 (and_30_out, in_1[3], in_1[1]);
  and and_31 (and_31_out, not_2_out, in_1[1]);
  and and_32 (and_32_out, in_1[3], not_2_out);
  and and_33 (and_33_out, not_1_out, in_1[2], not_3_out);
  and and_34 (and_34_out, in_1[1], not_4_out);
  and and_35 (and_35_out, in_1[3], in_1[0]);
  or or_1 (out_2[0], and_1_out, and_2_out, and_3_out, and_4_out, and_5_out, and_6_out);
  or or_2 (out_2[1], and_7_out, and_8_out, and_9_out, and_10_out, and_11_out);
  or or_3 (out_2[2], and_12_out, and_13_out, and_14_out, and_15_out, and_16_out);
  or or_4 (out_2[3], and_17_out, and_18_out, and_19_out, and_20_out, and_21_out);
  or or_5 (out_2[4], and_22_out, and_23_out, and_24_out, and_25_out);
  or or_6 (out_2[5], and_26_out, and_27_out, and_28_out, and_29_out, and_30_out);
  or or_7 (out_2[6], and_31_out, and_32_out, and_33_out, and_34_out, and_35_out);
endmodule

module main_vhdl (
  input  [2:0] sel,
  input  [3:0] A,
  input  [3:0] B,
  output [4:0] S
);

  unidade_logica_aritmetica_vhdl unidade_logica_aritmetica_vhdl_1 (.sel(sel), .A(A), .B(B), .S(S));
endmodule

module unidade_logica_aritmetica_vhdl (
  input  [2:0] sel,
  input  [3:0] A,
  input  [3:0] B,
  output [4:0] S
);

  wire not_1_out, not_2_out, not_3_out, not_4_out, not_5_out, not_6_out, not_7_out, not_8_out, not_9_out,
       not_10_out, not_11_out, not_12_out, not_13_out, not_14_out, not_15_out, not_16_out, not_17_out,
       not_18_out, not_19_out, not_20_out, not_21_out, not_22_out, not_23_out, not_24_out, not_25_out,
       not_26_out, not_27_out, not_28_out, not_29_out, not_30_out, not_31_out, not_32_out, not_33_out,
       not_34_out, not_35_out, not_36_out, not_37_out, not_38_out, not_39_out, not_40_out, not_41_out,
       not_42_out, not_43_out, not_44_out, not_45_out, not_46_out, not_47_out, not_48_out, not_49_out,
       not_50_out, not_51_out, not_52_out, not_53_out, not_54_out, not_55_out, not_56_out, not_57_out,
       not_58_out, not_59_out, not_60_out, not_61_out, not_62_out, not_63_out, not_64_out, not_65_out,
       not_66_out, not_67_out, not_68_out, s0, s1, s2, seletor_vhdl_1_sig3, seletor_vhdl_1_sig4,
       seletor_vhdl_1_sig5, seletor_vhdl_1_sig6, seletor_vhdl_1_sig7;
  wire [3:0] and_1_out, and_2_out;
  wire [3:3] or_1_out;
  wire [4:0] adder_000_vhdl_1_s, and_3_out, and_011_vhdl_1_s, gerador_de_paridade_111_vhdl_1_s,
       mascara_ligar_101_vhdl_1_s, mascara_modificar_110_vhdl_1_s, or_100_vhdl_1_s, subtractor_001_vhdl_1_s,
       twocomplementsub_010_vhdl_1_s;
  wire [6:0] decodificador_hex_vhdl_1_saida, decodificador_hex_vhdl_2_saida, decodificador_hex_vhdl_3_saida;

  not not_1 (not_1_out, sel[2]);
  not not_2 (not_2_out, sel[2]);
  _7_Segment_Display u_7_segment_display_1 (
    .f(not_1_out), .a(not_2_out), .b(1'b1), .e(not_3_out), .d(not_4_out), .c(1'b1));  // open: g, dp
  not not_3 (not_3_out, sel[2]);
  not not_4 (not_4_out, sel[2]);
  not not_5 (not_5_out, sel[1]);
  not not_6 (not_6_out, sel[0]);
  not not_7 (not_7_out, sel[0]);
  not not_8 (not_8_out, sel[1]);
  _7_Segment_Display u_7_segment_display_2 (
    .f(not_6_out), .a(not_7_out), .b(1'b1), .e(not_9_out), .d(not_10_out), .c(1'b1));  // open: g, dp
  _7_Segment_Display u_7_segment_display_3 (
    .f(not_8_out), .a(not_5_out), .b(1'b1), .e(not_11_out), .d(not_12_out), .c(1'b1));  // open: g, dp
  not not_9 (not_9_out, sel[0]);
  not not_10 (not_10_out, sel[0]);
  not not_11 (not_11_out, sel[1]);
  not not_12 (not_12_out, sel[1]);
  not not_13 (not_13_out, A[3]);
  not not_14 (not_14_out, A[3]);
  _7_Segment_Display u_7_segment_display_4 (
    .f(not_13_out), .a(not_14_out), .b(1'b1), .e(not_15_out), .d(not_16_out), .c(1'b1));  // open: g, dp
  not not_15 (not_15_out, A[3]);
  not not_16 (not_16_out, A[3]);
  not not_17 (not_17_out, A[2]);
  not not_18 (not_18_out, A[2]);
  not not_19 (not_19_out, A[1]);
  _7_Segment_Display u_7_segment_display_5 (
    .f(not_17_out), .a(not_18_out), .b(1'b1), .e(not_20_out), .d(not_21_out), .c(1'b1));  // open: g, dp
  _7_Segment_Display u_7_segment_display_6 (
    .f(not_19_out), .a(not_24_out), .b(1'b1), .e(not_22_out), .d(not_23_out), .c(1'b1));  // open: g, dp
  not not_20 (not_20_out, A[2]);
  not not_21 (not_21_out, A[2]);
  not not_22 (not_22_out, A[1]);
  not not_23 (not_23_out, A[1]);
  seletor_vhdl seletor_vhdl_1 (
    .sel(sel), .sig0(s0), .sig1(s1), .sig2(s2), .sig3(seletor_vhdl_1_sig3), .sig4(seletor_vhdl_1_sig4),
    .sig5(seletor_vhdl_1_sig5), .sig6(seletor_vhdl_1_sig6), .sig7(seletor_vhdl_1_sig7));
  not not_24 (not_24_out, A[1]);
  not not_25 (not_25_out, A[0]);
  not not_26 (not_26_out, A[0]);
  _7_Segment_Display u_7_segment_display_7 (
    .f(not_25_out), .a(not_26_out), .b(1'b1), .e(not_27_out), .d(not_28_out), .c(1'b1));  // open: g, dp
  not not_27 (not_27_out, A[0]);
  not not_28 (not_28_out, A[0]);
  not not_29 (not_29_out, B[3]);
  not not_30 (not_30_out, B[3]);
  _7_Segment_Display u_7_segment_display_8 (
    .f(not_29_out), .a(not_30_out), .b(1'b1), .e(not_31_out), .d(not_32_out), .c(1'b1));  // open: g, dp
  _7_Segment_Display u_7_segment_display_9 (
    .f(not_34_out), .a(not_35_out), .b(1'b1), .e(not_33_out), .d(not_38_out), .c(1'b1));  // open: g, dp
  not not_31 (not_31_out, B[3]);
  not not_32 (not_32_out, B[3]);
  not not_33 (not_33_out, B[2]);
  not not_34 (not_34_out, B[2]);
  not not_35 (not_35_out, B[2]);
  not not_36 (not_36_out, B[1]);
  not not_37 (not_37_out, B[1]);
  _7_Segment_Display u_7_segment_display_10 (
    .f(not_36_out), .a(not_37_out), .b(1'b1), .e(not_39_out), .d(not_40_out), .c(1'b1));  // open: g, dp
  not not_38 (not_38_out, B[2]);
  not not_39 (not_39_out, B[1]);
  not not_40 (not_40_out, B[1]);
  not not_41 (not_41_out, B[0]);
  not not_42 (not_42_out, B[0]);
  _7_Segment_Display u_7_segment_display_11 (
    .f(not_41_out), .a(not_42_out), .b(1'b1), .e(not_43_out), .d(not_44_out), .c(1'b1));  // open: g, dp
  not not_43 (not_43_out, B[0]);
  not not_44 (not_44_out, B[0]);
  not not_45 (not_45_out, S[4]);
  not not_46 (not_46_out, S[4]);
  not not_47 (not_47_out, S[3]);
  not not_48 (not_48_out, S[3]);
  _7_Segment_Display u_7_segment_display_12 (
    .f(not_45_out), .a(not_46_out), .b(1'b1), .e(not_49_out), .d(not_50_out), .c(1'b1));  // open: g, dp
  _7_Segment_Display u_7_segment_display_13 (
    .f(not_47_out), .a(not_48_out), .b(1'b1), .e(not_51_out), .d(not_52_out), .c(1'b1));  // open: g, dp
  not not_49 (not_49_out, S[4]);
  not not_50 (not_50_out, S[4]);
  not not_51 (not_51_out, S[3]);
  not not_52 (not_52_out, S[3]);
  adder_000_vhdl adder_000_vhdl_1 (.sig(s0), .A(A), .B(B), .S(adder_000_vhdl_1_s));
  subtractor_001_vhdl subtractor_001_vhdl_1 (.sig(s1), .A(A), .B(B), .S(subtractor_001_vhdl_1_s));
  twocomplementsub_010_vhdl twocomplementsub_010_vhdl_1 (.sig(s2), .A(A), .B(B), .S(twocomplementsub_010_vhdl_1_s));
  and_011_vhdl and_011_vhdl_1 (.sig(seletor_vhdl_1_sig3), .A(A), .B(B), .S(and_011_vhdl_1_s));
  or_100_vhdl or_100_vhdl_1 (.sig(seletor_vhdl_1_sig4), .A(A), .B(B), .S(or_100_vhdl_1_s));
  mascara_ligar_101_vhdl mascara_ligar_101_vhdl_1 (
    .sig(seletor_vhdl_1_sig5), .A(A), .B(B), .S(mascara_ligar_101_vhdl_1_s));
  mascara_modificar_110_vhdl mascara_modificar_110_vhdl_1 (
    .sig(seletor_vhdl_1_sig6), .A(A), .B(B), .S(mascara_modificar_110_vhdl_1_s));
  gerador_de_paridade_111_vhdl gerador_de_paridade_111_vhdl_1 (
    .sig(seletor_vhdl_1_sig7), .A(A), .B(B), .S(gerador_de_paridade_111_vhdl_1_s));
  not not_53 (not_53_out, S[2]);
  not not_54 (not_54_out, S[2]);
  _7_Segment_Display u_7_segment_display_14 (
    .f(not_53_out), .a(not_54_out), .b(1'b1), .e(not_55_out), .d(not_56_out), .c(1'b1));  // open: g, dp
  _7_Segment_Display u_7_segment_display_15 (
    .f(not_58_out), .a(not_59_out), .b(1'b1), .e(not_57_out), .d(not_62_out), .c(1'b1));  // open: g, dp
  not not_55 (not_55_out, S[2]);
  not not_56 (not_56_out, S[2]);
  not not_57 (not_57_out, S[1]);
  or or_1 (or_1_out[3], s0, s1, s2);
  not not_58 (not_58_out, S[1]);
  not not_59 (not_59_out, S[1]);
  not not_60 (not_60_out, S[0]);
  not not_61 (not_61_out, S[0]);
  _7_Segment_Display u_7_segment_display_16 (
    .f(not_60_out), .a(not_61_out), .b(1'b1), .e(not_63_out), .d(not_64_out), .c(1'b1));  // open: g, dp
  not not_62 (not_62_out, S[1]);
  not not_63 (not_63_out, S[0]);
  not not_64 (not_64_out, S[0]);
  assign and_1_out = {4{or_1_out[3]}} & A;  // AND_Gate and_1, 4 bits wide
  decodificador_hex_vhdl decodificador_hex_vhdl_1 (.entrada(and_1_out), .saida(decodificador_hex_vhdl_1_saida));
  _7_Segment_Display u_7_segment_display_17 (
    .g(decodificador_hex_vhdl_1_saida[6]), .f(decodificador_hex_vhdl_1_saida[5]),
    .a(decodificador_hex_vhdl_1_saida[0]), .b(decodificador_hex_vhdl_1_saida[1]),
    .e(decodificador_hex_vhdl_1_saida[4]), .d(decodificador_hex_vhdl_1_saida[3]),
    .c(decodificador_hex_vhdl_1_saida[2]));  // open: dp
  big_or_vhdl big_or_vhdl_1 (
    .S0(adder_000_vhdl_1_s), .S1(subtractor_001_vhdl_1_s), .S2(twocomplementsub_010_vhdl_1_s),
    .S3(and_011_vhdl_1_s), .S4(or_100_vhdl_1_s), .S5(mascara_ligar_101_vhdl_1_s),
    .S6(mascara_modificar_110_vhdl_1_s), .S7(gerador_de_paridade_111_vhdl_1_s), .S(S));
  assign and_2_out = {4{or_1_out[3]}} & B;  // AND_Gate and_2, 4 bits wide
  decodificador_hex_vhdl decodificador_hex_vhdl_2 (.entrada(and_2_out), .saida(decodificador_hex_vhdl_2_saida));
  assign and_3_out = S & {5{or_1_out[3]}};  // AND_Gate and_3, 5 bits wide
  decodificador_hex_vhdl decodificador_hex_vhdl_3 (.entrada(and_3_out[3:0]), .saida(decodificador_hex_vhdl_3_saida));
  _7_Segment_Display u_7_segment_display_18 (
    .g(decodificador_hex_vhdl_2_saida[6]), .f(decodificador_hex_vhdl_2_saida[5]),
    .a(decodificador_hex_vhdl_2_saida[0]), .b(decodificador_hex_vhdl_2_saida[1]),
    .e(decodificador_hex_vhdl_2_saida[4]), .d(decodificador_hex_vhdl_2_saida[3]),
    .c(decodificador_hex_vhdl_2_saida[2]));  // open: dp
  _7_Segment_Display u_7_segment_display_19 (
    .f(not_66_out), .a(not_67_out), .b(1'b1), .e(not_65_out), .d(not_68_out), .c(1'b1));  // open: g, dp
  not not_65 (not_65_out, and_3_out[4]);
  not not_66 (not_66_out, and_3_out[4]);
  not not_67 (not_67_out, and_3_out[4]);
  _7_Segment_Display u_7_segment_display_20 (
    .g(decodificador_hex_vhdl_3_saida[6]), .f(decodificador_hex_vhdl_3_saida[5]),
    .a(decodificador_hex_vhdl_3_saida[0]), .b(decodificador_hex_vhdl_3_saida[1]),
    .e(decodificador_hex_vhdl_3_saida[4]), .d(decodificador_hex_vhdl_3_saida[3]),
    .c(decodificador_hex_vhdl_3_saida[2]));  // open: dp
  not not_68 (not_68_out, and_3_out[4]);

  // Notes on the sheet:
  //   Seletor
  //   BINARIO
  //   Menu de Operações Lógicas
  //   Operações Lógicas
  //   HEXADECIMAL
endmodule

module adder_000_vhdl (
  input  sig,
  input  [3:0] A,
  input  [3:0] B,
  output [4:0] S
);

  wire A0_out, A1_out, A2_out, A3_out, B0_out, B1_out, B2_out, B3_out, full_adder_vhdl_2_cout,
       full_adder_vhdl_3_cout, full_adder_vhdl_4_cout;

  and A3 (A3_out, A[3], sig);
  and A2 (A2_out, A[2], sig);
  full_adder_vhdl full_adder_vhdl_1 (.A(A3_out), .B(B3_out), .Cin(full_adder_vhdl_2_cout), .S(S[3]), .Cout(S[4]));
  and A1 (A1_out, A[1], sig);
  and A0 (A0_out, A[0], sig);
  full_adder_vhdl full_adder_vhdl_2 (
    .A(A2_out), .B(B2_out), .Cin(full_adder_vhdl_3_cout), .S(S[2]), .Cout(full_adder_vhdl_2_cout));
  and B3 (B3_out, B[3], sig);
  and B2 (B2_out, B[2], sig);
  full_adder_vhdl full_adder_vhdl_3 (
    .A(A1_out), .B(B1_out), .Cin(full_adder_vhdl_4_cout), .S(S[1]), .Cout(full_adder_vhdl_3_cout));
  and B1 (B1_out, B[1], sig);
  and B0 (B0_out, B[0], sig);
  full_adder_vhdl full_adder_vhdl_4 (.A(A0_out), .B(B0_out), .Cin(1'b0), .S(S[0]), .Cout(full_adder_vhdl_4_cout));
endmodule

module subtractor_001_vhdl (
  input  sig,
  input  [3:0] A,
  input  [3:0] B,
  output [4:0] S
);

  wire A0_out, A1_out, A2_out, A3_out, B0_out, B1_out, B2_out, B3_out, full_subtractor_vhdl_2_cout,
       full_subtractor_vhdl_3_cout, full_subtractor_vhdl_4_cout;

  and A3 (A3_out, A[3], sig);
  and A2 (A2_out, A[2], sig);
  full_subtractor_vhdl full_subtractor_vhdl_1 (
    .A(A3_out), .B(B3_out), .Cin(full_subtractor_vhdl_2_cout), .S(S[3]), .Cout(S[4]));
  and A1 (A1_out, A[1], sig);
  and A0 (A0_out, A[0], sig);
  full_subtractor_vhdl full_subtractor_vhdl_2 (
    .A(A2_out), .B(B2_out), .Cin(full_subtractor_vhdl_3_cout), .S(S[2]), .Cout(full_subtractor_vhdl_2_cout));
  and B3 (B3_out, B[3], sig);
  and B2 (B2_out, B[2], sig);
  full_subtractor_vhdl full_subtractor_vhdl_3 (
    .A(A1_out), .B(B1_out), .Cin(full_subtractor_vhdl_4_cout), .S(S[1]), .Cout(full_subtractor_vhdl_3_cout));
  and B1 (B1_out, B[1], sig);
  and B0 (B0_out, B[0], sig);
  full_subtractor_vhdl full_subtractor_vhdl_4 (
    .A(A0_out), .B(B0_out), .Cin(1'b0), .S(S[0]), .Cout(full_subtractor_vhdl_4_cout));
endmodule

module twocomplementsub_010_vhdl (
  input  sig,
  input  [3:0] A,
  input  [3:0] B,
  output [4:0] S
);

  wire A0_out, A1_out, A2_out, A3_out, and_1_out, B0_out, B1_out, B2_out, B3_out, full_adder_vhdl_1_cout,
       full_adder_vhdl_2_cout, full_adder_vhdl_3_cout, full_adder_vhdl_4_cout, not_1_out, not_2_out,
       not_3_out, not_4_out;

  and A3 (A3_out, A[3], sig);
  and A2 (A2_out, A[2], sig);
  full_adder_vhdl full_adder_vhdl_1 (
    .A(A3_out), .B(B3_out), .Cin(full_adder_vhdl_2_cout), .S(S[3]), .Cout(full_adder_vhdl_1_cout));
  // NoConnect on full_adder_vhdl_1_cout
  and A1 (A1_out, A[1], sig);
  and A0 (A0_out, A[0], sig);
  full_adder_vhdl full_adder_vhdl_2 (
    .A(A2_out), .B(B2_out), .Cin(full_adder_vhdl_3_cout), .S(S[2]), .Cout(full_adder_vhdl_2_cout));
  not not_1 (not_1_out, B[3]);
  not not_2 (not_2_out, B[2]);
  and B3 (B3_out, not_1_out, sig);
  and B2 (B2_out, not_2_out, sig);
  full_adder_vhdl full_adder_vhdl_3 (
    .A(A1_out), .B(B1_out), .Cin(full_adder_vhdl_4_cout), .S(S[1]), .Cout(full_adder_vhdl_3_cout));
  not not_3 (not_3_out, B[1]);
  not not_4 (not_4_out, B[0]);
  and B1 (B1_out, not_3_out, sig);
  and B0 (B0_out, not_4_out, sig);
  and and_1 (and_1_out, sig, 1'b1);
  full_adder_vhdl full_adder_vhdl_4 (.A(A0_out), .B(B0_out), .Cin(and_1_out), .S(S[0]), .Cout(full_adder_vhdl_4_cout));

  assign S[4] = 1'b0;
endmodule

// VHDL entity seletor_vhdl, as the project stores it:
LIBRARY ieee;
USE ieee.std_logic_1164.all;

ENTITY seletor_vhdl IS
  PORT (
    sel     : IN  std_logic_vector(2 downto 0);
    sig0    : OUT std_logic;
    sig1    : OUT std_logic;
    sig2    : OUT std_logic;
    sig3    : OUT std_logic;
    sig4    : OUT std_logic;
    sig5    : OUT std_logic;
    sig6    : OUT std_logic;
    sig7    : OUT std_logic
  );
END seletor_vhdl;

ARCHITECTURE TypeArchitecture OF seletor_vhdl IS
BEGIN
  PROCESS (sel)
  BEGIN
    sig0 <= '0';
    sig1 <= '0';
    sig2 <= '0';
    sig3 <= '0';
    sig4 <= '0';
    sig5 <= '0';
    sig6 <= '0';
    sig7 <= '0';
    
    CASE sel IS
      WHEN "000" => sig0 <= '1';
      WHEN "001" => sig1 <= '1';
      WHEN "010" => sig2 <= '1';
      WHEN "011" => sig3 <= '1';
      WHEN "100" => sig4 <= '1';
      WHEN "101" => sig5 <= '1';
      WHEN "110" => sig6 <= '1';
      WHEN "111" => sig7 <= '1';
      WHEN OTHERS => NULL;
    END CASE;
  END PROCESS;
END TypeArchitecture;

// VHDL entity and_011_vhdl, as the project stores it:
LIBRARY ieee;
USE ieee.std_logic_1164.ALL;

ENTITY and_011_vhdl IS
  PORT (
    sig    : IN  std_logic;
    A      : IN  std_logic_vector(3 downto 0);
    B      : IN  std_logic_vector(3 downto 0);
    S      : OUT std_logic_vector(4 downto 0)
  );
END and_011_vhdl;

ARCHITECTURE Behavioral OF and_011_vhdl IS
BEGIN
  PROCESS (A, B, sig)
  BEGIN
    FOR i IN 0 TO 3 LOOP
      S(i) <= (A(i) AND B(i)) AND sig;
    END LOOP;
    S(4) <= '0';
  END PROCESS;
END Behavioral;

// VHDL entity or_100_vhdl, as the project stores it:
LIBRARY ieee;
USE ieee.std_logic_1164.ALL;

ENTITY or_100_vhdl IS
  PORT (
    sig    : IN  std_logic;
    A      : IN  std_logic_vector(3 downto 0);
    B      : IN  std_logic_vector(3 downto 0);
    S      : OUT std_logic_vector(4 downto 0)
  );
END or_100_vhdl;

ARCHITECTURE Behavioral OF or_100_vhdl IS
BEGIN
  PROCESS (A, B, sig)
  BEGIN
    FOR i IN 0 TO 3 LOOP
      S(i) <= (A(i) OR B(i)) AND sig;
    END LOOP;
    S(4) <= '0';
  END PROCESS;
END Behavioral;

// VHDL entity mascara_ligar_101_vhdl, as the project stores it:
LIBRARY ieee;
USE ieee.std_logic_1164.ALL;

ENTITY mascara_ligar_101_vhdl IS
  PORT (
    sig    : IN  std_logic;
    A      : IN  std_logic_vector(3 downto 0);
    B      : IN  std_logic_vector(3 downto 0);
    S      : OUT std_logic_vector(4 downto 0)
  );
END mascara_ligar_101_vhdl;

ARCHITECTURE Behavioral OF mascara_ligar_101_vhdl IS
BEGIN
  PROCESS (A, B, sig)
  BEGIN
    FOR i IN 0 TO 3 LOOP
      S(i) <= (A(i) OR B(i)) AND sig;
    END LOOP;
    S(4) <= '0';
  END PROCESS;
END Behavioral;

// VHDL entity mascara_modificar_110_vhdl, as the project stores it:
LIBRARY ieee;
USE ieee.std_logic_1164.ALL;

ENTITY mascara_modificar_110_vhdl IS
  PORT (
    sig    : IN  std_logic;
    A      : IN  std_logic_vector(3 downto 0);
    B      : IN  std_logic_vector(3 downto 0);
    S      : OUT std_logic_vector(4 downto 0)
  );
END mascara_modificar_110_vhdl;

ARCHITECTURE Behavioral OF mascara_modificar_110_vhdl IS
BEGIN
  PROCESS (A, B, sig)
  BEGIN
    FOR i IN 0 TO 3 LOOP
      S(i) <= (A(i) XOR B(i)) AND sig;
    END LOOP;
    S(4) <= '0';
  END PROCESS;
END Behavioral;

// VHDL entity gerador_de_paridade_111_vhdl, as the project stores it:
LIBRARY ieee;
USE ieee.std_logic_1164.ALL;

ENTITY gerador_de_paridade_111_vhdl IS
  PORT (
    sig    : IN  std_logic;
    A      : IN  std_logic_vector(3 downto 0);
    B      : IN  std_logic_vector(3 downto 0);
    S      : OUT std_logic_vector(4 downto 0)
  );
END gerador_de_paridade_111_vhdl;

ARCHITECTURE Behavioral OF gerador_de_paridade_111_vhdl IS
BEGIN
  S(0) <= (A(0) XOR NOT A(1) XOR A(2) XOR NOT A(3)) AND sig;
  S(1) <= '0';
  S(2) <= '0';
  S(3) <= '0';
  S(4) <= '0';
END Behavioral;

// VHDL entity full_adder_vhdl, as the project stores it:
LIBRARY ieee;
USE ieee.std_logic_1164.all;

ENTITY full_adder_vhdl IS
  PORT (
    A      : IN  std_logic;
    B      : IN  std_logic;
    Cin    : IN  std_logic;
    S      : OUT std_logic;
    Cout   : OUT std_logic
  );
END full_adder_vhdl;

ARCHITECTURE TypeArchitecture OF full_adder_vhdl IS
BEGIN
  S <= (A XOR B) XOR Cin;
  Cout <= (A AND B) or (A AND Cin) or (B AND Cin);
END TypeArchitecture;

// VHDL entity full_subtractor_vhdl, as the project stores it:
LIBRARY ieee;
USE ieee.std_logic_1164.all;

ENTITY full_subtractor_vhdl IS
  PORT (
    A      : IN  std_logic;
    B      : IN  std_logic;
    Cin    : IN  std_logic;
    S      : OUT std_logic;
    Cout   : OUT std_logic
  );
END full_subtractor_vhdl;

ARCHITECTURE TypeArchitecture OF full_subtractor_vhdl IS
BEGIN
  S <= (A XOR B) XOR Cin;
  Cout <= (NOT A AND B) or (NOT A AND Cin) or (B AND Cin);
END TypeArchitecture;

// VHDL entity big_or_vhdl, as the project stores it:
LIBRARY ieee;
USE ieee.std_logic_1164.all;

ENTITY big_or_vhdl IS
  PORT (
    S0  : IN  std_logic_vector(4 downto 0);
    S1  : IN  std_logic_vector(4 downto 0);
    S2  : IN  std_logic_vector(4 downto 0);
    S3  : IN  std_logic_vector(4 downto 0);
    S4  : IN  std_logic_vector(4 downto 0);
    S5  : IN  std_logic_vector(4 downto 0);
    S6  : IN  std_logic_vector(4 downto 0);
    S7  : IN  std_logic_vector(4 downto 0);
    S   : OUT std_logic_vector(4 downto 0)
  );
END big_or_vhdl;

ARCHITECTURE Behavioral OF big_or_vhdl IS
BEGIN
  PROCESS (S0, S1, S2, S3, S4, S5, S6, S7)
  BEGIN
    S <= S0 OR S1 OR S2 OR S3 OR S4 OR S5 OR S6 OR S7;
  END PROCESS;
END Behavioral;

// VHDL entity decodificador_dec_vhdl, as the project stores it:
library IEEE;
use IEEE.STD_LOGIC_1164.ALL;

entity decodificador_dec_vhdl is
    Port (
        entrada : in STD_LOGIC_VECTOR(3 downto 0);
        saida   : out STD_LOGIC_VECTOR(6 downto 0)
    );
end decodificador_dec_vhdl;

architecture Behavioral of decodificador_dec_vhdl is
begin
    process(entrada)
    begin
        case entrada is
            when "0000" => saida <= "0111111";
            when "0001" => saida <= "0000110";
            when "0010" => saida <= "1011011";
            when "0011" => saida <= "1001111";
            when "0100" => saida <= "1100110";
            when "0101" => saida <= "1101101";
            when "0110" => saida <= "1111101";
            when "0111" => saida <= "0000111";
            when "1000" => saida <= "1111111";
            when "1001" => saida <= "1101111";
            when others => saida <= "0000000";
        end case;
    end process;
end Behavioral;

// VHDL entity decodificador_hex_vhdl, as the project stores it:
library IEEE;
use IEEE.STD_LOGIC_1164.ALL;

entity decodificador_hex_vhdl is
    Port (
        entrada : in STD_LOGIC_VECTOR(3 downto 0);
        saida   : out STD_LOGIC_VECTOR(6 downto 0)
    );
end decodificador_hex_vhdl;

architecture Behavioral of decodificador_hex_vhdl is
begin
    process(entrada)
    begin
        case entrada is
            when "0000" => saida <= "0111111";
            when "0001" => saida <= "0000110";
            when "0010" => saida <= "1011011";
            when "0011" => saida <= "1001111";
            when "0100" => saida <= "1100110";
            when "0101" => saida <= "1101101";
            when "0110" => saida <= "1111101";
            when "0111" => saida <= "0000111";
            when "1000" => saida <= "1111111";
            when "1001" => saida <= "1101111";
            when "1010" => saida <= "1110111";
            when "1011" => saida <= "1111100";
            when "1100" => saida <= "0111001";
            when "1101" => saida <= "1011110";
            when "1110" => saida <= "1111001";
            when "1111" => saida <= "1110001";
            when others => saida <= "0000000";
        end case;
    end process;
end Behavioral;
