// Logisim project trabalhoFinal2.circ as structural Verilog
module main (
);

  and_nand and_nand_1 ();  // open: A, B, S
  not_nand not_nand_1 ();  // open: A, S
  HalfSubtractor halfsubtractor_1 ();  // open: A, B, S, Cout
  xor_nand xor_nand_1 ();  // open: A, B, S
  or_nand or_nand_1 ();  // open: A, B, S
  FullSubtractor fullsubtractor_1 ();  // open: A, B, Cin, S, Cout
  HalfAdder halfadder_1 ();  // open: A, B, S, Cout
  TwoComplementSubtractor_vhdl twocomplementsubtractor_vhdl_1 ();  // open: A, B, S, OVERF
  HalfSubtractor_nand halfsubtractor_nand_1 ();  // open: A, B, S, Cout
  HalfAdder_nand halfadder_nand_1 ();  // open: A, B, S, Cout
  FullAdder fulladder_1 ();  // open: A, B, Cin, S, Cout
  FullSubtractor_nand fullsubtractor_nand_1 ();  // open: A, B, Cin, S, Cout
  FullAdder_nand fulladder_nand_1 ();  // open: A, B, Cin, S, Cout
  HalfAdderSubtractor halfaddersubtractor_1 ();  // open: M, A, B, Cin, S, Cout
  HalfAdderSubtractor_nand halfaddersubtractor_nand_1 ();  // open: M, A, B, Cin, S, Cout
  AdderSubtractor4bits_vhdl addersubtractor4bits_vhdl_1 ();  // open: M, A, B, S, OVERF
  AdderSubtractor4bits addersubtractor4bits_1 ();  // open: A3, A2, A1, A0, B3, B2, B1, B0, M, OVERF, S3, S2, S1, S0
  AdderSubtractor4bits_nand addersubtractor4bits_nand_1 ();  // open: A3, A2, A1, A0, B3, B2, B1, B0, M, OVERF, S3, S2, S1, S0
  Adder4bits_vhdl adder4bits_vhdl_1 ();  // open: A, B, S, OVERF
  Subtractor4bits subtractor4bits_1 ();  // open: A3, A2, A1, A0, B3, B2, B1, B0, OVERF, S3, S2, S1, S0
  Subtractor4bits_nand subtractor4bits_nand_1 ();  // open: A3, A2, A1, A0, B3, B2, B1, B0, OVERF, S3, S2, S1, S0
  Sutractor4bits_vhdl sutractor4bits_vhdl_1 ();  // open: A, B, S, OVERF
  Adder4bits adder4bits_1 ();  // open: A3, A2, A1, A0, B3, B2, B1, B0, OVERF, S3, S2, S1, S0
  Adder4bits_nand adder4bits_nand_1 ();  // open: A3, A2, A1, A0, B3, B2, B1, B0, OVERF, S3, S2, S1, S0
  HalfAdderSubtractor_vhdl halfaddersubtractor_vhdl_1 ();  // open: A, B, Cin, M, S, Cout
  TwoComplementSubtractor4bits twocomplementsubtractor4bits_1 ();  // open: A3, A2, A1, A0, B3, B2, B1, B0, OVERF, S3, S2, S1, S0
  TwoComplementSubtractor4bits_nand twocomplementsubtractor4bits_nand_1 ();  // open: A3, A2, A1, A0, B3, B2, B1, B0, OVERF, S3, S2, S1, S0
  FullAdder_vhdl fulladder_vhdl_1 ();  // open: A, B, Cin, S, Cout
  FullSubtractor_vhdl fullsubtractor_vhdl_1 ();  // open: A, B, Cin, S, Cout
  HalfAdder_vhdl halfadder_vhdl_1 ();  // open: A, B, S, Cout
  HalfSubtractor_vhdl halfsubtractor_vhdl_1 ();  // open: A, B, S, Cout
endmodule

module TwoComplementSubtractor4bits (
  input  A3,
  input  A2,
  input  A1,
  input  A0,
  input  B3,
  input  B2,
  input  B1,
  input  B0,
  output OVERF,
  output S3,
  output S2,
  output S1,
  output S0
);

  wire fulladder_2_cout, fulladder_3_cout, fulladder_4_cout, not_1_out, not_2_out, not_3_out, not_4_out;

  FullAdder fulladder_1 (.A(A3), .B(not_1_out), .Cin(fulladder_2_cout), .S(S3), .Cout(OVERF));
  FullAdder fulladder_2 (.A(A2), .B(not_2_out), .Cin(fulladder_3_cout), .S(S2), .Cout(fulladder_2_cout));
  not not_1 (not_1_out, B3);
  not not_2 (not_2_out, B2);
  not not_3 (not_3_out, B1);
  FullAdder fulladder_3 (.A(A1), .B(not_3_out), .Cin(fulladder_4_cout), .S(S1), .Cout(fulladder_3_cout));
  not not_4 (not_4_out, B0);
  FullAdder fulladder_4 (.A(A0), .B(not_4_out), .Cin(1'b1), .S(S0), .Cout(fulladder_4_cout));
endmodule

module Adder4bits (
  input  A3,
  input  A2,
  input  A1,
  input  A0,
  input  B3,
  input  B2,
  input  B1,
  input  B0,
  output OVERF,
  output S3,
  output S2,
  output S1,
  output S0
);

  wire fulladder_2_cout, fulladder_3_cout, fulladder_4_cout;

  FullAdder fulladder_1 (.A(A3), .B(B3), .Cin(fulladder_2_cout), .S(S3), .Cout(OVERF));
  FullAdder fulladder_2 (.A(A2), .B(B2), .Cin(fulladder_3_cout), .S(S2), .Cout(fulladder_2_cout));
  FullAdder fulladder_3 (.A(A1), .B(B1), .Cin(fulladder_4_cout), .S(S1), .Cout(fulladder_3_cout));
  FullAdder fulladder_4 (.A(A0), .B(B0), .Cin(1'b0), .S(S0), .Cout(fulladder_4_cout));
endmodule

module Subtractor4bits (
  input  A3,
  input  A2,
  input  A1,
  input  A0,
  input  B3,
  input  B2,
  input  B1,
  input  B0,
  output OVERF,
  output S3,
  output S2,
  output S1,
  output S0
);

  wire fullsubtractor_2_cout, fullsubtractor_3_cout, fullsubtractor_4_cout;

  FullSubtractor fullsubtractor_1 (.A(A3), .B(B3), .Cin(fullsubtractor_2_cout), .S(S3), .Cout(OVERF));
  FullSubtractor fullsubtractor_2 (.A(A2), .B(B2), .Cin(fullsubtractor_3_cout), .S(S2), .Cout(fullsubtractor_2_cout));
  FullSubtractor fullsubtractor_3 (.A(A1), .B(B1), .Cin(fullsubtractor_4_cout), .S(S1), .Cout(fullsubtractor_3_cout));
  FullSubtractor fullsubtractor_4 (.A(A0), .B(B0), .Cin(1'b0), .S(S0), .Cout(fullsubtractor_4_cout));
endmodule

module AdderSubtractor4bits (
  input  A3,
  input  A2,
  input  A1,
  input  A0,
  input  B3,
  input  B2,
  input  B1,
  input  B0,
  input  M,
  output OVERF,
  output S3,
  output S2,
  output S1,
  output S0
);

  wire halfaddersubtractor_2_cout, halfaddersubtractor_3_cout, halfaddersubtractor_4_cout;

  HalfAdderSubtractor halfaddersubtractor_1 (
    .M(M), .A(A3), .B(B3), .Cin(halfaddersubtractor_2_cout), .S(S3), .Cout(OVERF));
  HalfAdderSubtractor halfaddersubtractor_2 (
    .M(M), .A(A2), .B(B2), .Cin(halfaddersubtractor_3_cout), .S(S2), .Cout(halfaddersubtractor_2_cout));
  HalfAdderSubtractor halfaddersubtractor_3 (
    .M(M), .A(A1), .B(B1), .Cin(halfaddersubtractor_4_cout), .S(S1), .Cout(halfaddersubtractor_3_cout));
  HalfAdderSubtractor halfaddersubtractor_4 (
    .M(M), .A(A0), .B(B0), .Cin(1'b0), .S(S0), .Cout(halfaddersubtractor_4_cout));
endmodule

module HalfAdderSubtractor (
  input  M,
  input  A,
  input  B,
  input  Cin,
  output S,
  output Cout
);

  wire and_1_out, and_2_out, and_3_out, xor_1_out, xor_2_out;

  xor xor_1 (xor_1_out, M, A);
  xor xor_2 (xor_2_out, A, B);
  and and_1 (and_1_out, xor_1_out, B);
  and and_2 (and_2_out, xor_1_out, Cin);
  and and_3 (and_3_out, B, Cin);
  xor xor_3 (S, xor_2_out, Cin);
  or or_1 (Cout, and_1_out, and_2_out, and_3_out);

  // Notes on the sheet:
  //   S = (A ⊕ B) ⊕ (Cin)
  //   Cout = ((M ⊕ A) . B) + ((M ⊕ A) . Cin) + (B . Cin)
endmodule

module FullAdder (
  input  A,
  input  B,
  input  Cin,
  output S,
  output Cout
);

  wire and_1_out, and_2_out, and_3_out, xor_1_out;

  xor xor_1 (xor_1_out, A, B);
  and and_1 (and_1_out, A, B);
  and and_2 (and_2_out, A, Cin);
  and and_3 (and_3_out, B, Cin);
  xor xor_2 (S, xor_1_out, Cin);
  or or_1 (Cout, and_1_out, and_2_out, and_3_out);

  // Notes on the sheet:
  //   S = (A ⊕ B) ⊕ Cin
  //   Cout = (A . B) + (A . Cin) + (B . Cin)
endmodule

module FullSubtractor (
  input  A,
  input  B,
  input  Cin,
  output S,
  output Cout
);

  wire and_1_out, and_2_out, and_3_out, not_1_out, xor_1_out;

  not not_1 (not_1_out, A);
  xor xor_1 (xor_1_out, A, B);
  and and_1 (and_1_out, not_1_out, B);
  and and_2 (and_2_out, not_1_out, Cin);
  and and_3 (and_3_out, B, Cin);
  xor xor_2 (S, xor_1_out, Cin);
  or or_1 (Cout, and_1_out, and_2_out, and_3_out);

  // Notes on the sheet:
  //   S = (A ⊕ B) ⊕ Cin
  //   Cout = (A' . B) + (A' . Cin) + (B . Cin)
endmodule

module HalfAdder (
  input  A,
  input  B,
  output S,
  output Cout
);

  xor xor_1 (S, A, B);
  and and_1 (Cout, A, B);

  // Notes on the sheet:
  //   S = A ⊕ B
  //   Cout = (A . B)
endmodule

module HalfSubtractor (
  input  A,
  input  B,
  output S,
  output Cout
);

  wire not_1_out;

  not not_1 (not_1_out, A);
  xor xor_1 (S, A, B);
  and and_1 (Cout, not_1_out, B);

  // Notes on the sheet:
  //   S = (A ⊕ B)
  //   Cout = (A' . B)
endmodule

module TwoComplementSubtractor4bits_nand (
  input  A3,
  input  A2,
  input  A1,
  input  A0,
  input  B3,
  input  B2,
  input  B1,
  input  B0,
  output OVERF,
  output S3,
  output S2,
  output S1,
  output S0
);

  wire fulladder_nand_2_cout, fulladder_nand_3_cout, fulladder_nand_4_cout, not_1_out, not_2_out, not_3_out,
       not_4_out;

  FullAdder_nand fulladder_nand_1 (.A(A3), .B(not_1_out), .Cin(fulladder_nand_2_cout), .S(S3), .Cout(OVERF));
  FullAdder_nand fulladder_nand_2 (
    .A(A2), .B(not_2_out), .Cin(fulladder_nand_3_cout), .S(S2), .Cout(fulladder_nand_2_cout));
  not not_1 (not_1_out, B3);
  not not_2 (not_2_out, B2);
  not not_3 (not_3_out, B1);
  FullAdder_nand fulladder_nand_3 (
    .A(A1), .B(not_3_out), .Cin(fulladder_nand_4_cout), .S(S1), .Cout(fulladder_nand_3_cout));
  not not_4 (not_4_out, B0);
  FullAdder_nand fulladder_nand_4 (.A(A0), .B(not_4_out), .Cin(1'b1), .S(S0), .Cout(fulladder_nand_4_cout));
endmodule

module Adder4bits_nand (
  input  A3,
  input  A2,
  input  A1,
  input  A0,
  input  B3,
  input  B2,
  input  B1,
  input  B0,
  output OVERF,
  output S3,
  output S2,
  output S1,
  output S0
);

  wire fulladder_nand_2_cout, fulladder_nand_3_cout, fulladder_nand_4_cout;

  FullAdder_nand fulladder_nand_1 (.A(A3), .B(B3), .Cin(fulladder_nand_2_cout), .S(S3), .Cout(OVERF));
  FullAdder_nand fulladder_nand_2 (.A(A2), .B(B2), .Cin(fulladder_nand_3_cout), .S(S2), .Cout(fulladder_nand_2_cout));
  FullAdder_nand fulladder_nand_3 (.A(A1), .B(B1), .Cin(fulladder_nand_4_cout), .S(S1), .Cout(fulladder_nand_3_cout));
  FullAdder_nand fulladder_nand_4 (.A(A0), .B(B0), .Cin(1'b0), .S(S0), .Cout(fulladder_nand_4_cout));
endmodule

module Subtractor4bits_nand (
  input  A3,
  input  A2,
  input  A1,
  input  A0,
  input  B3,
  input  B2,
  input  B1,
  input  B0,
  output OVERF,
  output S3,
  output S2,
  output S1,
  output S0
);

  wire fullsubtractor_nand_2_cout, fullsubtractor_nand_3_cout, fullsubtractor_nand_4_cout;

  FullSubtractor_nand fullsubtractor_nand_1 (.A(A3), .B(B3), .Cin(fullsubtractor_nand_2_cout), .S(S3), .Cout(OVERF));
  FullSubtractor_nand fullsubtractor_nand_2 (
    .A(A2), .B(B2), .Cin(fullsubtractor_nand_3_cout), .S(S2), .Cout(fullsubtractor_nand_2_cout));
  FullSubtractor_nand fullsubtractor_nand_3 (
    .A(A1), .B(B1), .Cin(fullsubtractor_nand_4_cout), .S(S1), .Cout(fullsubtractor_nand_3_cout));
  FullSubtractor_nand fullsubtractor_nand_4 (.A(A0), .B(B0), .Cin(1'b0), .S(S0), .Cout(fullsubtractor_nand_4_cout));
endmodule

module AdderSubtractor4bits_nand (
  input  A3,
  input  A2,
  input  A1,
  input  A0,
  input  B3,
  input  B2,
  input  B1,
  input  B0,
  input  M,
  output OVERF,
  output S3,
  output S2,
  output S1,
  output S0
);

  wire halfaddersubtractor_nand_2_cout, halfaddersubtractor_nand_3_cout, halfaddersubtractor_nand_4_cout;

  HalfAdderSubtractor_nand halfaddersubtractor_nand_1 (
    .M(M), .A(A3), .B(B3), .Cin(halfaddersubtractor_nand_2_cout), .S(S3), .Cout(OVERF));
  HalfAdderSubtractor_nand halfaddersubtractor_nand_2 (
    .M(M), .A(A2), .B(B2), .Cin(halfaddersubtractor_nand_3_cout), .S(S2),
    .Cout(halfaddersubtractor_nand_2_cout));
  HalfAdderSubtractor_nand halfaddersubtractor_nand_3 (
    .M(M), .A(A1), .B(B1), .Cin(halfaddersubtractor_nand_4_cout), .S(S1),
    .Cout(halfaddersubtractor_nand_3_cout));
  HalfAdderSubtractor_nand halfaddersubtractor_nand_4 (
    .M(M), .A(A0), .B(B0), .Cin(1'b0), .S(S0), .Cout(halfaddersubtractor_nand_4_cout));
endmodule

module HalfAdderSubtractor_nand (
  input  M,
  input  A,
  input  B,
  input  Cin,
  output S,
  output Cout
);

  wire and_nand_1_s, and_nand_2_s, and_nand_3_s, or_nand_1_s, xor_nand_1_s, xor_nand_2_s;

  xor_nand xor_nand_1 (.A(A), .B(M), .S(xor_nand_1_s));
  xor_nand xor_nand_2 (.A(A), .B(B), .S(xor_nand_2_s));
  and_nand and_nand_1 (.A(xor_nand_1_s), .B(B), .S(and_nand_1_s));
  and_nand and_nand_2 (.A(xor_nand_1_s), .B(Cin), .S(and_nand_2_s));
  and_nand and_nand_3 (.A(B), .B(Cin), .S(and_nand_3_s));
  xor_nand xor_nand_3 (.A(xor_nand_2_s), .B(Cin), .S(S));
  or_nand or_nand_1 (.A(and_nand_1_s), .B(and_nand_2_s), .S(or_nand_1_s));
  or_nand or_nand_2 (.A(or_nand_1_s), .B(and_nand_3_s), .S(Cout));

  // Notes on the sheet:
  //   S = (A ⊕ B) ⊕ (Cin)
  //   Cout = ((M ⊕ A) . B) + ((M ⊕ A) . Cin) + (B . Cin)
endmodule

module FullAdder_nand (
  input  A,
  input  B,
  input  Cin,
  output S,
  output Cout
);

  wire and_nand_1_s, and_nand_2_s, and_nand_3_s, or_nand_1_s, xor_nand_1_s;

  xor_nand xor_nand_1 (.A(A), .B(B), .S(xor_nand_1_s));
  xor_nand xor_nand_2 (.A(xor_nand_1_s), .B(Cin), .S(S));
  and_nand and_nand_1 (.A(A), .B(B), .S(and_nand_1_s));
  and_nand and_nand_2 (.A(A), .B(Cin), .S(and_nand_2_s));
  and_nand and_nand_3 (.A(B), .B(Cin), .S(and_nand_3_s));
  or_nand or_nand_1 (.A(and_nand_1_s), .B(and_nand_2_s), .S(or_nand_1_s));
  or_nand or_nand_2 (.A(or_nand_1_s), .B(and_nand_3_s), .S(Cout));

  // Notes on the sheet:
  //   S = (A ⊕ B) ⊕ Cin
  //   Cout = (A . B) + (A . Cin) + (B . Cin)
endmodule

module FullSubtractor_nand (
  input  A,
  input  B,
  input  Cin,
  output S,
  output Cout
);

  wire and_nand_1_s, and_nand_2_s, and_nand_3_s, not_nand_1_s, or_nand_1_s, xor_nand_1_s;

  not_nand not_nand_1 (.A(A), .S(not_nand_1_s));
  xor_nand xor_nand_1 (.A(A), .B(B), .S(xor_nand_1_s));
  xor_nand xor_nand_2 (.A(xor_nand_1_s), .B(Cin), .S(S));
  and_nand and_nand_1 (.A(not_nand_1_s), .B(B), .S(and_nand_1_s));
  and_nand and_nand_2 (.A(not_nand_1_s), .B(Cin), .S(and_nand_2_s));
  and_nand and_nand_3 (.A(B), .B(Cin), .S(and_nand_3_s));
  or_nand or_nand_1 (.A(and_nand_1_s), .B(and_nand_2_s), .S(or_nand_1_s));
  or_nand or_nand_2 (.A(or_nand_1_s), .B(and_nand_3_s), .S(Cout));

  // Notes on the sheet:
  //   S = (A ⊕ B) ⊕ Cin
  //   Cout = (A' . B) + (A' . Cin) + (B . Cin)
endmodule

module HalfAdder_nand (
  input  A,
  input  B,
  output S,
  output Cout
);

  xor_nand xor_nand_1 (.A(A), .B(B), .S(S));
  and_nand and_nand_1 (.A(A), .B(B), .S(Cout));

  // Notes on the sheet:
  //   S = A ⊕ B
  //   Cout = (A . B)
endmodule

module HalfSubtractor_nand (
  input  A,
  input  B,
  output S,
  output Cout
);

  wire not_nand_1_s;

  xor_nand xor_nand_1 (.A(A), .B(B), .S(S));
  not_nand not_nand_1 (.A(A), .S(not_nand_1_s));
  and_nand and_nand_1 (.A(not_nand_1_s), .B(B), .S(Cout));

  // Notes on the sheet:
  //   S = (A ⊕ B)
  //   Cout = (A' . B)
endmodule

module xor_nand (
  input  A,
  input  B,
  output S
);

  wire and_nand_1_s, and_nand_2_s, not_nand_1_s, not_nand_2_s;

  not_nand not_nand_1 (.A(A), .S(not_nand_1_s));
  not_nand not_nand_2 (.A(B), .S(not_nand_2_s));
  and_nand and_nand_1 (.A(not_nand_1_s), .B(B), .S(and_nand_1_s));
  and_nand and_nand_2 (.A(A), .B(not_nand_2_s), .S(and_nand_2_s));
  or_nand or_nand_1 (.A(and_nand_1_s), .B(and_nand_2_s), .S(S));
endmodule

module or_nand (
  input  A,
  input  B,
  output S
);

  wire not_nand_1_s, not_nand_2_s;

  not_nand not_nand_1 (.A(A), .S(not_nand_1_s));
  not_nand not_nand_2 (.A(B), .S(not_nand_2_s));
  nand nand_1 (S, not_nand_1_s, not_nand_2_s);
endmodule

module and_nand (
  input  A,
  input  B,
  output S
);

  wire nand_1_out;

  nand nand_1 (nand_1_out, A, B);
  not_nand not_nand_1 (.A(nand_1_out), .S(S));
endmodule

module not_nand (
  input  A,
  output S
);

  nand nand_1 (S, A, A);
endmodule

// VHDL entity HalfSubtractor_vhdl, as the project stores it:
LIBRARY ieee;
USE ieee.std_logic_1164.all;

ENTITY HalfSubtractor_vhdl IS
  PORT (
    A      : IN  std_logic;
    B      : IN  std_logic;
    S      : OUT std_logic;
    Cout   : OUT std_logic
  );
END HalfSubtractor_vhdl;

ARCHITECTURE TypeArchitecture OF HalfSubtractor_vhdl IS
BEGIN
  S <= A XOR B;
  Cout <= NOT A AND B;
END TypeArchitecture;

// VHDL entity HalfAdder_vhdl, as the project stores it:
LIBRARY ieee;
USE ieee.std_logic_1164.all;

ENTITY HalfAdder_vhdl IS
  PORT (
    A      : IN  std_logic;
    B      : IN  std_logic;
    S      : OUT std_logic;
    Cout   : OUT std_logic
  );
END HalfAdder_vhdl;

ARCHITECTURE TypeArchitecture OF HalfAdder_vhdl IS
BEGIN
  S <= A XOR B;
  Cout <= A AND B;
END TypeArchitecture;

// VHDL entity FullSubtractor_vhdl, as the project stores it:
LIBRARY ieee;
USE ieee.std_logic_1164.all;

ENTITY FullSubtractor_vhdl IS
  PORT (
    A      : IN  std_logic;
    B      : IN  std_logic;
    Cin    : IN  std_logic;
    S      : OUT std_logic;
    Cout   : OUT std_logic
  );
END FullSubtractor_vhdl;

ARCHITECTURE TypeArchitecture OF FullSubtractor_vhdl IS
BEGIN
  S <= (A XOR B) XOR Cin;
  Cout <= (NOT A AND B) or (NOT A AND Cin) or (B AND Cin);
END TypeArchitecture;

// VHDL entity FullAdder_vhdl, as the project stores it:
LIBRARY ieee;
USE ieee.std_logic_1164.all;

ENTITY FullAdder_vhdl IS
  PORT (
    A      : IN  std_logic;
    B      : IN  std_logic;
    Cin    : IN  std_logic;
    S      : OUT std_logic;
    Cout   : OUT std_logic
  );
END FullAdder_vhdl;

ARCHITECTURE TypeArchitecture OF FullAdder_vhdl IS
BEGIN
  S <= (A XOR B) XOR Cin;
  Cout <= (A AND B) or (A AND Cin) or (B AND Cin);
END TypeArchitecture;

// VHDL entity HalfAdderSubtractor_vhdl, as the project stores it:
LIBRARY ieee;
USE ieee.std_logic_1164.all;

ENTITY HalfAdderSubtractor_vhdl IS
  PORT (
    A      : IN  std_logic;
    B      : IN  std_logic;
    Cin    : IN  std_logic;
    M      : IN  std_logic;
    S      : OUT std_logic;
    Cout   : OUT std_logic
  );
END HalfAdderSubtractor_vhdl;

ARCHITECTURE TypeArchitecture OF HalfAdderSubtractor_vhdl IS
BEGIN
  S <= (A XOR B) XOR Cin;
  Cout <= ((M XOR A) AND B) OR ((M XOR A) AND Cin) OR (B AND Cin);
END TypeArchitecture;

// VHDL entity Sutractor4bits_vhdl, as the project stores it:
LIBRARY ieee;
USE ieee.std_logic_1164.all;

ENTITY Sutractor4bits_vhdl IS
  PORT (
    A     : IN  std_logic_vector(3 downto 0); 
    B     : IN  std_logic_vector(3 downto 0); 
    S     : OUT std_logic_vector(3 downto 0); 
    OVERF : OUT std_logic                     
  );
END Sutractor4bits_vhdl;

ARCHITECTURE TypeArchitecture OF Sutractor4bits_vhdl IS
  SIGNAL CARRY : std_logic_vector(3 downto 0);
BEGIN
  CARRY(0) <= '0';

  S(0) <= A(0) XOR B(0) XOR CARRY(0);
  CARRY(1) <= (NOT A(0) AND B(0)) OR (NOT A(0) AND CARRY(0)) OR (B(0) AND CARRY(0));

  S(1) <= A(1) XOR B(1) XOR CARRY(1);
  CARRY(2) <= (NOT A(1) AND B(1)) OR (NOT A(1) AND CARRY(1)) OR (B(1) AND CARRY(1));

  S(2) <= A(2) XOR B(2) XOR CARRY(2);
  CARRY(3) <= (NOT A(2) AND B(2)) OR (NOT A(2) AND CARRY(2)) OR (B(0) AND CARRY(2));

  S(3) <= A(3) XOR B(3) XOR CARRY(3);
  OVERF <= (NOT A(3) AND B(3)) OR (NOT A(3) AND CARRY(3)) OR (B(3) AND CARRY(3));
  
END TypeArchitecture;

// VHDL entity Adder4bits_vhdl, as the project stores it:
LIBRARY ieee;
USE ieee.std_logic_1164.all;

ENTITY Adder4bits_vhdl IS
  PORT (
    A     : IN  std_logic_vector(3 downto 0); 
    B     : IN  std_logic_vector(3 downto 0); 
    S     : OUT std_logic_vector(3 downto 0); 
    OVERF : OUT std_logic                     
  );
END Adder4bits_vhdl;

ARCHITECTURE TypeArchitecture OF Adder4bits_vhdl IS
  SIGNAL CARRY : std_logic_vector(3 downto 0);
BEGIN
  CARRY(0) <= '0';

  S(0) <= A(0) XOR B(0) XOR CARRY(0);
  CARRY(1) <= (A(0) AND B(0)) OR (A(0) AND CARRY(0)) OR (B(0) AND CARRY(0));

  S(1) <= A(1) XOR B(1) XOR CARRY(1);
  CARRY(2) <= (A(1) AND B(1)) OR (A(1) AND CARRY(1)) OR (B(1) AND CARRY(1));

  S(2) <= A(2) XOR B(2) XOR CARRY(2);
  CARRY(3) <= (A(2) AND B(2)) OR (A(2) AND CARRY(2)) OR (B(0) AND CARRY(2));

  S(3) <= A(3) XOR B(3) XOR CARRY(3);
  OVERF <= (A(3) AND B(3)) OR (A(3) AND CARRY(3)) OR (B(3) AND CARRY(3));
  
END TypeArchitecture;

// VHDL entity AdderSubtractor4bits_vhdl, as the project stores it:
LIBRARY ieee;
USE ieee.std_logic_1164.all;

ENTITY AdderSubtractor4bits_vhdl IS
  PORT (
    M	: IN	 std_logic;
    A     : IN  std_logic_vector(3 downto 0); 
    B     : IN  std_logic_vector(3 downto 0); 
    S     : OUT std_logic_vector(3 downto 0); 
    OVERF : OUT std_logic                     
  );
END AdderSubtractor4bits_vhdl;

ARCHITECTURE TypeArchitecture OF AdderSubtractor4bits_vhdl IS
  SIGNAL CARRY : std_logic_vector(3 downto 0);
BEGIN
  CARRY(0) <= '0';

  S(0) <= A(0) XOR B(0) XOR CARRY(0);
  CARRY(1) <= ((M XOR A(0)) AND B(0)) OR ((M XOR A(0)) AND CARRY(0)) OR (B(0) AND CARRY(0));

  S(1) <= A(1) XOR B(1) XOR CARRY(1);
  CARRY(2) <= ((M XOR A(1)) AND B(1)) OR ((M XOR A(1)) AND CARRY(1)) OR (B(1) AND CARRY(1));

  S(2) <= A(2) XOR B(2) XOR CARRY(2);
  CARRY(3) <= ((M XOR A(2)) AND B(2)) OR ((M XOR A(2)) AND CARRY(2)) OR (B(0) AND CARRY(2));

  S(3) <= A(3) XOR B(3) XOR CARRY(3);
  OVERF <= ((M XOR A(3)) AND B(3)) OR ((M XOR A(3)) AND CARRY(3)) OR (B(3) AND CARRY(3));
  
END TypeArchitecture;

// VHDL entity TwoComplementSubtractor_vhdl, as the project stores it:
LIBRARY ieee;
USE ieee.std_logic_1164.all;

ENTITY TwoComplementSubtractor_vhdl IS
  PORT (
    A     : IN  std_logic_vector(3 downto 0); 
    B     : IN  std_logic_vector(3 downto 0); 
    S     : OUT std_logic_vector(3 downto 0); 
    OVERF : OUT std_logic                     
  );
END TwoComplementSubtractor_vhdl;

ARCHITECTURE TypeArchitecture OF TwoComplementSubtractor_vhdl IS
  SIGNAL CARRY : std_logic_vector(3 downto 0);
BEGIN
  CARRY(0) <= '1';
  
  S(0) <= A(0) XOR NOT B(0) XOR CARRY(0);
  CARRY(1) <= (A(0) AND NOT B(0)) OR (A(0) AND CARRY(0)) OR (NOT B(0) AND CARRY(0));

  S(1) <= A(1) XOR NOT B(1) XOR CARRY(1);
  CARRY(2) <= (A(1) AND NOT B(1)) OR (A(1) AND CARRY(1)) OR (NOT B(1) AND CARRY(1));

  S(2) <= A(2) XOR NOT B(2) XOR CARRY(2);
  CARRY(3) <= (A(2) AND NOT B(2)) OR (A(2) AND CARRY(2)) OR (NOT B(0) AND CARRY(2));

  S(3) <= A(3) XOR NOT B(3) XOR CARRY(3);
  OVERF <= (A(3) AND NOT B(3)) OR (A(3) AND CARRY(3)) OR (NOT B(3) AND CARRY(3));
  
END TypeArchitecture;
